// Logisim project address_out_a0_to_a8.circ as structural Verilog: 1 circuit, main circuit main
module main (
  input  HCC0,
  input  HCC0_prime,
  input  BM6,
  input  BM7,
  input  BM2_CDC2,
  input  BM8,
  input  BM1_CDC1,
  input  BM3,
  input  BM4,
  input  BM0_CDC0,
  input  BM5,
  input  VMC11,
  input  VMC10,
  input  VMC9,
  input  VMC8,
  input  VMC7,
  input  VMC6,
  input  VMC5,
  input  VMC4,
  input  VMC3,
  input  VMC2,
  input  VMC1,
  input  VMC0
);

  wire not_1_out, not_2_out, not_3_out, not_4_out, not_5_out, not_6_out, not_7_out, not_8_out, not_9_out,
       transistor_1_out, transistor_3_out, transistor_5_out, transistor_7_out, transistor_9_out,
       transistor_10_out, transistor_13_out, transistor_14_out, transistor_17_out;

  // Probe on not_2_out
  // Probe on not_1_out
  not not_1 (not_1_out, transistor_3_out);
  not not_2 (not_2_out, transistor_1_out);
  Transistor #(.\type ("n")) transistor_1 (.in(BM8), .out(transistor_1_out), .gate(HCC0));
  Transistor #(.\type ("n")) transistor_2 (.in(VMC9), .out(transistor_1_out), .gate(HCC0_prime));
  Transistor #(.\type ("n")) transistor_3 (.in(VMC8), .out(transistor_3_out), .gate(HCC0_prime));
  // Probe on not_3_out
  not not_3 (not_3_out, transistor_5_out);
  Transistor #(.\type ("n")) transistor_4 (.in(BM7), .out(transistor_3_out), .gate(HCC0));
  Transistor #(.\type ("n")) transistor_5 (.in(VMC7), .out(transistor_5_out), .gate(HCC0_prime));
  // Probe on not_4_out
  not not_4 (not_4_out, transistor_7_out);
  Transistor #(.\type ("n")) transistor_6 (.in(BM6), .out(transistor_5_out), .gate(HCC0));
  Transistor #(.\type ("n")) transistor_7 (.in(BM5), .out(transistor_7_out), .gate(HCC0));
  Transistor #(.\type ("n")) transistor_8 (.in(VMC6), .out(transistor_7_out), .gate(HCC0_prime));
  // Probe on not_6_out
  // Probe on not_5_out
  not not_5 (not_5_out, transistor_10_out);
  not not_6 (not_6_out, transistor_9_out);
  Transistor #(.\type ("n")) transistor_9 (.in(BM4), .out(transistor_9_out), .gate(HCC0));
  Transistor #(.\type ("n")) transistor_10 (.in(VMC4), .out(transistor_10_out), .gate(HCC0_prime));
  Transistor #(.\type ("n")) transistor_11 (.in(VMC5), .out(transistor_9_out), .gate(HCC0_prime));
  // Probe on not_7_out
  not not_7 (not_7_out, transistor_13_out);
  Transistor #(.\type ("n")) transistor_12 (.in(BM3), .out(transistor_10_out), .gate(HCC0));
  Transistor #(.\type ("n")) transistor_13 (.in(VMC3), .out(transistor_13_out), .gate(HCC0_prime));
  // Probe on not_8_out
  not not_8 (not_8_out, transistor_14_out);
  Transistor #(.\type ("n")) transistor_14 (.in(BM1_CDC1), .out(transistor_14_out), .gate(HCC0));
  Transistor #(.\type ("n")) transistor_15 (.in(BM2_CDC2), .out(transistor_13_out), .gate(HCC0));
  Transistor #(.\type ("n")) transistor_16 (.in(VMC2), .out(transistor_14_out), .gate(HCC0_prime));
  // Probe on not_9_out
  not not_9 (not_9_out, transistor_17_out);
  Transistor #(.\type ("n")) transistor_17 (.in(BM0_CDC0), .out(transistor_17_out), .gate(HCC0));
  Transistor #(.\type ("n")) transistor_18 (.in(VMC1), .out(transistor_17_out), .gate(HCC0_prime));
endmodule
