// Logisim project base_address_calculation_4.circ as structural Verilog: 4 circuits, main circuit main
module main (
  input  VMC11,
  input  BV10,
  input  BV11,
  input  VMC10,
  input  BV9,
  input  BV12,
  input  BV13,
  input  BM11,
  input  BC11,
  input  BC12,
  input  BM10,
  input  BC10,
  input  BC13,
  input  BM9,
  input  HCC0
);

  wire _1_2_out, _1_3_out, _1_out, _2_2_out, _2_3_out, _2_4_out, _2_5_out, _2_6_out, _2_7_out, _2_8_out,
       _2_9_out, _2_out, _3_2_out, _3_3_out, _3_out, _4_2_out, _4_3_out, _4_out, _5_2_out, _5_3_out, _5_out,
       not_1_out, not_2_out, not_3_out, not_4_out, not_5_out, not_6_out, not_7_out, not_8_out, not_9_out,
       not_10_out, not_11_out, not_12_out, not_13_out, not_14_out, not_15_out, not_16_out, not_17_out,
       not_18_out, not_19_out, transistor_1_out, transistor_2_out, transistor_3_out, transistor_5_out,
       transistor_7_out, transistor_10_out, transistor_11_out, transistor_13_out, transistor_15_out,
       transistor_17_out, transistor_20_out;

  nand _2 (_2_out, not_8_out, not_7_out);
  not not_1 (not_1_out, _2_out);
  and _2_2 (_2_2_out, _1_out, not_1_out);
  not not_2 (not_2_out, transistor_15_out);
  // Probe on not_2_out
  // Probe on not_3_out
  not not_3 (not_3_out, transistor_1_out);
  not not_4 (not_4_out, transistor_2_out);
  // Probe on not_4_out
  not not_5 (not_5_out, transistor_10_out);
  // Probe on not_5_out
  not not_6 (not_6_out, transistor_20_out);
  // Probe on not_6_out
  or _2_3 (_2_3_out, _1_out, not_8_out, not_7_out);
  nor _2_4 (_2_4_out, _2_2_out, _2_5_out);
  Transistor #(.\type ("n")) transistor_1 (.in(_2_4_out), .out(transistor_1_out), .gate(not_19_out));
  and _2_5 (_2_5_out, _2_3_out, _2_6_out);
  Transistor #(.\type ("n")) transistor_2 (.in(_2_4_out), .out(transistor_2_out), .gate(HCC0));
  not not_7 (not_7_out, transistor_3_out);
  Transistor #(.\type ("n")) transistor_3 (.in(VMC11), .out(transistor_3_out), .gate(not_19_out));
  Transistor #(.\type ("n")) transistor_4 (.in(BM11), .out(transistor_3_out), .gate(HCC0));
  nor _2_6 (_2_6_out, _2_7_out, _2_8_out);
  and _2_7 (_2_7_out, not_7_out, not_8_out);
  not not_8 (not_8_out, transistor_5_out);
  Transistor #(.\type ("n")) transistor_5 (.in(BV10), .out(transistor_5_out), .gate(not_19_out));
  Transistor #(.\type ("n")) transistor_6 (.in(BC11), .out(transistor_5_out), .gate(HCC0));
  and _2_8 (_2_8_out, _1_out, _2_9_out);
  or _2_9 (_2_9_out, not_8_out, not_7_out);
  Transistor #(.\type ("n")) transistor_7 (.in(BV11), .out(transistor_7_out), .gate(not_19_out));
  not not_9 (not_9_out, not_10_out);
  not not_10 (not_10_out, transistor_7_out);
  Transistor #(.\type ("n")) transistor_8 (.in(BC12), .out(transistor_7_out), .gate(HCC0));
  nand _3 (_3_out, _2_6_out, not_9_out);
  or _3_2 (_3_2_out, _2_6_out, not_9_out);
  Transistor #(.\type ("n")) transistor_9 (.in(not_11_out), .out(transistor_2_out), .gate(not_19_out));
  Transistor #(.\type ("n")) transistor_10 (.in(not_11_out), .out(transistor_10_out), .gate(HCC0));
  nand _3_3 (_3_3_out, _3_out, _3_2_out);
  not not_11 (not_11_out, _3_3_out);
  not not_12 (not_12_out, not_13_out);
  not not_13 (not_13_out, transistor_11_out);
  Transistor #(.\type ("n")) transistor_11 (.in(VMC10), .out(transistor_11_out), .gate(not_19_out));
  Transistor #(.\type ("n")) transistor_12 (.in(BM10), .out(transistor_11_out), .gate(HCC0));
  not not_14 (not_14_out, not_15_out);
  not not_15 (not_15_out, transistor_13_out);
  Transistor #(.\type ("n")) transistor_13 (.in(BV9), .out(transistor_13_out), .gate(not_19_out));
  Transistor #(.\type ("n")) transistor_14 (.in(BC10), .out(transistor_13_out), .gate(HCC0));
  nand _1 (_1_out, not_14_out, not_12_out);
  or _1_2 (_1_2_out, not_14_out, not_12_out);
  Transistor #(.\type ("n")) transistor_15 (.in(not_16_out), .out(transistor_15_out), .gate(not_19_out));
  nand _1_3 (_1_3_out, _1_out, _1_2_out);
  not not_16 (not_16_out, _1_3_out);
  Transistor #(.\type ("n")) transistor_16 (.in(not_16_out), .out(transistor_1_out), .gate(HCC0));
  not not_17 (not_17_out, transistor_17_out);
  Transistor #(.\type ("n")) transistor_17 (.in(BV12), .out(transistor_17_out), .gate(not_19_out));
  Transistor #(.\type ("n")) transistor_18 (.in(BC13), .out(transistor_17_out), .gate(HCC0));
  and _4 (_4_out, _3_out, not_17_out);
  nor _4_2 (_4_2_out, _3_out, not_17_out);
  Transistor #(.\type ("n")) transistor_19 (.in(_4_3_out), .out(transistor_10_out), .gate(not_19_out));
  Transistor #(.\type ("n")) transistor_20 (.in(_4_3_out), .out(transistor_20_out), .gate(HCC0));
  nor _4_3 (_4_3_out, _4_out, _4_2_out);
  nand _5 (_5_out, _4_2_out, BV13);
  or _5_2 (_5_2_out, _4_2_out, BV13);
  Transistor #(.\type ("n")) transistor_21 (.in(not_18_out), .out(transistor_20_out), .gate(not_19_out));
  Transistor #(.\type ("n")) transistor_22 (.in(BM9), .out(transistor_15_out), .gate(HCC0));
  nand _5_3 (_5_3_out, _5_out, _5_2_out);
  not not_18 (not_18_out, _5_3_out);
  not not_19 (not_19_out, HCC0);
endmodule

module Pass_Transistor (
  input  in_1,
  input  in_2,
  output out_3
);

  Register #(.width(1)) register_1 (.D(in_1), .en(1'b1), .Q(out_3), .clk(in_2));  // open: clr
endmodule

module Pass_Transistor_2 (
  input  IN,
  input  in_2,
  input  CLEAR,
  input  PRESET,
  output OUT
);

  D_Flip_Flop d_ff_1 (.clk(in_2), .D(IN), .Q(OUT), .preset(PRESET), .en(1'b1), .reset(CLEAR));  // open: Qn
endmodule

module Pass_Transistor_3 (
  input  IN,
  input  in_2,
  input  SET,
  output OUT
);

  wire controlled_buffer_1_out, controlled_buffer_2_out, not_1_out;

  not not_1 (not_1_out, SET);
  assign controlled_buffer_1_out = SET ? SET : 1'bz;  // Controlled_Buffer controlled_buffer_1
  assign controlled_buffer_2_out = not_1_out ? not_1_out : 1'bz;  // Controlled_Buffer controlled_buffer_2
  D_Flip_Flop d_ff_1 (
    .clk(in_2), .D(IN), .Q(OUT), .preset(controlled_buffer_1_out), .en(1'b1), .reset(controlled_buffer_2_out));  // open: Qn
endmodule
