// Logisim project cell_depth_counter_actual.circ as structural Verilog: 3 circuits, main circuit main
module main (
  input  INCREMENT,
  input  RESET
);

  wire and_1_out, and_2_out, F1_out, F2_out, nand_1_out, nand_2_out, nand_3_out, nand_4_out, nor_1_out,
       nor_2_out, nor_3_out, nor_4_out, not_1_out, not_2_out, not_3_out, not_4_out, not_5_out, not_6_out,
       or_1_out, or_2_out, pass_transistor_1_out_3, pass_transistor_2_1_out, pass_transistor_2_2_out,
       pass_transistor_2_3_out, pass_transistor_2_4_out, pass_transistor_2_out_3, pass_transistor_3_out_3,
       pass_transistor_4_out_3, transistor_1_out, transistor_2_out, transistor_3_out, transistor_4_out;

  // Probe on not_1_out
  // Probe on pass_transistor_1_out_3
  // Probe on not_2_out
  // Probe on pass_transistor_3_out_3
  // Probe on not_5_out
  not F2 (F2_out, F1_out);
  Clock F1 (.out(F1_out));
  Pass_Transistor_2 pass_transistor_2_1 (
    .in_2(F1_out), .IN(not_1_out), .OUT(pass_transistor_2_1_out));  // open: CLEAR, PRESET
  Transistor transistor_1 (.in(pass_transistor_2_1_out), .out(transistor_1_out), .gate(RESET));
  not not_1 (not_1_out, pass_transistor_1_out_3);
  nand nand_1 (nand_1_out, pass_transistor_2_1_out, nor_1_out);
  Pass_Transistor pass_transistor_1 (.in_1(nand_2_out), .out_3(pass_transistor_1_out_3), .in_2(F2_out));
  nand nand_2 (nand_2_out, nand_1_out, or_1_out);
  not not_2 (not_2_out, not_3_out);
  or or_1 (or_1_out, pass_transistor_2_1_out, nor_1_out);
  // Probe on not_3_out
  Pass_Transistor_2 pass_transistor_2_2 (
    .in_2(F1_out), .IN(not_3_out), .OUT(pass_transistor_2_2_out));  // open: CLEAR, PRESET
  Transistor transistor_2 (.in(pass_transistor_2_2_out), .out(transistor_2_out), .gate(RESET));
  not not_3 (not_3_out, pass_transistor_2_out_3);
  nor nor_1 (nor_1_out, pass_transistor_2_2_out, nand_4_out);
  Pass_Transistor pass_transistor_2 (.in_1(nor_2_out), .out_3(pass_transistor_2_out_3), .in_2(F2_out));
  nor nor_2 (nor_2_out, nor_1_out, and_1_out);
  and and_1 (and_1_out, pass_transistor_2_2_out, nand_4_out);
  // Probe on not_4_out
  not not_4 (not_4_out, pass_transistor_3_out_3);
  Pass_Transistor_2 pass_transistor_2_3 (
    .in_2(F1_out), .IN(not_4_out), .OUT(pass_transistor_2_3_out));  // open: CLEAR, PRESET
  Transistor transistor_3 (.in(pass_transistor_2_3_out), .out(transistor_3_out), .gate(RESET));
  Pass_Transistor pass_transistor_3 (.in_1(nand_3_out), .out_3(pass_transistor_3_out_3), .in_2(F2_out));
  nand nand_3 (nand_3_out, nand_4_out, or_2_out);
  nand nand_4 (nand_4_out, pass_transistor_2_3_out, nor_3_out);
  not not_5 (not_5_out, not_6_out);
  or or_2 (or_2_out, pass_transistor_2_3_out, nor_3_out);
  // Probe on not_6_out
  not not_6 (not_6_out, pass_transistor_4_out_3);
  Pass_Transistor_2 pass_transistor_2_4 (
    .in_2(F1_out), .IN(not_6_out), .OUT(pass_transistor_2_4_out));  // open: CLEAR, PRESET
  nor nor_3 (nor_3_out, pass_transistor_2_4_out, INCREMENT);
  Transistor transistor_4 (.in(pass_transistor_2_4_out), .out(transistor_4_out), .gate(RESET));
  Pass_Transistor pass_transistor_4 (.in_1(nor_4_out), .out_3(pass_transistor_4_out_3), .in_2(F2_out));
  nor nor_4 (nor_4_out, nor_3_out, and_2_out);
  and and_2 (and_2_out, pass_transistor_2_4_out, INCREMENT);
  // also tied to GND on the sheet: {transistor_1_out, transistor_3_out}
  // also tied to VCC on the sheet: {transistor_2_out, transistor_4_out}

  // Notes on the sheet:
  //   VSS
  //   VDD
  //   VSS
  //   VDD
endmodule

module Pass_Transistor (
  input  in_1,
  input  in_2,
  output out_3
);

  Register #(.width(1)) register_1 (.D(in_1), .en(1'b1), .Q(out_3), .clk(in_2));  // open: clr
endmodule

module Pass_Transistor_2 (
  input  IN,
  input  in_2,
  input  CLEAR,
  input  PRESET,
  output OUT
);

  D_Flip_Flop d_ff_1 (.clk(in_2), .D(IN), .Q(OUT), .preset(PRESET), .en(1'b1), .reset(CLEAR));  // open: Qn
endmodule
