// Logisim project cell_depth_counter_reset.circ as structural Verilog: 1 circuit, main circuit main
module main (
  input  D
);

  wire and_1_out, and_2_out, and_3_out, and_4_out, CDC0_prime_out, CDC1_prime_out, CDC2_prime_out,
       CDC3_prime_out, clock_1_out, nor_1_out, not_1_out, or_1_out, or_2_out, or_3_out;
  wire [3:0] CELL_DEPTH_CNTR_q;

  Counter #(.width(4), .max('hf)) CELL_DEPTH_CNTR (
    .count(1'b1), .Q(CELL_DEPTH_CNTR_q), .clk(clock_1_out));  // open: load, D, carry, clr
  Clock clock_1 (.out(clock_1_out));
  not CDC3_prime (CDC3_prime_out, CELL_DEPTH_CNTR_q[3]);
  not CDC2_prime (CDC2_prime_out, CELL_DEPTH_CNTR_q[2]);
  not CDC1_prime (CDC1_prime_out, CELL_DEPTH_CNTR_q[1]);
  not CDC0_prime (CDC0_prime_out, CELL_DEPTH_CNTR_q[0]);
  not not_1 (not_1_out, D);
  or or_1 (or_1_out, D, not_1_out);
  or or_2 (or_2_out, D, not_1_out);
  or or_3 (or_3_out, D, not_1_out);
  and and_1 (and_1_out, D, CDC3_prime_out);
  and and_2 (and_2_out, or_1_out, CDC2_prime_out);
  and and_3 (and_3_out, or_2_out, CDC1_prime_out);
  and and_4 (and_4_out, or_3_out, CDC0_prime_out);
  nor nor_1 (nor_1_out, and_1_out, and_2_out, and_3_out, and_4_out);
  // Probe on nor_1_out
endmodule
