// Logisim project cell_depth_counter_reset_3.circ as structural Verilog: 1 circuit, main circuit main
module main (
  input  D,
  input  LOAD_NUM_COLUMNS,
  input  NON_MATRIX_LINE
);

  wire and_1_out, and_2_out, and_3_out, and_4_out, and_5_out, CDC0_prime_out, CDC1_prime_out, CDC2_prime_out,
       CDC3_prime_out, nor_1_out, nor_2_out, not_1_out, not_2_out, or_1_out, or_2_out, or_3_out;
  wire [3:0] CELL_DEPTH_CNTR_q;

  Counter #(.width(4), .max('hf)) CELL_DEPTH_CNTR (
    .count(1'b1), .Q(CELL_DEPTH_CNTR_q), .clk(nor_1_out), .clr(and_5_out));  // open: load, D, carry
  // Probe on nor_1_out
  not CDC3_prime (CDC3_prime_out, CELL_DEPTH_CNTR_q[3]);
  not CDC2_prime (CDC2_prime_out, CELL_DEPTH_CNTR_q[2]);
  not CDC1_prime (CDC1_prime_out, CELL_DEPTH_CNTR_q[1]);
  not CDC0_prime (CDC0_prime_out, CELL_DEPTH_CNTR_q[0]);
  not not_1 (not_1_out, D);
  nor nor_1 (nor_1_out, not_2_out, and_5_out, NON_MATRIX_LINE);
  or or_1 (or_1_out, D, not_1_out);
  or or_2 (or_2_out, D, not_1_out);
  or or_3 (or_3_out, D, not_1_out);
  // Probe on nor_2_out
  not not_2 (not_2_out, LOAD_NUM_COLUMNS);
  and and_1 (and_1_out, D, CDC3_prime_out);
  and and_2 (and_2_out, or_1_out, CDC2_prime_out);
  and and_3 (and_3_out, or_2_out, CDC1_prime_out);
  and and_4 (and_4_out, or_3_out, CDC0_prime_out);
  and and_5 (and_5_out, nor_2_out, LOAD_NUM_COLUMNS);
  // Probe on and_5_out
  nor nor_2 (nor_2_out, and_1_out, and_2_out, and_3_out, and_4_out);
  Clock F1 ();  // open: out
endmodule
