// Logisim project cell_depth_counter_reset_and_increment_logic_2.circ as structural Verilog: 2 circuits, main circuit main
module main (
  input  DOUBLE_HEIGHT_CHARS__D,
  input  START_OF_NEW_LINE,
  input  NON_MATRIX_LINE
);

  wire and_1_out, and_2_out, and_3_out, and_4_out, CDC0_prime_out, CDC1_prime_out, CDC2_prime_out,
       CDC3_prime_out, F1_out, nand_1_out, nor_1_out, nor_2_out, not_1_out, not_2_out, not_3_out, or_1_out,
       or_2_out, or_3_out, pass_transistor_1_out_3, pass_transistor_2_out_3, pass_transistor_3_out_3;
  wire [3:0] CELL_DEPTH_CNTR_q;

  Counter #(.width(4), .max('hf)) CELL_DEPTH_CNTR (
    .count(1'b1), .Q(CELL_DEPTH_CNTR_q), .clk(nor_1_out), .clr(not_3_out));  // open: load, D, carry
  not CDC3_prime (CDC3_prime_out, CELL_DEPTH_CNTR_q[3]);
  not CDC2_prime (CDC2_prime_out, CELL_DEPTH_CNTR_q[2]);
  not CDC1_prime (CDC1_prime_out, CELL_DEPTH_CNTR_q[1]);
  not CDC0_prime (CDC0_prime_out, CELL_DEPTH_CNTR_q[0]);
  nor nor_1 (nor_1_out, pass_transistor_1_out_3, not_3_out, pass_transistor_2_out_3);
  not not_1 (not_1_out, DOUBLE_HEIGHT_CHARS__D);
  Pass_Transistor pass_transistor_1 (.in_1(not_2_out), .out_3(pass_transistor_1_out_3), .in_2(F1_out));
  not not_2 (not_2_out, START_OF_NEW_LINE);
  or or_1 (or_1_out, DOUBLE_HEIGHT_CHARS__D, not_1_out);
  or or_2 (or_2_out, DOUBLE_HEIGHT_CHARS__D, not_1_out);
  or or_3 (or_3_out, DOUBLE_HEIGHT_CHARS__D, not_1_out);
  nand nand_1 (nand_1_out, nor_2_out, START_OF_NEW_LINE);
  Pass_Transistor pass_transistor_2 (.in_1(NON_MATRIX_LINE), .out_3(pass_transistor_2_out_3), .in_2(F1_out));
  and and_1 (and_1_out, DOUBLE_HEIGHT_CHARS__D, CDC3_prime_out);
  and and_2 (and_2_out, or_1_out, CDC2_prime_out);
  and and_3 (and_3_out, or_2_out, CDC1_prime_out);
  and and_4 (and_4_out, or_3_out, CDC0_prime_out);
  not not_3 (not_3_out, pass_transistor_3_out_3);
  Pass_Transistor pass_transistor_3 (.in_1(nand_1_out), .out_3(pass_transistor_3_out_3), .in_2(F1_out));
  Clock F1 (.out(F1_out));
  nor nor_2 (nor_2_out, and_1_out, and_2_out, and_3_out, and_4_out);

  // Notes on the sheet:
  //   CDC RESET
  //   CDC INCREMENT ENABLE
  //   CDC LAST VALUE
endmodule

module Pass_Transistor (
  input  in_1,
  input  in_2,
  output out_3
);

  Register #(.width(1)) register_1 (.D(in_1), .en(1'b1), .Q(out_3), .clk(in_2));  // open: clr
endmodule
