// Logisim project cell_index.circ as structural Verilog: 1 circuit, main circuit main
module main (
  input  D7,
  input  D6,
  input  D5,
  input  D4,
  input  D3,
  input  D2,
  input  D1,
  input  D0
);
endmodule
