// Logisim project cell_index_2.circ as structural Verilog: 4 circuits, main circuit main
module main (
  input  F2,
  input  HCC0,
  input  MEM_CLK,
  input  D7,
  input  D6,
  input  D5,
  input  D4,
  input  D3,
  input  D2,
  input  D1,
  input  D0,
  input  CDC3,
  input  D,
  input  CDC2,
  input  CDC1,
  input  CDC0
);

  wire nor_1_out, not_1_out, not_2_out, not_3_out, not_4_out, not_5_out, not_6_out, not_7_out, not_8_out,
       not_9_out, not_10_out, not_11_out, not_12_out, not_13_out, not_14_out, not_15_out, not_16_out,
       not_17_out, not_18_out, not_19_out, not_20_out, not_21_out, not_22_out, not_23_out, not_24_out,
       not_25_out, not_26_out, not_27_out, not_28_out, not_29_out, not_30_out, not_31_out, not_32_out,
       not_33_out, not_34_out, not_35_out, pass_transistor_1_out_3, pass_transistor_2_out_3,
       pass_transistor_3_out_3, pass_transistor_4_out_3, pass_transistor_5_out_3, pass_transistor_6_out_3,
       pass_transistor_7_out_3, pass_transistor_8_out_3, transistor_1_out, transistor_2_out,
       transistor_4_out, transistor_6_out, transistor_8_out, transistor_10_out, transistor_12_out,
       transistor_14_out, transistor_16_out;

  Transistor #(.\type ("n"), .gate("br")) transistor_1 (.in(1'b0), .out(transistor_1_out), .gate(not_35_out));
  nor nor_1 (nor_1_out, F2, HCC0, MEM_CLK);
  // Probe on not_1_out
  not not_1 (not_1_out, not_2_out);
  not not_2 (not_2_out, transistor_1_out);
  Transistor #(.\type ("n"), .gate("br")) transistor_2 (.in(not_3_out), .out(transistor_2_out), .gate(not_35_out));
  Transistor #(.\type ("n"), .gate("br")) transistor_3 (.in(not_3_out), .out(transistor_1_out), .gate(D));
  not not_3 (not_3_out, not_4_out);
  not not_4 (not_4_out, pass_transistor_1_out_3);
  Pass_Transistor pass_transistor_1 (.in_1(D7), .out_3(pass_transistor_1_out_3), .in_2(nor_1_out));
  // Probe on not_5_out
  not not_5 (not_5_out, not_6_out);
  not not_6 (not_6_out, transistor_2_out);
  Transistor #(.\type ("n"), .gate("br")) transistor_4 (.in(not_7_out), .out(transistor_4_out), .gate(not_35_out));
  Transistor #(.\type ("n"), .gate("br")) transistor_5 (.in(not_7_out), .out(transistor_2_out), .gate(D));
  not not_7 (not_7_out, not_8_out);
  not not_8 (not_8_out, pass_transistor_2_out_3);
  Pass_Transistor pass_transistor_2 (.in_1(D6), .out_3(pass_transistor_2_out_3), .in_2(nor_1_out));
  // Probe on not_9_out
  not not_9 (not_9_out, not_10_out);
  not not_10 (not_10_out, transistor_4_out);
  Transistor #(.\type ("n"), .gate("br")) transistor_6 (.in(not_11_out), .out(transistor_6_out), .gate(not_35_out));
  Transistor #(.\type ("n"), .gate("br")) transistor_7 (.in(not_11_out), .out(transistor_4_out), .gate(D));
  not not_11 (not_11_out, not_12_out);
  not not_12 (not_12_out, pass_transistor_3_out_3);
  Pass_Transistor pass_transistor_3 (.in_1(D5), .out_3(pass_transistor_3_out_3), .in_2(nor_1_out));
  // Probe on not_13_out
  not not_13 (not_13_out, not_14_out);
  not not_14 (not_14_out, transistor_6_out);
  Transistor #(.\type ("n"), .gate("br")) transistor_8 (.in(not_15_out), .out(transistor_8_out), .gate(not_35_out));
  Transistor #(.\type ("n"), .gate("br")) transistor_9 (.in(not_15_out), .out(transistor_6_out), .gate(D));
  not not_15 (not_15_out, not_16_out);
  not not_16 (not_16_out, pass_transistor_4_out_3);
  Pass_Transistor pass_transistor_4 (.in_1(D4), .out_3(pass_transistor_4_out_3), .in_2(nor_1_out));
  // Probe on not_17_out
  not not_17 (not_17_out, not_18_out);
  not not_18 (not_18_out, transistor_8_out);
  Transistor #(.\type ("n"), .gate("br")) transistor_10 (.in(not_19_out), .out(transistor_10_out), .gate(not_35_out));
  Transistor #(.\type ("n"), .gate("br")) transistor_11 (.in(not_19_out), .out(transistor_8_out), .gate(D));
  not not_19 (not_19_out, not_20_out);
  not not_20 (not_20_out, pass_transistor_5_out_3);
  Pass_Transistor pass_transistor_5 (.in_1(D3), .out_3(pass_transistor_5_out_3), .in_2(nor_1_out));
  // Probe on not_21_out
  not not_21 (not_21_out, not_22_out);
  not not_22 (not_22_out, transistor_10_out);
  Transistor #(.\type ("n"), .gate("br")) transistor_12 (.in(not_23_out), .out(transistor_12_out), .gate(not_35_out));
  Transistor #(.\type ("n"), .gate("br")) transistor_13 (.in(not_23_out), .out(transistor_10_out), .gate(D));
  not not_23 (not_23_out, not_24_out);
  not not_24 (not_24_out, pass_transistor_6_out_3);
  Pass_Transistor pass_transistor_6 (.in_1(D2), .out_3(pass_transistor_6_out_3), .in_2(nor_1_out));
  // Probe on not_25_out
  not not_25 (not_25_out, not_26_out);
  not not_26 (not_26_out, transistor_12_out);
  Transistor #(.\type ("n"), .gate("br")) transistor_14 (.in(not_27_out), .out(transistor_14_out), .gate(not_35_out));
  Transistor #(.\type ("n"), .gate("br")) transistor_15 (.in(not_27_out), .out(transistor_12_out), .gate(D));
  not not_27 (not_27_out, not_28_out);
  not not_28 (not_28_out, pass_transistor_7_out_3);
  Pass_Transistor pass_transistor_7 (.in_1(D1), .out_3(pass_transistor_7_out_3), .in_2(nor_1_out));
  // Probe on not_29_out
  not not_29 (not_29_out, not_30_out);
  not not_30 (not_30_out, transistor_14_out);
  Transistor #(.\type ("n"), .gate("br")) transistor_16 (.in(not_31_out), .out(transistor_16_out), .gate(not_35_out));
  Transistor #(.\type ("n"), .gate("br")) transistor_17 (.in(not_31_out), .out(transistor_14_out), .gate(D));
  not not_31 (not_31_out, not_32_out);
  not not_32 (not_32_out, pass_transistor_8_out_3);
  Pass_Transistor pass_transistor_8 (.in_1(D0), .out_3(pass_transistor_8_out_3), .in_2(nor_1_out));
  // Probe on not_33_out
  not not_33 (not_33_out, not_34_out);
  not not_34 (not_34_out, transistor_16_out);
  Transistor #(.\type ("n"), .gate("br")) transistor_18 (.in(CDC3), .out(transistor_16_out), .gate(D));
  not not_35 (not_35_out, D);
  // Probe on CDC1
  // Probe on CDC2
  // Probe on CDC0
endmodule

module Pass_Transistor (
  input  in_1,
  input  in_2,
  output out_3
);

  Register #(.width(1)) register_1 (.D(in_1), .en(1'b1), .Q(out_3), .clk(in_2));  // open: clr
endmodule

module Pass_Transistor_2 (
  input  IN,
  input  in_2,
  input  CLEAR,
  input  PRESET,
  output OUT
);

  D_Flip_Flop d_ff_1 (.clk(in_2), .D(IN), .Q(OUT), .preset(PRESET), .en(1'b1), .reset(CLEAR));  // open: Qn
endmodule

module Pass_Transistor_3 (
  input  IN,
  input  in_2,
  input  SET,
  output OUT
);

  wire controlled_buffer_1_out, controlled_buffer_2_out, not_1_out;

  not not_1 (not_1_out, SET);
  assign controlled_buffer_1_out = SET ? SET : 1'bz;  // Controlled_Buffer controlled_buffer_1
  assign controlled_buffer_2_out = not_1_out ? not_1_out : 1'bz;  // Controlled_Buffer controlled_buffer_2
  D_Flip_Flop d_ff_1 (
    .clk(in_2), .D(IN), .Q(OUT), .preset(controlled_buffer_1_out), .en(1'b1), .reset(controlled_buffer_2_out));  // open: Qn
endmodule
