// Logisim project clock_generation_3.circ as structural Verilog: 4 circuits, main circuit main
module main (
  input  EXT_RESET_prime
);

  wire IN1__4_43_Mhz_out, nand_1_out, nand_2_out, nor_1_out, nor_2_out, nor_3_out, nor_4_out, nor_5_out,
       nor_6_out, nor_7_out, nor_8_out, nor_9_out, not_1_out, not_2_out, not_3_out, not_4_out, not_5_out,
       not_6_out, not_7_out, not_8_out, not_9_out, not_10_out, not_11_out, not_12_out, not_13_out,
       not_14_out, not_15_out, not_16_out, not_17_out, not_18_out, not_19_out, not_20_out, or_1_out,
       pass_transistor_1_out_3, pass_transistor_2_out_3, pass_transistor_3_out_3, pass_transistor_4_out_3,
       pass_transistor_5_out_3, pass_transistor_6_out_3, transistor_1_out;

  nor nor_1 (nor_1_out, nor_4_out, not_5_out);
  not not_1 (not_1_out, nor_1_out);
  not not_2 (not_2_out, not_1_out);
  // Probe on not_2_out
  not not_3 (not_3_out, nor_4_out);
  nor nor_2 (nor_2_out, not_2_out, not_3_out);
  not not_4 (not_4_out, nor_2_out);
  not not_5 (not_5_out, not_4_out);
  // Probe on not_5_out
  // Probe on not_9_out
  not not_6 (not_6_out, pass_transistor_1_out_3);
  Pass_Transistor pass_transistor_1 (.in_1(not_7_out), .out_3(pass_transistor_1_out_3), .in_2(not_16_out));
  not not_7 (not_7_out, EXT_RESET_prime);
  Pass_Transistor pass_transistor_2 (.in_1(not_6_out), .out_3(pass_transistor_2_out_3), .in_2(not_15_out));
  not not_8 (not_8_out, not_10_out);
  not not_9 (not_9_out, not_11_out);
  nor nor_3 (nor_3_out, pass_transistor_2_out_3, EXT_RESET_prime);
  not not_10 (not_10_out, nor_5_out);
  not not_11 (not_11_out, nor_6_out);
  nor nor_4 (nor_4_out, nor_3_out, pass_transistor_4_out_3);
  Pass_Transistor pass_transistor_3 (.in_1(nor_4_out), .out_3(pass_transistor_3_out_3), .in_2(not_15_out));
  nor nor_5 (nor_5_out, not_13_out, not_9_out);
  nor nor_6 (nor_6_out, not_8_out, not_12_out);
  Pass_Transistor pass_transistor_4 (.in_1(nand_1_out), .out_3(pass_transistor_4_out_3), .in_2(not_16_out));
  nand nand_1 (nand_1_out, nand_2_out, or_1_out);
  nand nand_2 (nand_2_out, pass_transistor_3_out_3, not_14_out);
  not not_12 (not_12_out, not_13_out);
  or or_1 (or_1_out, pass_transistor_3_out_3, not_14_out);
  Pass_Transistor pass_transistor_5 (.in_1(nor_7_out), .out_3(pass_transistor_5_out_3), .in_2(not_16_out));
  nor nor_7 (nor_7_out, nor_3_out, not_14_out);
  not not_13 (not_13_out, pass_transistor_5_out_3);
  not not_14 (not_14_out, pass_transistor_6_out_3);
  Pass_Transistor pass_transistor_6 (.in_1(not_13_out), .out_3(pass_transistor_6_out_3), .in_2(not_15_out));
  not not_15 (not_15_out, not_17_out);
  not not_16 (not_16_out, not_18_out);
  nor nor_8 (nor_8_out, not_19_out, not_16_out);
  not not_17 (not_17_out, nor_8_out);
  nor nor_9 (nor_9_out, not_15_out, IN1__4_43_Mhz_out);
  not not_18 (not_18_out, nor_9_out);
  not not_19 (not_19_out, IN1__4_43_Mhz_out);
  Transistor #(.\type ("n")) transistor_1 (.in(1'b1), .out(transistor_1_out), .gate(not_15_out));
  Transistor #(.\type ("n")) transistor_2 (.in(1'b0), .out(transistor_1_out), .gate(not_16_out));
  Clock IN1__4_43_Mhz (.out(IN1__4_43_Mhz_out));
  not not_20 (not_20_out, transistor_1_out);
  // Probe on not_20_out

  // Notes on the sheet:
  //   <---   1.1 MHz
  //   <---   2.2 MHz
endmodule

module Pass_Transistor (
  input  in_1,
  input  in_2,
  output out_3
);

  Register #(.width(1)) register_1 (.D(in_1), .en(1'b1), .Q(out_3), .clk(in_2));  // open: clr
endmodule

module Pass_Transistor_2 (
  input  IN,
  input  in_2,
  input  CLEAR,
  input  PRESET,
  output OUT
);

  D_Flip_Flop d_ff_1 (.clk(in_2), .D(IN), .Q(OUT), .preset(PRESET), .en(1'b1), .reset(CLEAR));  // open: Qn
endmodule

module Pass_Transistor_3 (
  input  IN,
  input  in_2,
  input  SET,
  output OUT
);

  wire controlled_buffer_1_out, controlled_buffer_2_out, not_1_out;

  not not_1 (not_1_out, SET);
  assign controlled_buffer_1_out = SET ? SET : 1'bz;  // Controlled_Buffer controlled_buffer_1
  assign controlled_buffer_2_out = not_1_out ? not_1_out : 1'bz;  // Controlled_Buffer controlled_buffer_2
  D_Flip_Flop d_ff_1 (
    .clk(in_2), .D(IN), .Q(OUT), .preset(controlled_buffer_1_out), .en(1'b1), .reset(controlled_buffer_2_out));  // open: Qn
endmodule
