// Logisim project combined_sync.circ as structural Verilog: 1 circuit, main circuit main
module main (
  input  HSYNC,
  input  VBLANK,
  input  VBLANKPULSE,
  input  VSYNC
);

  wire and_1_out, and_2_out, and_3_out, nor_1_out, nor_2_out, not_1_out;

  not not_1 (not_1_out, VBLANK);
  and and_1 (and_1_out, HSYNC, not_1_out);
  and and_2 (and_2_out, VBLANK, VBLANKPULSE);
  nor nor_1 (nor_1_out, and_1_out, and_2_out, VSYNC);
  and and_3 (and_3_out, VSYNC, VBLANKPULSE);
  nor nor_2 (nor_2_out, nor_1_out, and_3_out);
  // Probe on nor_2_out
endmodule
