// Logisim project frequency_divider_redundant.circ as structural Verilog: 2 circuits, main circuit main
module main (
);

  wire clock_1_out, not_1_out, not_2_out, not_3_out, not_4_out, not_5_out, not_6_out,
       pass_transistor_1_out_3, pass_transistor_2_out_3, pass_transistor_3_out_3, pass_transistor_4_out_3;

  Pass_Transistor pass_transistor_1 (.in_1(not_6_out), .out_3(pass_transistor_1_out_3), .in_2(clock_1_out));
  Clock clock_1 (.out(clock_1_out));
  not not_1 (not_1_out, pass_transistor_1_out_3);
  not not_2 (not_2_out, clock_1_out);
  Pass_Transistor pass_transistor_2 (.in_1(not_1_out), .out_3(pass_transistor_2_out_3), .in_2(not_2_out));
  not not_3 (not_3_out, pass_transistor_2_out_3);
  Pass_Transistor pass_transistor_3 (.in_1(not_3_out), .out_3(pass_transistor_3_out_3), .in_2(clock_1_out));
  not not_4 (not_4_out, pass_transistor_3_out_3);
  Pass_Transistor pass_transistor_4 (.in_1(not_4_out), .out_3(pass_transistor_4_out_3), .in_2(not_2_out));
  not not_5 (not_5_out, pass_transistor_4_out_3);
  not not_6 (not_6_out, not_5_out);
endmodule

module Pass_Transistor (
  input  in_1,
  input  in_2,
  output out_3
);

  Register #(.width(1)) register_1 (.D(in_1), .en(1'b1), .Q(out_3), .clk(in_2));  // open: clr
endmodule
