// Logisim project horizontal_cell_counter_actual.circ as structural Verilog: 3 circuits, main circuit main
module main (
  input  INCREMENT
);

  wire and_1_out, and_2_out, and_3_out, and_4_out, F1_out, F2_out, LOAD_out, nand_1_out, nand_2_out,
       nand_3_out, nand_4_out, nand_5_out, nand_6_out, nand_7_out, nand_8_out, nor_1_out, nor_2_out,
       nor_3_out, nor_4_out, nor_5_out, nor_6_out, nor_7_out, nor_8_out, nor_9_out, nor_10_out, not_1_out,
       not_2_out, not_3_out, not_4_out, not_5_out, not_6_out, not_7_out, not_8_out, not_9_out, not_10_out,
       not_11_out, not_12_out, not_13_out, or_1_out, or_2_out, or_3_out, or_4_out, pass_transistor_2_1_out,
       pass_transistor_2_2_out, pass_transistor_2_4_out, pass_transistor_2_5_out, pass_transistor_2_7_out,
       pass_transistor_2_8_out, pass_transistor_2_10_out, pass_transistor_2_11_out, pass_transistor_2_13_out,
       pass_transistor_2_15_out, pass_transistor_2_16_out, pass_transistor_2_18_out,
       pass_transistor_2_19_out, pass_transistor_2_21_out, pass_transistor_2_22_out,
       pass_transistor_2_24_out, pass_transistor_2_25_out;

  Button LOAD (.out(LOAD_out));
  Clock F1 (.out(F1_out));
  not F2 (F2_out, F1_out);
  // Probe on nor_10_out
  Pass_Transistor_2 pass_transistor_2_1 (
    .in_2(LOAD_out), .IN(1'b0), .OUT(pass_transistor_2_1_out));  // open: CLEAR, PRESET
  and and_1 (and_1_out, INCREMENT, pass_transistor_2_1_out);
  nor nor_1 (nor_1_out, INCREMENT, pass_transistor_2_1_out);
  nor nor_2 (nor_2_out, and_1_out, nor_1_out);
  Pass_Transistor_2 pass_transistor_2_2 (
    .in_2(F2_out), .IN(nor_2_out), .OUT(pass_transistor_2_2_out));  // open: CLEAR, PRESET
  not not_1 (not_1_out, pass_transistor_2_2_out);
  Pass_Transistor_2 pass_transistor_2_3 (
    .in_2(F1_out), .IN(not_1_out), .OUT(pass_transistor_2_1_out));  // open: CLEAR, PRESET
  not not_2 (not_2_out, 1'b0);
  Pass_Transistor_2 pass_transistor_2_4 (
    .in_2(LOAD_out), .IN(not_2_out), .OUT(pass_transistor_2_4_out));  // open: CLEAR, PRESET
  or or_1 (or_1_out, nor_1_out, pass_transistor_2_4_out);
  nand nand_1 (nand_1_out, nor_1_out, pass_transistor_2_4_out);
  nand nand_2 (nand_2_out, or_1_out, nand_1_out);
  Pass_Transistor_2 pass_transistor_2_5 (
    .in_2(F2_out), .IN(nand_2_out), .OUT(pass_transistor_2_5_out));  // open: CLEAR, PRESET
  not not_3 (not_3_out, pass_transistor_2_5_out);
  Pass_Transistor_2 pass_transistor_2_6 (
    .in_2(F1_out), .IN(not_3_out), .OUT(pass_transistor_2_4_out));  // open: CLEAR, PRESET
  and and_2 (and_2_out, nand_1_out, pass_transistor_2_7_out);
  Pass_Transistor_2 pass_transistor_2_7 (
    .in_2(LOAD_out), .IN(1'b1), .OUT(pass_transistor_2_7_out));  // open: CLEAR, PRESET
  nor nor_3 (nor_3_out, and_2_out, nor_4_out);
  Pass_Transistor_2 pass_transistor_2_8 (
    .in_2(F2_out), .IN(nor_3_out), .OUT(pass_transistor_2_8_out));  // open: CLEAR, PRESET
  not not_4 (not_4_out, pass_transistor_2_8_out);
  nor nor_4 (nor_4_out, nand_1_out, pass_transistor_2_7_out);
  Pass_Transistor_2 pass_transistor_2_9 (
    .in_2(F1_out), .IN(not_4_out), .OUT(pass_transistor_2_7_out));  // open: CLEAR, PRESET
  not not_5 (not_5_out, 1'b1);
  Pass_Transistor_2 pass_transistor_2_10 (
    .in_2(LOAD_out), .IN(not_5_out), .OUT(pass_transistor_2_10_out));  // open: CLEAR, PRESET
  or or_2 (or_2_out, nor_4_out, pass_transistor_2_10_out);
  nand nand_3 (nand_3_out, or_2_out, nand_4_out);
  Pass_Transistor_2 pass_transistor_2_11 (
    .in_2(F2_out), .IN(nand_3_out), .OUT(pass_transistor_2_11_out));  // open: CLEAR, PRESET
  not not_6 (not_6_out, pass_transistor_2_11_out);
  nand nand_4 (nand_4_out, nor_4_out, pass_transistor_2_10_out);
  Pass_Transistor_2 pass_transistor_2_12 (
    .in_2(F1_out), .IN(not_6_out), .OUT(pass_transistor_2_10_out));  // open: CLEAR, PRESET
  Pass_Transistor_2 pass_transistor_2_13 (
    .in_2(LOAD_out), .IN(LOAD_out), .OUT(pass_transistor_2_13_out));  // open: CLEAR, PRESET
  Pass_Transistor_2 pass_transistor_2_14 (
    .in_2(F1_out), .IN(not_7_out), .OUT(pass_transistor_2_13_out));  // open: CLEAR, PRESET
  not not_7 (not_7_out, nor_5_out);
  nor nor_5 (nor_5_out, pass_transistor_2_5_out, pass_transistor_2_11_out, not_4_out, not_1_out);
  Pass_Transistor_2 pass_transistor_2_15 (
    .in_2(LOAD_out), .IN(1'b0), .OUT(pass_transistor_2_15_out));  // open: CLEAR, PRESET
  and and_3 (and_3_out, pass_transistor_2_13_out, pass_transistor_2_15_out);
  nor nor_6 (nor_6_out, pass_transistor_2_13_out, pass_transistor_2_15_out);
  nor nor_7 (nor_7_out, and_3_out, nor_6_out);
  Pass_Transistor_2 pass_transistor_2_16 (
    .in_2(F2_out), .IN(nor_7_out), .OUT(pass_transistor_2_16_out));  // open: CLEAR, PRESET
  not not_8 (not_8_out, pass_transistor_2_16_out);
  Pass_Transistor_2 pass_transistor_2_17 (
    .in_2(F1_out), .IN(not_8_out), .OUT(pass_transistor_2_15_out));  // open: CLEAR, PRESET
  or or_3 (or_3_out, nor_6_out, pass_transistor_2_18_out);
  not not_9 (not_9_out, 1'b1);
  Pass_Transistor_2 pass_transistor_2_18 (
    .in_2(LOAD_out), .IN(not_9_out), .OUT(pass_transistor_2_18_out));  // open: CLEAR, PRESET
  nand nand_5 (nand_5_out, or_3_out, nand_6_out);
  Pass_Transistor_2 pass_transistor_2_19 (
    .in_2(F2_out), .IN(nand_5_out), .OUT(pass_transistor_2_19_out));  // open: CLEAR, PRESET
  not not_10 (not_10_out, pass_transistor_2_19_out);
  nand nand_6 (nand_6_out, nor_6_out, pass_transistor_2_18_out);
  Pass_Transistor_2 pass_transistor_2_20 (
    .in_2(F1_out), .IN(not_10_out), .OUT(pass_transistor_2_18_out));  // open: CLEAR, PRESET
  Pass_Transistor_2 pass_transistor_2_21 (
    .in_2(LOAD_out), .IN(1'b0), .OUT(pass_transistor_2_21_out));  // open: CLEAR, PRESET
  and and_4 (and_4_out, nand_6_out, pass_transistor_2_21_out);
  nor nor_8 (nor_8_out, and_4_out, nor_9_out);
  Pass_Transistor_2 pass_transistor_2_22 (
    .in_2(F2_out), .IN(nor_8_out), .OUT(pass_transistor_2_22_out));  // open: CLEAR, PRESET
  not not_11 (not_11_out, pass_transistor_2_22_out);
  nor nor_9 (nor_9_out, nand_6_out, pass_transistor_2_21_out);
  Pass_Transistor_2 pass_transistor_2_23 (
    .in_2(F1_out), .IN(not_11_out), .OUT(pass_transistor_2_21_out));  // open: CLEAR, PRESET
  not not_12 (not_12_out, 1'b0);
  Pass_Transistor_2 pass_transistor_2_24 (
    .in_2(LOAD_out), .IN(not_12_out), .OUT(pass_transistor_2_24_out));  // open: CLEAR, PRESET
  or or_4 (or_4_out, nor_9_out, pass_transistor_2_24_out);
  nand nand_7 (nand_7_out, or_4_out, nand_8_out);
  Pass_Transistor_2 pass_transistor_2_25 (
    .in_2(F2_out), .IN(nand_7_out), .OUT(pass_transistor_2_25_out));  // open: CLEAR, PRESET
  not not_13 (not_13_out, pass_transistor_2_25_out);
  nand nand_8 (nand_8_out, nor_9_out, pass_transistor_2_24_out);
  Pass_Transistor_2 pass_transistor_2_26 (
    .in_2(F1_out), .IN(not_13_out), .OUT(pass_transistor_2_24_out));  // open: CLEAR, PRESET
  nor nor_10 (nor_10_out, pass_transistor_2_19_out, pass_transistor_2_25_out, not_7_out, not_11_out, not_8_out);
endmodule

module Pass_Transistor (
  input  in_1,
  input  in_2,
  output out_3
);

  Register #(.width(1)) register_1 (.D(in_1), .en(1'b1), .Q(out_3), .clk(in_2));  // open: clr
endmodule

module Pass_Transistor_2 (
  input  IN,
  input  in_2,
  input  CLEAR,
  input  PRESET,
  output OUT
);

  D_Flip_Flop d_ff_1 (.clk(in_2), .D(IN), .Q(OUT), .preset(PRESET), .en(1'b1), .reset(CLEAR));  // open: Qn
endmodule
