// Logisim project horizontal_counter_actual_2.circ as structural Verilog: 3 circuits, main circuit main
module main (
  input  RESET
);

  wire and_1_out, and_2_out, and_3_out, and_4_out, F1_out, F2_out, nand_1_out, nand_2_out, nand_3_out,
       nand_4_out, nand_5_out, nand_6_out, nand_7_out, nand_8_out, nor_1_out, nor_2_out, nor_3_out,
       nor_4_out, nor_5_out, nor_6_out, nor_7_out, nor_8_out, nor_9_out, not_1_out, not_2_out, not_3_out,
       not_4_out, not_5_out, not_6_out, not_7_out, not_8_out, not_9_out, not_10_out, not_11_out, not_12_out,
       not_13_out, not_14_out, not_15_out, not_16_out, not_17_out, or_1_out, or_2_out, or_3_out, or_4_out,
       pass_transistor_1_out_3, pass_transistor_2_1_out, pass_transistor_2_2_out, pass_transistor_2_3_out,
       pass_transistor_2_4_out, pass_transistor_2_5_out, pass_transistor_2_6_out, pass_transistor_2_7_out,
       pass_transistor_2_8_out, pass_transistor_2_9_out, pass_transistor_2_out_3, pass_transistor_3_out_3,
       pass_transistor_4_out_3, pass_transistor_5_out_3, pass_transistor_6_out_3, pass_transistor_7_out_3,
       pass_transistor_8_out_3, transistor_1_out, transistor_2_out, transistor_3_out, transistor_4_out,
       transistor_5_out, transistor_6_out, transistor_7_out, transistor_8_out, transistor_9_out;

  // Probe on not_2_out
  Transistor #(.\type ("n")) transistor_1 (.in(F1_out), .out(transistor_1_out), .gate(F2_out));
  and and_1 (and_1_out, RESET, pass_transistor_2_1_out);
  // Probe on not_1_out
  not not_1 (not_1_out, not_2_out);
  not not_2 (not_2_out, pass_transistor_1_out_3);
  Pass_Transistor pass_transistor_1 (.in_1(nor_1_out), .out_3(pass_transistor_1_out_3), .in_2(F2_out));
  nor nor_1 (nor_1_out, and_1_out, nor_2_out);
  nor nor_2 (nor_2_out, RESET, pass_transistor_2_1_out);
  Pass_Transistor_2 pass_transistor_2_1 (
    .in_2(F1_out), .IN(not_2_out), .OUT(pass_transistor_2_1_out));  // open: CLEAR, PRESET
  Transistor #(.\type ("n")) transistor_2 (.in(pass_transistor_2_1_out), .out(transistor_2_out), .gate(RESET));
  // Probe on not_3_out
  not not_3 (not_3_out, not_4_out);
  or or_1 (or_1_out, nor_2_out, pass_transistor_2_2_out);
  // Probe on not_4_out
  not not_4 (not_4_out, pass_transistor_2_out_3);
  Pass_Transistor pass_transistor_2 (.in_1(nand_1_out), .out_3(pass_transistor_2_out_3), .in_2(F2_out));
  nand nand_1 (nand_1_out, or_1_out, nand_2_out);
  nand nand_2 (nand_2_out, nor_2_out, pass_transistor_2_2_out);
  Pass_Transistor_2 pass_transistor_2_2 (
    .in_2(F1_out), .IN(not_4_out), .OUT(pass_transistor_2_2_out));  // open: CLEAR, PRESET
  Transistor #(.\type ("n")) transistor_3 (.in(pass_transistor_2_2_out), .out(transistor_3_out), .gate(RESET));
  // Probe on not_5_out
  and and_2 (and_2_out, nand_2_out, pass_transistor_2_3_out);
  not not_5 (not_5_out, pass_transistor_3_out_3);
  Pass_Transistor pass_transistor_3 (.in_1(nor_3_out), .out_3(pass_transistor_3_out_3), .in_2(F2_out));
  nor nor_3 (nor_3_out, and_2_out, nor_4_out);
  // Probe on not_6_out
  not not_6 (not_6_out, not_5_out);
  Pass_Transistor_2 pass_transistor_2_3 (
    .in_2(F1_out), .IN(not_5_out), .OUT(pass_transistor_2_3_out));  // open: CLEAR, PRESET
  Transistor #(.\type ("n")) transistor_4 (.in(pass_transistor_2_3_out), .out(transistor_4_out), .gate(RESET));
  nor nor_4 (nor_4_out, nand_2_out, pass_transistor_2_3_out);
  // Probe on not_7_out
  not not_7 (not_7_out, not_8_out);
  not not_8 (not_8_out, pass_transistor_4_out_3);
  Pass_Transistor pass_transistor_4 (.in_1(nand_3_out), .out_3(pass_transistor_4_out_3), .in_2(F2_out));
  nand nand_3 (nand_3_out, or_2_out, nand_4_out);
  or or_2 (or_2_out, nor_4_out, pass_transistor_2_4_out);
  // Probe on not_8_out
  Transistor #(.\type ("n")) transistor_5 (.in(pass_transistor_2_4_out), .out(transistor_5_out), .gate(RESET));
  nand nand_4 (nand_4_out, nor_4_out, pass_transistor_2_4_out);
  Pass_Transistor_2 pass_transistor_2_4 (
    .in_2(F1_out), .IN(not_8_out), .OUT(pass_transistor_2_4_out));  // open: CLEAR, PRESET
  nor nor_5 (nor_5_out, not_2_out, not_5_out, pass_transistor_4_out_3, pass_transistor_2_out_3);
  not not_9 (not_9_out, nor_5_out);
  Pass_Transistor_2 pass_transistor_2_5 (
    .in_2(F1_out), .IN(not_9_out), .OUT(pass_transistor_2_5_out));  // open: CLEAR, PRESET
  // Probe on not_11_out
  and and_3 (and_3_out, pass_transistor_2_5_out, pass_transistor_2_6_out);
  // Probe on not_10_out
  not not_10 (not_10_out, not_11_out);
  not not_11 (not_11_out, pass_transistor_5_out_3);
  Pass_Transistor pass_transistor_5 (.in_1(nor_6_out), .out_3(pass_transistor_5_out_3), .in_2(F2_out));
  nor nor_6 (nor_6_out, and_3_out, nor_7_out);
  nor nor_7 (nor_7_out, pass_transistor_2_5_out, pass_transistor_2_6_out);
  Pass_Transistor_2 pass_transistor_2_6 (
    .in_2(F1_out), .IN(not_11_out), .OUT(pass_transistor_2_6_out));  // open: CLEAR, PRESET
  Transistor #(.\type ("n")) transistor_6 (.in(pass_transistor_2_6_out), .out(transistor_6_out), .gate(RESET));
  // Probe on not_12_out
  not not_12 (not_12_out, not_13_out);
  or or_3 (or_3_out, nor_7_out, pass_transistor_2_7_out);
  not not_13 (not_13_out, pass_transistor_6_out_3);
  Pass_Transistor pass_transistor_6 (.in_1(nand_5_out), .out_3(pass_transistor_6_out_3), .in_2(F2_out));
  nand nand_5 (nand_5_out, or_3_out, nand_6_out);
  // Probe on not_13_out
  Pass_Transistor_2 pass_transistor_2_7 (
    .in_2(F1_out), .IN(not_13_out), .OUT(pass_transistor_2_7_out));  // open: CLEAR, PRESET
  Transistor #(.\type ("n")) transistor_7 (.in(pass_transistor_2_7_out), .out(transistor_7_out), .gate(RESET));
  nand nand_6 (nand_6_out, nor_7_out, pass_transistor_2_7_out);
  // Probe on not_14_out
  not not_14 (not_14_out, pass_transistor_7_out_3);
  Pass_Transistor pass_transistor_7 (.in_1(nor_8_out), .out_3(pass_transistor_7_out_3), .in_2(F2_out));
  nor nor_8 (nor_8_out, and_4_out, nor_9_out);
  and and_4 (and_4_out, nand_6_out, pass_transistor_2_8_out);
  // Probe on not_15_out
  not not_15 (not_15_out, not_14_out);
  Transistor #(.\type ("n")) transistor_8 (.in(pass_transistor_2_8_out), .out(transistor_8_out), .gate(RESET));
  nor nor_9 (nor_9_out, nand_6_out, pass_transistor_2_8_out);
  Pass_Transistor_2 pass_transistor_2_8 (
    .in_2(F1_out), .IN(not_14_out), .OUT(pass_transistor_2_8_out));  // open: CLEAR, PRESET
  // Probe on not_16_out
  not not_16 (not_16_out, not_17_out);
  not not_17 (not_17_out, pass_transistor_8_out_3);
  Pass_Transistor pass_transistor_8 (.in_1(nand_7_out), .out_3(pass_transistor_8_out_3), .in_2(F2_out));
  nand nand_7 (nand_7_out, or_4_out, nand_8_out);
  or or_4 (or_4_out, nor_9_out, pass_transistor_2_9_out);
  // Probe on not_17_out
  Transistor #(.\type ("n")) transistor_9 (.in(pass_transistor_2_9_out), .out(transistor_9_out), .gate(RESET));
  nand nand_8 (nand_8_out, nor_9_out, pass_transistor_2_9_out);
  Pass_Transistor_2 pass_transistor_2_9 (
    .in_2(F1_out), .IN(not_17_out), .OUT(pass_transistor_2_9_out));  // open: CLEAR, PRESET
  not F2 (F2_out, F1_out);
  Clock F1 (.out(F1_out));
  // also tied to GND on the sheet: {transistor_1_out, transistor_3_out, transistor_5_out, transistor_7_out, transistor_9_out}
  // also tied to VCC on the sheet: {transistor_2_out, transistor_4_out, transistor_6_out, transistor_8_out}
endmodule

module Pass_Transistor (
  input  in_1,
  input  in_2,
  output out_3
);

  Register #(.width(1)) register_1 (.D(in_1), .en(1'b1), .Q(out_3), .clk(in_2));  // open: clr
endmodule

module Pass_Transistor_2 (
  input  IN,
  input  in_2,
  input  CLEAR,
  input  PRESET,
  output OUT
);

  D_Flip_Flop d_ff_1 (.clk(in_2), .D(IN), .Q(OUT), .preset(PRESET), .en(1'b1), .reset(CLEAR));  // open: Qn
endmodule
