// Logisim project noise_shift_register_8.circ as structural Verilog: 3 circuits, main circuit main
module main (
  input  CR_D_7_prime,
  input  CNT_RELOAD,
  input  F1,
  input  F2,
  output NSR0,
  output NSR1,
  output NSR2,
  output NSR4,
  output NSR5,
  output NSR6,
  output NSR7,
  output NSR8,
  output NSR9,
  output NSR10,
  output NSR11,
  output NSR13
);

  wire nand_1_out, nor_1_out, nor_2_out, nor_3_out, not_1_out, not_2_out, not_3_out, not_4_out, not_6_out,
       not_8_out, not_10_out, not_11_out, not_12_out, not_14_out, not_16_out, not_18_out, not_20_out,
       not_22_out, not_24_out, not_26_out, not_28_out, not_29_out, not_30_out, not_32_out, not_33_out,
       not_34_out, not_35_out, pass_transistor_1_out_3, pass_transistor_2_out_3, pass_transistor_3_out_3,
       pass_transistor_4_out_3, pass_transistor_5_out_3, pass_transistor_6_out_3, pass_transistor_7_out_3,
       pass_transistor_8_out_3, pass_transistor_9_out_3, pass_transistor_10_out_3, pass_transistor_11_out_3,
       pass_transistor_12_out_3, pass_transistor_13_out_3, pass_transistor_14_out_3,
       pass_transistor_15_out_3, pass_transistor_16_out_3, pass_transistor_17_out_3,
       pass_transistor_18_out_3, pass_transistor_19_out_3, pass_transistor_20_out_3,
       pass_transistor_21_out_3, pass_transistor_22_out_3, pass_transistor_23_out_3,
       pass_transistor_24_out_3, pass_transistor_25_out_3, pass_transistor_26_out_3,
       pass_transistor_27_out_3, pass_transistor_28_out_3, pass_transistor_29_out_3,
       pass_transistor_30_out_3, pass_transistor_31_out_3, pass_transistor_32_out_3,
       pass_transistor_33_out_3, pass_transistor_34_out_3, xnor_1_out, xor_1_out, xor_2_out;

  not not_1 (not_1_out, CNT_RELOAD);
  Pass_Transistor pass_transistor_1 (.in_1(CNT_RELOAD), .out_3(pass_transistor_1_out_3), .in_2(F1));
  not not_2 (not_2_out, CR_D_7_prime);
  xor xor_1 (xor_1_out, not_35_out, not_33_out);
  xor xor_2 (xor_2_out, not_29_out, not_11_out);
  not not_3 (not_3_out, pass_transistor_1_out_3);
  Pass_Transistor pass_transistor_2 (.in_1(not_3_out), .out_3(pass_transistor_2_out_3), .in_2(F2));
  Pass_Transistor pass_transistor_3 (.in_1(nand_1_out), .out_3(pass_transistor_3_out_3), .in_2(nor_1_out));
  Transistor #(.\type ("n"), .gate("br")) transistor_1 (.in(NSR0), .out(pass_transistor_3_out_3), .gate(nor_3_out));
  Pass_Transistor pass_transistor_4 (.in_1(NSR0), .out_3(pass_transistor_4_out_3), .in_2(nor_1_out));
  Transistor #(.\type ("n"), .gate("br")) transistor_2 (.in(NSR1), .out(pass_transistor_4_out_3), .gate(nor_3_out));
  Pass_Transistor pass_transistor_5 (.in_1(NSR1), .out_3(pass_transistor_5_out_3), .in_2(nor_1_out));
  Transistor #(.\type ("n"), .gate("br")) transistor_3 (.in(NSR2), .out(pass_transistor_5_out_3), .gate(nor_3_out));
  Pass_Transistor pass_transistor_6 (.in_1(NSR2), .out_3(pass_transistor_6_out_3), .in_2(nor_1_out));
  Transistor #(.\type ("n"), .gate("br")) transistor_4 (
    .in(not_11_out), .out(pass_transistor_6_out_3), .gate(nor_3_out));
  Pass_Transistor pass_transistor_7 (.in_1(not_11_out), .out_3(pass_transistor_7_out_3), .in_2(nor_1_out));
  Transistor #(.\type ("n"), .gate("br")) transistor_5 (.in(NSR4), .out(pass_transistor_7_out_3), .gate(nor_3_out));
  Pass_Transistor pass_transistor_8 (.in_1(NSR4), .out_3(pass_transistor_8_out_3), .in_2(nor_1_out));
  Transistor #(.\type ("n"), .gate("br")) transistor_6 (.in(NSR5), .out(pass_transistor_8_out_3), .gate(nor_3_out));
  Pass_Transistor pass_transistor_9 (.in_1(NSR5), .out_3(pass_transistor_9_out_3), .in_2(nor_1_out));
  Transistor #(.\type ("n"), .gate("br")) transistor_7 (.in(NSR6), .out(pass_transistor_9_out_3), .gate(nor_3_out));
  Pass_Transistor pass_transistor_10 (.in_1(NSR6), .out_3(pass_transistor_10_out_3), .in_2(nor_1_out));
  Transistor #(.\type ("n"), .gate("br")) transistor_8 (.in(NSR7), .out(pass_transistor_10_out_3), .gate(nor_3_out));
  Pass_Transistor pass_transistor_11 (.in_1(NSR7), .out_3(pass_transistor_11_out_3), .in_2(nor_1_out));
  Transistor #(.\type ("n"), .gate("br")) transistor_9 (.in(NSR8), .out(pass_transistor_11_out_3), .gate(nor_3_out));
  Pass_Transistor pass_transistor_12 (.in_1(NSR8), .out_3(pass_transistor_12_out_3), .in_2(nor_1_out));
  Transistor #(.\type ("n"), .gate("br")) transistor_10 (.in(NSR9), .out(pass_transistor_12_out_3), .gate(nor_3_out));
  Pass_Transistor pass_transistor_13 (.in_1(NSR9), .out_3(pass_transistor_13_out_3), .in_2(nor_1_out));
  Transistor #(.\type ("n"), .gate("br")) transistor_11 (.in(NSR10), .out(pass_transistor_13_out_3), .gate(nor_3_out));
  Pass_Transistor pass_transistor_14 (.in_1(NSR10), .out_3(pass_transistor_14_out_3), .in_2(nor_1_out));
  Transistor #(.\type ("n"), .gate("br")) transistor_12 (.in(NSR11), .out(pass_transistor_14_out_3), .gate(nor_3_out));
  Pass_Transistor pass_transistor_15 (.in_1(NSR11), .out_3(pass_transistor_15_out_3), .in_2(nor_1_out));
  Transistor #(.\type ("n"), .gate("br")) transistor_13 (
    .in(not_29_out), .out(pass_transistor_15_out_3), .gate(nor_3_out));
  Pass_Transistor pass_transistor_16 (.in_1(not_29_out), .out_3(pass_transistor_16_out_3), .in_2(nor_1_out));
  Transistor #(.\type ("n"), .gate("br")) transistor_14 (.in(NSR13), .out(pass_transistor_16_out_3), .gate(nor_3_out));
  Pass_Transistor pass_transistor_17 (.in_1(NSR13), .out_3(pass_transistor_17_out_3), .in_2(nor_1_out));
  Transistor #(.\type ("n"), .gate("br")) transistor_15 (
    .in(not_33_out), .out(pass_transistor_17_out_3), .gate(nor_3_out));
  Pass_Transistor pass_transistor_18 (.in_1(not_33_out), .out_3(pass_transistor_18_out_3), .in_2(nor_1_out));
  Transistor #(.\type ("n"), .gate("br")) transistor_16 (
    .in(not_35_out), .out(pass_transistor_18_out_3), .gate(nor_3_out));
  nor nor_1 (nor_1_out, pass_transistor_1_out_3, nor_2_out);
  nor nor_2 (nor_2_out, nor_1_out, not_3_out);
  nor nor_3 (nor_3_out, pass_transistor_2_out_3, not_1_out);
  xnor xnor_1 (xnor_1_out, xor_1_out, xor_2_out);
  not not_4 (not_4_out, pass_transistor_3_out_3);
  not not_5 (NSR0, pass_transistor_19_out_3);
  not not_6 (not_6_out, pass_transistor_4_out_3);
  not not_7 (NSR1, pass_transistor_20_out_3);
  not not_8 (not_8_out, pass_transistor_5_out_3);
  not not_9 (NSR2, pass_transistor_21_out_3);
  not not_10 (not_10_out, pass_transistor_6_out_3);
  not not_11 (not_11_out, pass_transistor_22_out_3);
  not not_12 (not_12_out, pass_transistor_7_out_3);
  not not_13 (NSR4, pass_transistor_23_out_3);
  not not_14 (not_14_out, pass_transistor_8_out_3);
  not not_15 (NSR5, pass_transistor_24_out_3);
  not not_16 (not_16_out, pass_transistor_9_out_3);
  not not_17 (NSR6, pass_transistor_25_out_3);
  not not_18 (not_18_out, pass_transistor_10_out_3);
  not not_19 (NSR7, pass_transistor_26_out_3);
  not not_20 (not_20_out, pass_transistor_11_out_3);
  not not_21 (NSR8, pass_transistor_27_out_3);
  not not_22 (not_22_out, pass_transistor_12_out_3);
  not not_23 (NSR9, pass_transistor_28_out_3);
  not not_24 (not_24_out, pass_transistor_13_out_3);
  not not_25 (NSR10, pass_transistor_29_out_3);
  not not_26 (not_26_out, pass_transistor_14_out_3);
  not not_27 (NSR11, pass_transistor_30_out_3);
  not not_28 (not_28_out, pass_transistor_15_out_3);
  not not_29 (not_29_out, pass_transistor_31_out_3);
  not not_30 (not_30_out, pass_transistor_16_out_3);
  not not_31 (NSR13, pass_transistor_32_out_3);
  not not_32 (not_32_out, pass_transistor_17_out_3);
  not not_33 (not_33_out, pass_transistor_33_out_3);
  not not_34 (not_34_out, pass_transistor_18_out_3);
  not not_35 (not_35_out, pass_transistor_34_out_3);
  nand nand_1 (nand_1_out, not_2_out, xnor_1_out);
  Pass_Transistor pass_transistor_19 (.in_1(not_4_out), .out_3(pass_transistor_19_out_3), .in_2(nor_2_out));
  Pass_Transistor pass_transistor_20 (.in_1(not_6_out), .out_3(pass_transistor_20_out_3), .in_2(nor_2_out));
  Pass_Transistor pass_transistor_21 (.in_1(not_8_out), .out_3(pass_transistor_21_out_3), .in_2(nor_2_out));
  Pass_Transistor pass_transistor_22 (.in_1(not_10_out), .out_3(pass_transistor_22_out_3), .in_2(nor_2_out));
  Pass_Transistor pass_transistor_23 (.in_1(not_12_out), .out_3(pass_transistor_23_out_3), .in_2(nor_2_out));
  Pass_Transistor pass_transistor_24 (.in_1(not_14_out), .out_3(pass_transistor_24_out_3), .in_2(nor_2_out));
  Pass_Transistor pass_transistor_25 (.in_1(not_16_out), .out_3(pass_transistor_25_out_3), .in_2(nor_2_out));
  Pass_Transistor pass_transistor_26 (.in_1(not_18_out), .out_3(pass_transistor_26_out_3), .in_2(nor_2_out));
  Pass_Transistor pass_transistor_27 (.in_1(not_20_out), .out_3(pass_transistor_27_out_3), .in_2(nor_2_out));
  Pass_Transistor pass_transistor_28 (.in_1(not_22_out), .out_3(pass_transistor_28_out_3), .in_2(nor_2_out));
  Pass_Transistor pass_transistor_29 (.in_1(not_24_out), .out_3(pass_transistor_29_out_3), .in_2(nor_2_out));
  Pass_Transistor pass_transistor_30 (.in_1(not_26_out), .out_3(pass_transistor_30_out_3), .in_2(nor_2_out));
  Pass_Transistor pass_transistor_31 (.in_1(not_28_out), .out_3(pass_transistor_31_out_3), .in_2(nor_2_out));
  Pass_Transistor pass_transistor_32 (.in_1(not_30_out), .out_3(pass_transistor_32_out_3), .in_2(nor_2_out));
  Pass_Transistor pass_transistor_33 (.in_1(not_32_out), .out_3(pass_transistor_33_out_3), .in_2(nor_2_out));
  Pass_Transistor pass_transistor_34 (.in_1(not_34_out), .out_3(pass_transistor_34_out_3), .in_2(nor_2_out));

  // Notes on the sheet:
  //   NSR12
  //   NSR3
  //   NSR14
  //   NSR15
  //   CR-D-7
endmodule

module Pass_Transistor (
  input  in_1,
  input  in_2,
  output out_3
);

  Register #(.width(1)) register_1 (.D(in_1), .en(1'b1), .Q(out_3), .clk(in_2));  // open: clr
endmodule

module Pass_Transistor_2 (
  input  IN,
  input  in_2,
  input  CLEAR,
  input  PRESET,
  output OUT
);

  D_Flip_Flop d_ff_1 (.clk(in_2), .D(IN), .Q(OUT), .preset(PRESET), .en(1'b1), .reset(CLEAR));  // open: Qn
endmodule
