// Logisim project reset_logic_4.circ as structural Verilog: 2 circuits, main circuit main
module main (
  input  Y_311,
  input  Y_312,
  input  FORCE_VCNT_RESET,
  input  X___0,
  input  X___35
);

  wire controlled_buffer_1_out, F1_out, F2_out, nor_1_out, nor_2_out, nor_3_out, nor_4_out, not_2_out,
       not_3_out, not_4_out, not_5_out, not_6_out, pass_transistor_1_out_3, pass_transistor_2_out_3,
       pass_transistor_3_out_3, pass_transistor_4_out_3, pass_transistor_5_out_3, pass_transistor_6_out_3,
       pass_transistor_7_out_3, transistor_1_out, transistor_2_out;

  Clock F1 (.out(F1_out));
  not F2 (F2_out, F1_out);
  Pass_Transistor pass_transistor_1 (.in_1(nor_1_out), .out_3(pass_transistor_1_out_3), .in_2(F1_out));
  // NOT_Gate not_1 has open pins: in=pass_transistor_1_out_3, out=open
  nor nor_1 (nor_1_out, controlled_buffer_1_out, not_2_out);
  Pass_Transistor pass_transistor_2 (.in_1(Y_311), .out_3(pass_transistor_2_out_3), .in_2(F1_out));
  // Probe on not_2_out
  Pass_Transistor pass_transistor_3 (.in_1(Y_312), .out_3(pass_transistor_3_out_3), .in_2(F1_out));
  nor nor_2 (nor_2_out, pass_transistor_2_out_3, pass_transistor_3_out_3, pass_transistor_5_out_3);
  Pass_Transistor pass_transistor_4 (.in_1(nor_2_out), .out_3(pass_transistor_4_out_3), .in_2(F2_out));
  not not_2 (not_2_out, pass_transistor_4_out_3);
  Pass_Transistor pass_transistor_5 (.in_1(FORCE_VCNT_RESET), .out_3(pass_transistor_5_out_3), .in_2(F1_out));
  Transistor #(.\type ("n")) transistor_1 (.in(1'b0), .out(transistor_1_out), .gate(pass_transistor_5_out_3));
  not not_3 (not_3_out, FORCE_VCNT_RESET);
  assign controlled_buffer_1_out = FORCE_VCNT_RESET ? transistor_1_out : 1'bz;  // Controlled_Buffer controlled_buffer_1
  nor nor_3 (nor_3_out, X___0, X___35);
  assign controlled_buffer_1_out = not_3_out ? nor_3_out : 1'bz;  // Controlled_Buffer controlled_buffer_2
  not not_4 (not_4_out, pass_transistor_6_out_3);
  Pass_Transistor pass_transistor_6 (.in_1(nor_4_out), .out_3(pass_transistor_6_out_3), .in_2(F1_out));
  nor nor_4 (nor_4_out, controlled_buffer_1_out, pass_transistor_4_out_3);
  not not_5 (not_5_out, not_4_out);
  not not_6 (not_6_out, nor_4_out);
  Pass_Transistor pass_transistor_7 (.in_1(not_6_out), .out_3(pass_transistor_7_out_3), .in_2(F2_out));
  Transistor #(.\type ("n")) transistor_2 (.in(F1_out), .out(transistor_2_out), .gate(pass_transistor_7_out_3));
  Transistor #(.\type ("n")) transistor_3 (.in(1'b0), .out(transistor_2_out), .gate(nor_4_out));
  // Probe on not_5_out
  // Probe on transistor_2_out
  // Probe on nothing

  // Notes on the sheet:
  //   X=0,35 ON LAST LINE
endmodule

module Pass_Transistor (
  input  in_1,
  input  in_2,
  output out_3
);

  Register #(.width(1)) register_1 (.D(in_1), .en(1'b1), .Q(out_3), .clk(in_2));  // open: clr
endmodule
