// Logisim project screen_origin_comparators.circ as structural Verilog: 1 circuit, main circuit main
module main (
  input  INT,
  input  SX0,
  input  SX1,
  input  SX2,
  input  SX3,
  input  SX4,
  input  SX5,
  input  SX6,
  input  SY0,
  input  SY1,
  input  SY2,
  input  SY3,
  input  SY4,
  input  SY5,
  input  SY6,
  input  SY7,
  input  HC0,
  input  HC1,
  input  HC2,
  input  HC3,
  input  HC4,
  input  HC5,
  input  HC6,
  input  VC0,
  input  VC1,
  input  VC2,
  input  VC3,
  input  VC4,
  input  VC5,
  input  VC6,
  input  VC7,
  input  VC8
);

  wire and_1_out, and_2_out, and_3_out, and_4_out, and_5_out, and_6_out, and_7_out, and_8_out, and_9_out,
       and_10_out, and_11_out, and_12_out, and_13_out, and_14_out, and_15_out, nor_1_out, nor_2_out,
       nor_3_out, nor_4_out, nor_5_out, nor_6_out, nor_7_out, nor_8_out, nor_9_out, nor_10_out, nor_11_out,
       nor_12_out, nor_13_out, nor_14_out, nor_15_out, nor_16_out, nor_17_out, nor_18_out, nor_19_out,
       nor_20_out, nor_21_out, nor_22_out, nor_23_out, nor_24_out, nor_25_out, nor_26_out, nor_27_out,
       nor_28_out, nor_29_out, nor_30_out, nor_31_out, nor_32_out;

  // Probe on INT
  nor nor_1 (nor_1_out, SX0, HC0);
  and and_1 (and_1_out, SX0, HC0);
  nor nor_2 (nor_2_out, SX1, HC1);
  and and_2 (and_2_out, SX1, HC1);
  nor nor_3 (nor_3_out, SX2, HC2);
  and and_3 (and_3_out, SX2, HC2);
  nor nor_4 (nor_4_out, SX3, HC3);
  and and_4 (and_4_out, SX3, HC3);
  nor nor_5 (nor_5_out, SX4, HC4);
  and and_5 (and_5_out, SX4, HC4);
  nor nor_6 (nor_6_out, SX5, HC5);
  and and_6 (and_6_out, SX5, HC5);
  nor nor_7 (nor_7_out, SX6, HC6);
  and and_7 (and_7_out, SX6, HC6);
  nor nor_8 (nor_8_out, nor_1_out, and_1_out);
  nor nor_9 (nor_9_out, nor_2_out, and_2_out);
  nor nor_10 (nor_10_out, nor_3_out, and_3_out);
  nor nor_11 (nor_11_out, nor_4_out, and_4_out);
  nor nor_12 (nor_12_out, nor_5_out, and_5_out);
  nor nor_13 (nor_13_out, nor_6_out, and_6_out);
  nor nor_14 (nor_14_out, nor_7_out, and_7_out);
  nor nor_15 (nor_15_out, nor_14_out, nor_13_out, nor_12_out, nor_11_out, nor_10_out, nor_9_out, nor_8_out);
  nor nor_16 (nor_16_out, nor_17_out, nor_18_out, nor_19_out, nor_20_out, nor_21_out, nor_22_out, nor_23_out, nor_24_out);
  nor nor_17 (nor_17_out, nor_25_out, and_8_out);
  nor nor_18 (nor_18_out, nor_26_out, and_9_out);
  nor nor_19 (nor_19_out, nor_27_out, and_10_out);
  nor nor_20 (nor_20_out, nor_28_out, and_11_out);
  nor nor_21 (nor_21_out, nor_29_out, and_12_out);
  nor nor_22 (nor_22_out, nor_30_out, and_13_out);
  nor nor_23 (nor_23_out, nor_31_out, and_14_out);
  nor nor_24 (nor_24_out, nor_32_out, and_15_out);
  nor nor_25 (nor_25_out, SY7, VC8);
  and and_8 (and_8_out, SY7, VC8);
  nor nor_26 (nor_26_out, SY6, VC7);
  and and_9 (and_9_out, SY6, VC7);
  nor nor_27 (nor_27_out, SY5, VC6);
  and and_10 (and_10_out, SY5, VC6);
  nor nor_28 (nor_28_out, SY4, VC5);
  and and_11 (and_11_out, SY4, VC5);
  nor nor_29 (nor_29_out, SY3, VC4);
  and and_12 (and_12_out, SY3, VC4);
  nor nor_30 (nor_30_out, SY2, VC3);
  and and_13 (and_13_out, SY2, VC3);
  nor nor_31 (nor_31_out, SY1, VC2);
  and and_14 (and_14_out, SY1, VC2);
  nor nor_32 (nor_32_out, SY0, VC1);
  and and_15 (and_15_out, SY0, VC1);
  // Probe on nor_16_out
  // Probe on nor_15_out
endmodule
