// Logisim project screen_origin_x_comparator.circ as structural Verilog: 1 circuit, main circuit main
module main (
  input  INT,
  input  SX0,
  input  SX1,
  input  SX2,
  input  SX3,
  input  SX4,
  input  SX5,
  input  SX6,
  input  HC0,
  input  HC1,
  input  HC2,
  input  HC3,
  input  HC4,
  input  HC5,
  input  HC6
);

  wire and_1_out, and_2_out, and_3_out, and_4_out, and_5_out, and_6_out, and_7_out, nor_1_out, nor_2_out,
       nor_3_out, nor_4_out, nor_5_out, nor_6_out, nor_7_out, nor_8_out, nor_9_out, nor_10_out, nor_11_out,
       nor_12_out, nor_13_out, nor_14_out, nor_15_out;

  nor nor_1 (nor_1_out, SX0, HC0);
  and and_1 (and_1_out, SX0, HC0);
  nor nor_2 (nor_2_out, SX1, HC1);
  and and_2 (and_2_out, SX1, HC1);
  nor nor_3 (nor_3_out, SX2, HC2);
  and and_3 (and_3_out, SX2, HC2);
  nor nor_4 (nor_4_out, SX3, HC3);
  and and_4 (and_4_out, SX3, HC3);
  nor nor_5 (nor_5_out, SX4, HC4);
  and and_5 (and_5_out, SX4, HC4);
  nor nor_6 (nor_6_out, SX5, HC5);
  and and_6 (and_6_out, SX5, HC5);
  nor nor_7 (nor_7_out, SX6, HC6);
  and and_7 (and_7_out, SX6, HC6);
  nor nor_8 (nor_8_out, nor_1_out, and_1_out);
  nor nor_9 (nor_9_out, nor_2_out, and_2_out);
  nor nor_10 (nor_10_out, nor_3_out, and_3_out);
  nor nor_11 (nor_11_out, nor_4_out, and_4_out);
  nor nor_12 (nor_12_out, nor_5_out, and_5_out);
  nor nor_13 (nor_13_out, nor_6_out, and_6_out);
  nor nor_14 (nor_14_out, nor_7_out, and_7_out);
  nor nor_15 (nor_15_out, nor_14_out, nor_13_out, nor_12_out, nor_11_out, nor_10_out, nor_9_out, nor_8_out);
  // Probe on nor_15_out
endmodule
