// Logisim project screen_origin_y_comparator.circ as structural Verilog: 1 circuit, main circuit main
module main (
  input  SY0,
  input  SY1,
  input  SY2,
  input  SY3,
  input  SY4,
  input  SY5,
  input  SY6,
  input  SY7,
  input  VC0,
  input  VC1,
  input  VC2,
  input  VC3,
  input  VC4,
  input  VC5,
  input  VC6,
  input  VC7,
  input  VC8
);

  wire and_1_out, and_2_out, and_3_out, and_4_out, and_5_out, and_6_out, and_7_out, and_8_out, nor_1_out,
       nor_2_out, nor_3_out, nor_4_out, nor_5_out, nor_6_out, nor_7_out, nor_8_out, nor_9_out, nor_10_out,
       nor_11_out, nor_12_out, nor_13_out, nor_14_out, nor_15_out, nor_16_out, nor_17_out;

  nor nor_1 (nor_1_out, nor_2_out, nor_3_out, nor_4_out, nor_5_out, nor_6_out, nor_7_out, nor_8_out, nor_9_out);
  nor nor_2 (nor_2_out, nor_10_out, and_1_out);
  nor nor_3 (nor_3_out, nor_11_out, and_2_out);
  nor nor_4 (nor_4_out, nor_12_out, and_3_out);
  nor nor_5 (nor_5_out, nor_13_out, and_4_out);
  nor nor_6 (nor_6_out, nor_14_out, and_5_out);
  nor nor_7 (nor_7_out, nor_15_out, and_6_out);
  nor nor_8 (nor_8_out, nor_16_out, and_7_out);
  nor nor_9 (nor_9_out, nor_17_out, and_8_out);
  nor nor_10 (nor_10_out, SY7, VC8);
  and and_1 (and_1_out, SY7, VC8);
  nor nor_11 (nor_11_out, SY6, VC7);
  and and_2 (and_2_out, SY6, VC7);
  nor nor_12 (nor_12_out, SY5, VC6);
  and and_3 (and_3_out, SY5, VC6);
  nor nor_13 (nor_13_out, SY4, VC5);
  and and_4 (and_4_out, SY4, VC5);
  nor nor_14 (nor_14_out, SY3, VC4);
  and and_5 (and_5_out, SY3, VC4);
  nor nor_15 (nor_15_out, SY2, VC3);
  and and_6 (and_6_out, SY2, VC3);
  nor nor_16 (nor_16_out, SY1, VC2);
  and and_7 (and_7_out, SY1, VC2);
  nor nor_17 (nor_17_out, SY0, VC1);
  and and_8 (and_8_out, SY0, VC1);
  // Probe on nor_1_out
endmodule
