// Logisim project screen_origin_y_comparator_single_cell.circ as structural Verilog: 1 circuit, main circuit main
module main (
  input  SY7,
  input  VCNT8
);

  wire and_1_out, nor_1_out, nor_2_out;

  // Probe on nor_1_out
  nor nor_1 (nor_1_out, nor_2_out, and_1_out);
  nor nor_2 (nor_2_out, SY7, VCNT8);
  and and_1 (and_1_out, SY7, VCNT8);
endmodule
