// Logisim project two_phase_non_overlapping_clock_2.circ as structural Verilog: 1 circuit, main circuit main
module main (
);

  wire IN1_out, nor_1_out, nor_2_out, not_1_out, not_2_out, not_3_out, not_4_out, not_5_out;

  // Probe on not_1_out
  // Probe on not_2_out
  not not_1 (not_1_out, not_3_out);
  not not_2 (not_2_out, not_4_out);
  nor nor_1 (nor_1_out, not_5_out, not_2_out);
  not not_3 (not_3_out, nor_1_out);
  nor nor_2 (nor_2_out, not_1_out, IN1_out);
  not not_4 (not_4_out, nor_2_out);
  not not_5 (not_5_out, IN1_out);
  Clock IN1 (.out(IN1_out));
endmodule
