// Logisim project vblank.circ as structural Verilog: 1 circuit, main circuit main
module main (
);

  wire button_1_out, clock_1_out, nor_1_out, nor_2_out, not_1_out, not_2_out, not_3_out, not_4_out,
       not_5_out, not_6_out, not_7_out, not_8_out, not_9_out, pull_resistor_1_node, transistor_10_out;
  wire [8:0] V_CNT_q;

  Clock clock_1 (.out(clock_1_out));
  Counter #(.width(9), .max('h137)) V_CNT (
    .load(1'b0), .count(1'b1), .Q(V_CNT_q), .clk(clock_1_out), .clr(button_1_out));  // open: D, carry
  Button button_1 (.out(button_1_out));
  not not_1 (not_1_out, V_CNT_q[0]);
  not not_2 (not_2_out, V_CNT_q[1]);
  not not_3 (not_3_out, V_CNT_q[2]);
  not not_4 (not_4_out, V_CNT_q[3]);
  not not_5 (not_5_out, V_CNT_q[4]);
  not not_6 (not_6_out, V_CNT_q[5]);
  not not_7 (not_7_out, V_CNT_q[6]);
  not not_8 (not_8_out, V_CNT_q[7]);
  not not_9 (not_9_out, V_CNT_q[8]);
  Pull_Resistor #(.pull(1)) pull_resistor_1 (.node(pull_resistor_1_node));
  Transistor #(.\type ("n")) transistor_1 (.in(1'b0), .out(pull_resistor_1_node), .gate(V_CNT_q[0]));
  Transistor #(.\type ("n")) transistor_2 (.in(1'b0), .out(pull_resistor_1_node), .gate(not_2_out));
  Transistor #(.\type ("n")) transistor_3 (.in(1'b0), .out(pull_resistor_1_node), .gate(V_CNT_q[2]));
  Transistor #(.\type ("n")) transistor_4 (.in(1'b0), .out(pull_resistor_1_node), .gate(not_4_out));
  Transistor #(.\type ("n")) transistor_5 (.in(1'b0), .out(pull_resistor_1_node), .gate(V_CNT_q[4]));
  Transistor #(.\type ("n")) transistor_6 (.in(1'b0), .out(pull_resistor_1_node), .gate(V_CNT_q[5]));
  Transistor #(.\type ("n")) transistor_7 (.in(1'b0), .out(pull_resistor_1_node), .gate(V_CNT_q[6]));
  Transistor #(.\type ("n")) transistor_8 (.in(1'b0), .out(pull_resistor_1_node), .gate(V_CNT_q[7]));
  Transistor #(.\type ("n")) transistor_9 (.in(1'b0), .out(pull_resistor_1_node), .gate(V_CNT_q[8]));
  Transistor #(.\type ("n")) transistor_10 (.in(1'b0), .out(transistor_10_out), .gate(not_1_out));
  Pull_Resistor #(.pull(1)) pull_resistor_2 (.node(transistor_10_out));
  Transistor #(.\type ("n")) transistor_11 (.in(1'b0), .out(transistor_10_out), .gate(V_CNT_q[1]));
  Transistor #(.\type ("n")) transistor_12 (.in(1'b0), .out(transistor_10_out), .gate(V_CNT_q[2]));
  Transistor #(.\type ("n")) transistor_13 (.in(1'b0), .out(transistor_10_out), .gate(V_CNT_q[3]));
  Transistor #(.\type ("n")) transistor_14 (.in(1'b0), .out(transistor_10_out), .gate(V_CNT_q[4]));
  Transistor #(.\type ("n")) transistor_15 (.in(1'b0), .out(transistor_10_out), .gate(V_CNT_q[5]));
  Transistor #(.\type ("n")) transistor_16 (.in(1'b0), .out(transistor_10_out), .gate(V_CNT_q[6]));
  Transistor #(.\type ("n")) transistor_17 (.in(1'b0), .out(transistor_10_out), .gate(V_CNT_q[7]));
  Transistor #(.\type ("n")) transistor_18 (.in(1'b0), .out(transistor_10_out), .gate(V_CNT_q[8]));
  nor nor_1 (nor_1_out, transistor_10_out, nor_2_out);
  nor nor_2 (nor_2_out, nor_1_out, pull_resistor_1_node);
  // Probe on nor_2_out
endmodule
