// Logisim project vblank2.circ as structural Verilog: 1 circuit, main circuit main
module main (
  input  INT
);

  wire button_1_out, clock_1_out, nor_1_out, nor_2_out, not_1_out, not_2_out, not_3_out, not_4_out,
       not_5_out, not_6_out, not_7_out, not_8_out, not_9_out, not_10_out, not_11_out, transistor_1_out,
       transistor_10_out;
  wire [9:0] V_CNT_q;

  Clock clock_1 (.out(clock_1_out));
  Counter #(.width(10), .max('h20)) V_CNT (
    .load(1'b0), .count(1'b1), .Q(V_CNT_q), .clk(clock_1_out), .clr(button_1_out));  // open: D, carry
  Button button_1 (.out(button_1_out));
  not not_1 (not_1_out, INT);
  not not_2 (not_2_out, V_CNT_q[0]);
  not not_3 (not_3_out, V_CNT_q[1]);
  not not_4 (not_4_out, V_CNT_q[2]);
  not not_5 (not_5_out, V_CNT_q[3]);
  not not_6 (not_6_out, V_CNT_q[4]);
  not not_7 (not_7_out, V_CNT_q[5]);
  not not_8 (not_8_out, V_CNT_q[6]);
  not not_9 (not_9_out, V_CNT_q[7]);
  not not_10 (not_10_out, V_CNT_q[8]);
  not not_11 (not_11_out, V_CNT_q[9]);
  Transistor #(.\type ("n")) transistor_1 (.in(1'b0), .out(transistor_1_out), .gate(V_CNT_q[1]));
  Transistor #(.\type ("n")) transistor_2 (.in(1'b0), .out(transistor_1_out), .gate(not_4_out));
  Transistor #(.\type ("n")) transistor_3 (.in(1'b0), .out(transistor_1_out), .gate(V_CNT_q[3]));
  Transistor #(.\type ("n")) transistor_4 (.in(1'b0), .out(transistor_1_out), .gate(not_6_out));
  Transistor #(.\type ("n")) transistor_5 (.in(1'b0), .out(transistor_1_out), .gate(V_CNT_q[5]));
  Transistor #(.\type ("n")) transistor_6 (.in(1'b0), .out(transistor_1_out), .gate(V_CNT_q[6]));
  Transistor #(.\type ("n")) transistor_7 (.in(1'b0), .out(transistor_1_out), .gate(V_CNT_q[7]));
  Transistor #(.\type ("n")) transistor_8 (.in(1'b0), .out(transistor_1_out), .gate(V_CNT_q[8]));
  Transistor #(.\type ("n")) transistor_9 (.in(1'b0), .out(transistor_1_out), .gate(V_CNT_q[9]));
  Pull_Resistor #(.pull(1)) pull_resistor_1 (.node(transistor_1_out));
  Transistor #(.\type ("n")) transistor_10 (.in(1'b0), .out(transistor_10_out), .gate(not_3_out));
  Transistor #(.\type ("n")) transistor_11 (.in(1'b0), .out(transistor_10_out), .gate(V_CNT_q[2]));
  Transistor #(.\type ("n")) transistor_12 (.in(1'b0), .out(transistor_10_out), .gate(V_CNT_q[3]));
  Transistor #(.\type ("n")) transistor_13 (.in(1'b0), .out(transistor_10_out), .gate(V_CNT_q[4]));
  Transistor #(.\type ("n")) transistor_14 (.in(1'b0), .out(transistor_10_out), .gate(V_CNT_q[5]));
  Transistor #(.\type ("n")) transistor_15 (.in(1'b0), .out(transistor_10_out), .gate(V_CNT_q[6]));
  Transistor #(.\type ("n")) transistor_16 (.in(1'b0), .out(transistor_10_out), .gate(V_CNT_q[7]));
  Transistor #(.\type ("n")) transistor_17 (.in(1'b0), .out(transistor_10_out), .gate(V_CNT_q[8]));
  Transistor #(.\type ("n")) transistor_18 (.in(1'b0), .out(transistor_10_out), .gate(V_CNT_q[9]));
  nor nor_1 (nor_1_out, nor_2_out, transistor_10_out);
  nor nor_2 (nor_2_out, transistor_1_out, nor_1_out);
  // Probe on nor_2_out
  Pull_Resistor #(.pull(1)) pull_resistor_2 (.node(transistor_10_out));
endmodule
