// Logisim project vertical_cell_counter_actual.circ as structural Verilog: 3 circuits, main circuit main
module main (
  input  N0,
  input  N1,
  input  N2,
  input  N3,
  input  N4,
  input  N5,
  input  INCREMENT_prime,
  input  F1,
  input  F2
);

  wire and_1_out, and_2_out, and_3_out, LOAD_out, nand_1_out, nand_2_out, nand_3_out, nand_4_out, nand_5_out,
       nand_6_out, nor_1_out, nor_2_out, nor_3_out, nor_4_out, nor_5_out, nor_6_out, nor_7_out, not_1_out,
       not_2_out, not_3_out, not_4_out, not_5_out, not_6_out, not_7_out, not_8_out, not_9_out, or_1_out,
       or_2_out, or_3_out, pass_transistor_2_1_out, pass_transistor_2_2_out, pass_transistor_2_4_out,
       pass_transistor_2_5_out, pass_transistor_2_7_out, pass_transistor_2_8_out, pass_transistor_2_10_out,
       pass_transistor_2_11_out, pass_transistor_2_13_out, pass_transistor_2_14_out,
       pass_transistor_2_16_out, pass_transistor_2_17_out;

  Button LOAD (.out(LOAD_out));
  // Probe on nor_7_out
  and and_1 (and_1_out, INCREMENT_prime, pass_transistor_2_1_out);
  Pass_Transistor_2 pass_transistor_2_1 (
    .in_2(LOAD_out), .IN(N0), .OUT(pass_transistor_2_1_out));  // open: CLEAR, PRESET
  nor nor_1 (nor_1_out, and_1_out, nor_2_out);
  Pass_Transistor_2 pass_transistor_2_2 (
    .in_2(F2), .IN(nor_1_out), .OUT(pass_transistor_2_2_out));  // open: CLEAR, PRESET
  not not_1 (not_1_out, pass_transistor_2_2_out);
  nor nor_2 (nor_2_out, INCREMENT_prime, pass_transistor_2_1_out);
  Pass_Transistor_2 pass_transistor_2_3 (
    .in_2(F1), .IN(not_1_out), .OUT(pass_transistor_2_1_out));  // open: CLEAR, PRESET
  not not_2 (not_2_out, N1);
  Pass_Transistor_2 pass_transistor_2_4 (
    .in_2(LOAD_out), .IN(not_2_out), .OUT(pass_transistor_2_4_out));  // open: CLEAR, PRESET
  or or_1 (or_1_out, nor_2_out, pass_transistor_2_4_out);
  nand nand_1 (nand_1_out, or_1_out, nand_2_out);
  Pass_Transistor_2 pass_transistor_2_5 (
    .in_2(F2), .IN(nand_1_out), .OUT(pass_transistor_2_5_out));  // open: CLEAR, PRESET
  not not_3 (not_3_out, pass_transistor_2_5_out);
  nand nand_2 (nand_2_out, nor_2_out, pass_transistor_2_4_out);
  Pass_Transistor_2 pass_transistor_2_6 (
    .in_2(F1), .IN(not_3_out), .OUT(pass_transistor_2_4_out));  // open: CLEAR, PRESET
  Pass_Transistor_2 pass_transistor_2_7 (
    .in_2(LOAD_out), .IN(N2), .OUT(pass_transistor_2_7_out));  // open: CLEAR, PRESET
  and and_2 (and_2_out, nand_2_out, pass_transistor_2_7_out);
  nor nor_3 (nor_3_out, nand_2_out, pass_transistor_2_7_out);
  nor nor_4 (nor_4_out, and_2_out, nor_3_out);
  Pass_Transistor_2 pass_transistor_2_8 (
    .in_2(F2), .IN(nor_4_out), .OUT(pass_transistor_2_8_out));  // open: CLEAR, PRESET
  not not_4 (not_4_out, pass_transistor_2_8_out);
  Pass_Transistor_2 pass_transistor_2_9 (
    .in_2(F1), .IN(not_4_out), .OUT(pass_transistor_2_7_out));  // open: CLEAR, PRESET
  not not_5 (not_5_out, N3);
  Pass_Transistor_2 pass_transistor_2_10 (
    .in_2(LOAD_out), .IN(not_5_out), .OUT(pass_transistor_2_10_out));  // open: CLEAR, PRESET
  or or_2 (or_2_out, nor_3_out, pass_transistor_2_10_out);
  nand nand_3 (nand_3_out, nor_3_out, pass_transistor_2_10_out);
  nand nand_4 (nand_4_out, or_2_out, nand_3_out);
  Pass_Transistor_2 pass_transistor_2_11 (
    .in_2(F2), .IN(nand_4_out), .OUT(pass_transistor_2_11_out));  // open: CLEAR, PRESET
  not not_6 (not_6_out, pass_transistor_2_11_out);
  Pass_Transistor_2 pass_transistor_2_12 (
    .in_2(F1), .IN(not_6_out), .OUT(pass_transistor_2_10_out));  // open: CLEAR, PRESET
  and and_3 (and_3_out, nand_3_out, pass_transistor_2_13_out);
  Pass_Transistor_2 pass_transistor_2_13 (
    .in_2(LOAD_out), .IN(N4), .OUT(pass_transistor_2_13_out));  // open: CLEAR, PRESET
  nor nor_5 (nor_5_out, and_3_out, nor_6_out);
  Pass_Transistor_2 pass_transistor_2_14 (
    .in_2(F2), .IN(nor_5_out), .OUT(pass_transistor_2_14_out));  // open: CLEAR, PRESET
  not not_7 (not_7_out, pass_transistor_2_14_out);
  nor nor_6 (nor_6_out, nand_3_out, pass_transistor_2_13_out);
  Pass_Transistor_2 pass_transistor_2_15 (
    .in_2(F1), .IN(not_7_out), .OUT(pass_transistor_2_13_out));  // open: CLEAR, PRESET
  not not_8 (not_8_out, N5);
  Pass_Transistor_2 pass_transistor_2_16 (
    .in_2(LOAD_out), .IN(not_8_out), .OUT(pass_transistor_2_16_out));  // open: CLEAR, PRESET
  or or_3 (or_3_out, nor_6_out, pass_transistor_2_16_out);
  nand nand_5 (nand_5_out, or_3_out, nand_6_out);
  Pass_Transistor_2 pass_transistor_2_17 (
    .in_2(F2), .IN(nand_5_out), .OUT(pass_transistor_2_17_out));  // open: CLEAR, PRESET
  not not_9 (not_9_out, pass_transistor_2_17_out);
  nand nand_6 (nand_6_out, nor_6_out, pass_transistor_2_16_out);
  Pass_Transistor_2 pass_transistor_2_18 (
    .in_2(F1), .IN(not_9_out), .OUT(pass_transistor_2_16_out));  // open: CLEAR, PRESET
  nor nor_7 (nor_7_out, pass_transistor_2_11_out, pass_transistor_2_17_out, pass_transistor_2_5_out, not_1_out, not_7_out, not_4_out);

  // Notes on the sheet:
  //   VERTICAL CELL COUNTER
endmodule

module Pass_Transistor (
  input  in_1,
  input  in_2,
  output out_3
);

  Register #(.width(1)) register_1 (.D(in_1), .en(1'b1), .Q(out_3), .clk(in_2));  // open: clr
endmodule

module Pass_Transistor_2 (
  input  IN,
  input  in_2,
  input  CLEAR,
  input  PRESET,
  output OUT
);

  D_Flip_Flop d_ff_1 (.clk(in_2), .D(IN), .Q(OUT), .preset(PRESET), .en(1'b1), .reset(CLEAR));  // open: Qn
endmodule
