// Logisim project vertical_counter_reset_logic_3.circ as structural Verilog: 2 circuits, main circuit main
module main (
  input  Y_311,
  input  Y_312,
  input  FORCE_VCNT_RESET,
  input  X___35,
  input  X___0
);

  wire F1_out, F2_out, nor_1_out, nor_2_out, nor_4_out, nor_5_out, not_1_out, not_2_out, not_3_out,
       not_4_out, not_5_out, not_6_out, pass_transistor_1_out_3, pass_transistor_2_out_3,
       pass_transistor_3_out_3, pass_transistor_4_out_3, pass_transistor_5_out_3, pass_transistor_6_out_3,
       pass_transistor_7_out_3, pass_transistor_8_out_3, transistor_1_out, transistor_2_out;

  Clock F1 (.out(F1_out));
  not F2 (F2_out, F1_out);
  Pass_Transistor pass_transistor_1 (.in_1(nor_1_out), .out_3(pass_transistor_1_out_3), .in_2(F1_out));
  not not_1 (not_1_out, pass_transistor_1_out_3);
  nor nor_1 (nor_1_out, transistor_1_out, not_2_out);
  Pass_Transistor pass_transistor_2 (.in_1(Y_311), .out_3(pass_transistor_2_out_3), .in_2(F1_out));
  // Probe on not_2_out
  Pass_Transistor pass_transistor_3 (.in_1(Y_312), .out_3(pass_transistor_3_out_3), .in_2(F1_out));
  nor nor_2 (nor_2_out, pass_transistor_2_out_3, pass_transistor_3_out_3, pass_transistor_5_out_3);
  Pass_Transistor pass_transistor_4 (.in_1(nor_2_out), .out_3(pass_transistor_4_out_3), .in_2(F2_out));
  not not_2 (not_2_out, pass_transistor_4_out_3);
  Pass_Transistor pass_transistor_5 (.in_1(FORCE_VCNT_RESET), .out_3(pass_transistor_5_out_3), .in_2(F1_out));
  Transistor #(.\type ("n")) transistor_1 (.in(1'b0), .out(transistor_1_out), .gate(pass_transistor_5_out_3));
  nor nor_3 (transistor_1_out, X___35, X___0);
  not not_3 (not_3_out, pass_transistor_6_out_3);
  Pass_Transistor pass_transistor_6 (.in_1(nor_4_out), .out_3(pass_transistor_6_out_3), .in_2(F1_out));
  nor nor_4 (nor_4_out, transistor_1_out, pass_transistor_4_out_3);
  not not_4 (not_4_out, not_3_out);
  not not_5 (not_5_out, nor_4_out);
  Pass_Transistor pass_transistor_7 (.in_1(not_5_out), .out_3(pass_transistor_7_out_3), .in_2(F2_out));
  Transistor #(.\type ("n")) transistor_2 (.in(F1_out), .out(transistor_2_out), .gate(pass_transistor_7_out_3));
  Transistor #(.\type ("n")) transistor_3 (.in(1'b0), .out(transistor_2_out), .gate(nor_4_out));
  // Probe on not_4_out
  // Probe on transistor_2_out
  not not_6 (not_6_out, X___0);
  Pass_Transistor pass_transistor_8 (.in_1(not_6_out), .out_3(pass_transistor_8_out_3), .in_2(F1_out));
  nor nor_5 (nor_5_out, pass_transistor_8_out_3, not_1_out);
  // Probe on nor_5_out
  // Probe on not_1_out

  // Notes on the sheet:
  //   WHEN NOT LAST LINE
  //   X != 0,35
endmodule

module Pass_Transistor (
  input  in_1,
  input  in_2,
  output out_3
);

  Register #(.width(1)) register_1 (.D(in_1), .en(1'b1), .Q(out_3), .clk(in_2));  // open: clr
endmodule
