// Logisim project video_matrix_counter_4.circ as structural Verilog: 4 circuits, main circuit main
module main (
  input  INCREMENT,
  input  LOAD_CNTR,
  input  STORE_CNTR,
  input  VSYNC
);

  wire and_1_out, and_2_out, F1_out, F2_out, nand_1_out, nand_2_out, nand_3_out, nand_4_out, nor_2_out,
       nor_3_out, nor_4_out, nor_5_out, not_1_out, not_2_out, not_3_out, not_4_out, not_5_out, not_6_out,
       not_7_out, not_8_out, not_9_out, not_10_out, not_11_out, not_12_out, or_1_out, or_2_out,
       pass_transistor_1_out_3, pass_transistor_2_out_3, pass_transistor_3_out_3, pass_transistor_6_out_3,
       pass_transistor_7_out_3, pass_transistor_8_out_3, pass_transistor_11_out_3, pass_transistor_12_out_3,
       pass_transistor_14_out_3, pass_transistor_16_out_3, pass_transistor_17_out_3,
       pass_transistor_18_out_3, transistor_1_out, transistor_2_out, transistor_3_out, transistor_4_out;

  // NOR_Gate nor_1 has open pins: in0=not_10_out, in1=not_4_out, in2=pass_transistor_14_out_3, in3=pass_transistor_3_out_3, out=open
  Pass_Transistor pass_transistor_1 (.in_1(not_1_out), .out_3(pass_transistor_1_out_3), .in_2(F1_out));
  Pass_Transistor pass_transistor_2 (.in_1(not_1_out), .out_3(pass_transistor_2_out_3), .in_2(STORE_CNTR));
  not not_1 (not_1_out, pass_transistor_3_out_3);
  Pass_Transistor pass_transistor_3 (.in_1(nand_1_out), .out_3(pass_transistor_3_out_3), .in_2(F2_out));
  nand nand_1 (nand_1_out, nand_2_out, or_1_out);
  nand nand_2 (nand_2_out, pass_transistor_1_out_3, nor_2_out);
  Pass_Transistor pass_transistor_4 (.in_1(not_3_out), .out_3(pass_transistor_2_out_3), .in_2(F2_out));
  not not_2 (not_2_out, pass_transistor_2_out_3);
  or or_1 (or_1_out, pass_transistor_1_out_3, nor_2_out);
  Pass_Transistor pass_transistor_5 (.in_1(not_3_out), .out_3(pass_transistor_1_out_3), .in_2(LOAD_CNTR));
  not not_3 (not_3_out, not_2_out);
  Transistor #(.\type ("n")) transistor_1 (.in(not_3_out), .out(transistor_1_out), .gate(VSYNC));
  Pass_Transistor pass_transistor_6 (.in_1(not_4_out), .out_3(pass_transistor_6_out_3), .in_2(STORE_CNTR));
  Pass_Transistor pass_transistor_7 (.in_1(not_4_out), .out_3(pass_transistor_7_out_3), .in_2(F1_out));
  nor nor_2 (nor_2_out, pass_transistor_7_out_3, nand_3_out);
  not not_4 (not_4_out, pass_transistor_8_out_3);
  Pass_Transistor pass_transistor_8 (.in_1(nor_3_out), .out_3(pass_transistor_8_out_3), .in_2(F2_out));
  nor nor_3 (nor_3_out, nor_2_out, and_1_out);
  Pass_Transistor pass_transistor_9 (.in_1(not_5_out), .out_3(pass_transistor_7_out_3), .in_2(LOAD_CNTR));
  Pass_Transistor pass_transistor_10 (.in_1(not_5_out), .out_3(pass_transistor_6_out_3), .in_2(F2_out));
  not not_5 (not_5_out, not_6_out);
  not not_6 (not_6_out, pass_transistor_6_out_3);
  and and_1 (and_1_out, pass_transistor_7_out_3, nand_3_out);
  Transistor #(.\type ("n")) transistor_2 (.in(not_6_out), .out(transistor_2_out), .gate(VSYNC));
  Pass_Transistor pass_transistor_11 (.in_1(not_8_out), .out_3(pass_transistor_11_out_3), .in_2(F1_out));
  Pass_Transistor pass_transistor_12 (.in_1(not_8_out), .out_3(pass_transistor_12_out_3), .in_2(STORE_CNTR));
  nand nand_3 (nand_3_out, pass_transistor_11_out_3, nor_5_out);
  Pass_Transistor pass_transistor_13 (.in_1(not_9_out), .out_3(pass_transistor_12_out_3), .in_2(F2_out));
  not not_7 (not_7_out, pass_transistor_12_out_3);
  not not_8 (not_8_out, pass_transistor_14_out_3);
  Pass_Transistor pass_transistor_14 (.in_1(nand_4_out), .out_3(pass_transistor_14_out_3), .in_2(F2_out));
  nand nand_4 (nand_4_out, nand_3_out, or_2_out);
  or or_2 (or_2_out, pass_transistor_11_out_3, nor_5_out);
  Pass_Transistor pass_transistor_15 (.in_1(not_9_out), .out_3(pass_transistor_11_out_3), .in_2(LOAD_CNTR));
  not not_9 (not_9_out, not_7_out);
  Transistor #(.\type ("n")) transistor_3 (.in(not_9_out), .out(transistor_3_out), .gate(VSYNC));
  Pass_Transistor pass_transistor_16 (.in_1(not_10_out), .out_3(pass_transistor_16_out_3), .in_2(F1_out));
  Pass_Transistor pass_transistor_17 (.in_1(not_10_out), .out_3(pass_transistor_17_out_3), .in_2(STORE_CNTR));
  not not_10 (not_10_out, pass_transistor_18_out_3);
  Pass_Transistor pass_transistor_18 (.in_1(nor_4_out), .out_3(pass_transistor_18_out_3), .in_2(F2_out));
  nor nor_4 (nor_4_out, nor_5_out, and_2_out);
  nor nor_5 (nor_5_out, pass_transistor_16_out_3, INCREMENT);
  Pass_Transistor pass_transistor_19 (.in_1(not_12_out), .out_3(pass_transistor_17_out_3), .in_2(F2_out));
  not not_11 (not_11_out, pass_transistor_17_out_3);
  and and_2 (and_2_out, pass_transistor_16_out_3, INCREMENT);
  Pass_Transistor pass_transistor_20 (.in_1(not_12_out), .out_3(pass_transistor_16_out_3), .in_2(LOAD_CNTR));
  not not_12 (not_12_out, not_11_out);
  Transistor #(.\type ("n")) transistor_4 (.in(not_11_out), .out(transistor_4_out), .gate(VSYNC));
  Clock F1 (.out(F1_out));
  not F2 (F2_out, F1_out);
  // also tied to GND on the sheet: {transistor_1_out, transistor_2_out, transistor_3_out, transistor_4_out}
endmodule

module Pass_Transistor (
  input  in_1,
  input  in_2,
  output out_3
);

  Register #(.width(1)) register_1 (.D(in_1), .en(1'b1), .Q(out_3), .clk(in_2));  // open: clr
endmodule

module Pass_Transistor_2 (
  input  IN,
  input  in_2,
  input  CLEAR,
  input  PRESET,
  output OUT
);

  D_Flip_Flop d_ff_1 (.clk(in_2), .D(IN), .Q(OUT), .preset(PRESET), .en(1'b1), .reset(CLEAR));  // open: Qn
endmodule

module Pass_Transistor_3 (
  input  IN,
  input  in_2,
  input  SET,
  output OUT
);

  wire controlled_buffer_1_out, controlled_buffer_2_out, not_1_out;

  not not_1 (not_1_out, SET);
  assign controlled_buffer_1_out = SET ? SET : 1'bz;  // Controlled_Buffer controlled_buffer_1
  assign controlled_buffer_2_out = not_1_out ? not_1_out : 1'bz;  // Controlled_Buffer controlled_buffer_2
  D_Flip_Flop d_ff_1 (
    .clk(in_2), .D(IN), .Q(OUT), .preset(controlled_buffer_1_out), .en(1'b1), .reset(controlled_buffer_2_out));  // open: Qn
endmodule
