// Logisim project video_matrix_counter_8.circ as structural Verilog: 4 circuits, main circuit main
module main (
  input  F1__INCREMENT,
  input  F2,
  input  INCR_ENABLE_prime,
  input  LOAD_CNTR,
  input  STORE_CNTR,
  input  VSYNC
);

  wire and_1_out, and_2_out, and_3_out, and_4_out, and_5_out, and_6_out, nand_1_out, nand_2_out, nand_3_out,
       nand_4_out, nand_5_out, nand_6_out, nand_7_out, nand_8_out, nand_9_out, nand_10_out, nand_11_out,
       nand_12_out, nor_1_out, nor_2_out, nor_3_out, nor_4_out, nor_5_out, nor_6_out, nor_7_out, nor_8_out,
       nor_9_out, nor_10_out, nor_11_out, nor_12_out, nor_13_out, nor_14_out, not_1_out, not_2_out,
       not_3_out, not_4_out, not_5_out, not_6_out, not_7_out, not_8_out, not_9_out, not_10_out, not_11_out,
       not_12_out, not_13_out, not_14_out, not_15_out, not_16_out, not_17_out, not_18_out, not_19_out,
       not_20_out, not_21_out, not_22_out, not_23_out, not_24_out, not_25_out, not_26_out, not_27_out,
       not_28_out, not_29_out, not_30_out, not_31_out, not_32_out, not_33_out, not_34_out, not_35_out,
       not_36_out, not_37_out, not_38_out, not_39_out, not_40_out, not_41_out, not_42_out, not_43_out,
       not_44_out, or_1_out, or_2_out, or_3_out, or_4_out, or_5_out, or_6_out, pass_transistor_1_out_3,
       pass_transistor_2_out_3, pass_transistor_3_out_3, pass_transistor_6_out_3, pass_transistor_7_out_3,
       pass_transistor_9_out_3, pass_transistor_11_out_3, pass_transistor_12_out_3, pass_transistor_13_out_3,
       pass_transistor_16_out_3, pass_transistor_17_out_3, pass_transistor_18_out_3,
       pass_transistor_21_out_3, pass_transistor_22_out_3, pass_transistor_23_out_3,
       pass_transistor_24_out_3, pass_transistor_27_out_3, pass_transistor_28_out_3,
       pass_transistor_30_out_3, pass_transistor_32_out_3, pass_transistor_33_out_3,
       pass_transistor_34_out_3, pass_transistor_37_out_3, pass_transistor_38_out_3,
       pass_transistor_39_out_3, pass_transistor_42_out_3, pass_transistor_43_out_3,
       pass_transistor_44_out_3, pass_transistor_46_out_3, pass_transistor_48_out_3,
       pass_transistor_49_out_3, pass_transistor_50_out_3, pass_transistor_53_out_3,
       pass_transistor_54_out_3, pass_transistor_55_out_3, pass_transistor_58_out_3,
       pass_transistor_59_out_3, pass_transistor_60_out_3, transistor_1_out, transistor_2_out,
       transistor_3_out, transistor_4_out, transistor_5_out, transistor_6_out, transistor_7_out,
       transistor_8_out, transistor_9_out, transistor_10_out, transistor_11_out, transistor_12_out,
       transistor_13_out;

  Pass_Transistor pass_transistor_1 (.in_1(not_2_out), .out_3(pass_transistor_1_out_3), .in_2(STORE_CNTR));
  Pass_Transistor pass_transistor_2 (.in_1(not_2_out), .out_3(pass_transistor_2_out_3), .in_2(F1__INCREMENT));
  nand nand_1 (nand_1_out, pass_transistor_2_out_3, nor_1_out);
  // Probe on not_1_out
  not not_1 (not_1_out, not_2_out);
  not not_2 (not_2_out, pass_transistor_3_out_3);
  Pass_Transistor pass_transistor_3 (.in_1(nand_2_out), .out_3(pass_transistor_3_out_3), .in_2(F2));
  nand nand_2 (nand_2_out, nand_1_out, or_1_out);
  Pass_Transistor pass_transistor_4 (.in_1(not_3_out), .out_3(pass_transistor_2_out_3), .in_2(LOAD_CNTR));
  Pass_Transistor pass_transistor_5 (.in_1(not_3_out), .out_3(pass_transistor_1_out_3), .in_2(F2));
  not not_3 (not_3_out, not_4_out);
  not not_4 (not_4_out, pass_transistor_1_out_3);
  or or_1 (or_1_out, pass_transistor_2_out_3, nor_1_out);
  Transistor #(.\type ("n")) transistor_1 (.in(not_3_out), .out(transistor_1_out), .gate(VSYNC));
  Pass_Transistor pass_transistor_6 (.in_1(not_6_out), .out_3(pass_transistor_6_out_3), .in_2(F1__INCREMENT));
  Pass_Transistor pass_transistor_7 (.in_1(not_6_out), .out_3(pass_transistor_7_out_3), .in_2(STORE_CNTR));
  nor nor_1 (nor_1_out, pass_transistor_6_out_3, nand_4_out);
  Pass_Transistor pass_transistor_8 (.in_1(not_7_out), .out_3(pass_transistor_7_out_3), .in_2(F2));
  not not_5 (not_5_out, pass_transistor_7_out_3);
  // Probe on not_6_out
  not not_6 (not_6_out, pass_transistor_9_out_3);
  Pass_Transistor pass_transistor_9 (.in_1(nor_2_out), .out_3(pass_transistor_9_out_3), .in_2(F2));
  nor nor_2 (nor_2_out, nor_1_out, and_1_out);
  and and_1 (and_1_out, pass_transistor_6_out_3, nand_4_out);
  Pass_Transistor pass_transistor_10 (.in_1(not_7_out), .out_3(pass_transistor_6_out_3), .in_2(LOAD_CNTR));
  not not_7 (not_7_out, not_5_out);
  Transistor #(.\type ("n")) transistor_2 (.in(not_5_out), .out(transistor_2_out), .gate(VSYNC));
  Pass_Transistor pass_transistor_11 (.in_1(not_9_out), .out_3(pass_transistor_11_out_3), .in_2(STORE_CNTR));
  Pass_Transistor pass_transistor_12 (.in_1(not_9_out), .out_3(pass_transistor_12_out_3), .in_2(F1__INCREMENT));
  // Probe on not_8_out
  not not_8 (not_8_out, not_9_out);
  not not_9 (not_9_out, pass_transistor_13_out_3);
  Pass_Transistor pass_transistor_13 (.in_1(nand_3_out), .out_3(pass_transistor_13_out_3), .in_2(F2));
  nand nand_3 (nand_3_out, nand_4_out, or_2_out);
  nand nand_4 (nand_4_out, pass_transistor_12_out_3, nor_3_out);
  Pass_Transistor pass_transistor_14 (.in_1(not_11_out), .out_3(pass_transistor_11_out_3), .in_2(F2));
  not not_10 (not_10_out, pass_transistor_11_out_3);
  or or_2 (or_2_out, pass_transistor_12_out_3, nor_3_out);
  Pass_Transistor pass_transistor_15 (.in_1(not_11_out), .out_3(pass_transistor_12_out_3), .in_2(LOAD_CNTR));
  not not_11 (not_11_out, not_10_out);
  Transistor #(.\type ("n")) transistor_3 (.in(not_11_out), .out(transistor_3_out), .gate(VSYNC));
  Pass_Transistor pass_transistor_16 (.in_1(not_12_out), .out_3(pass_transistor_16_out_3), .in_2(STORE_CNTR));
  Pass_Transistor pass_transistor_17 (.in_1(not_12_out), .out_3(pass_transistor_17_out_3), .in_2(F1__INCREMENT));
  nor nor_3 (nor_3_out, pass_transistor_17_out_3, pass_transistor_21_out_3);
  // Probe on not_12_out
  not not_12 (not_12_out, pass_transistor_18_out_3);
  Pass_Transistor pass_transistor_18 (.in_1(nor_4_out), .out_3(pass_transistor_18_out_3), .in_2(F2));
  nor nor_4 (nor_4_out, nor_3_out, and_2_out);
  and and_2 (and_2_out, pass_transistor_17_out_3, pass_transistor_21_out_3);
  Pass_Transistor pass_transistor_19 (.in_1(not_13_out), .out_3(pass_transistor_17_out_3), .in_2(LOAD_CNTR));
  Pass_Transistor pass_transistor_20 (.in_1(not_13_out), .out_3(pass_transistor_16_out_3), .in_2(F2));
  not not_13 (not_13_out, not_14_out);
  not not_14 (not_14_out, pass_transistor_16_out_3);
  not not_15 (not_15_out, nor_5_out);
  Pass_Transistor pass_transistor_21 (.in_1(not_15_out), .out_3(pass_transistor_21_out_3), .in_2(F1__INCREMENT));
  Transistor #(.\type ("n")) transistor_4 (.in(not_14_out), .out(transistor_4_out), .gate(VSYNC));
  nor nor_5 (nor_5_out, not_27_out, not_21_out, pass_transistor_34_out_3, pass_transistor_24_out_3, not_30_out);
  Pass_Transistor pass_transistor_22 (.in_1(not_17_out), .out_3(pass_transistor_22_out_3), .in_2(STORE_CNTR));
  Pass_Transistor pass_transistor_23 (.in_1(not_17_out), .out_3(pass_transistor_23_out_3), .in_2(F1__INCREMENT));
  nand nand_5 (nand_5_out, pass_transistor_23_out_3, nor_6_out);
  // Probe on not_16_out
  not not_16 (not_16_out, not_17_out);
  not not_17 (not_17_out, pass_transistor_24_out_3);
  Pass_Transistor pass_transistor_24 (.in_1(nand_6_out), .out_3(pass_transistor_24_out_3), .in_2(F2));
  nand nand_6 (nand_6_out, nand_5_out, or_3_out);
  Pass_Transistor pass_transistor_25 (.in_1(not_18_out), .out_3(pass_transistor_23_out_3), .in_2(LOAD_CNTR));
  Pass_Transistor pass_transistor_26 (.in_1(not_18_out), .out_3(pass_transistor_22_out_3), .in_2(F2));
  not not_18 (not_18_out, not_19_out);
  not not_19 (not_19_out, pass_transistor_22_out_3);
  or or_3 (or_3_out, pass_transistor_23_out_3, nor_6_out);
  Transistor #(.\type ("n")) transistor_5 (.in(not_18_out), .out(transistor_5_out), .gate(VSYNC));
  Pass_Transistor pass_transistor_27 (.in_1(not_21_out), .out_3(pass_transistor_27_out_3), .in_2(F1__INCREMENT));
  Pass_Transistor pass_transistor_28 (.in_1(not_21_out), .out_3(pass_transistor_28_out_3), .in_2(STORE_CNTR));
  nor nor_6 (nor_6_out, pass_transistor_27_out_3, nand_8_out);
  Pass_Transistor pass_transistor_29 (.in_1(not_22_out), .out_3(pass_transistor_28_out_3), .in_2(F2));
  not not_20 (not_20_out, pass_transistor_28_out_3);
  // Probe on not_21_out
  not not_21 (not_21_out, pass_transistor_30_out_3);
  Pass_Transistor pass_transistor_30 (.in_1(nor_7_out), .out_3(pass_transistor_30_out_3), .in_2(F2));
  nor nor_7 (nor_7_out, nor_6_out, and_3_out);
  and and_3 (and_3_out, pass_transistor_27_out_3, nand_8_out);
  Pass_Transistor pass_transistor_31 (.in_1(not_22_out), .out_3(pass_transistor_27_out_3), .in_2(LOAD_CNTR));
  not not_22 (not_22_out, not_20_out);
  Transistor #(.\type ("n")) transistor_6 (.in(not_20_out), .out(transistor_6_out), .gate(VSYNC));
  Pass_Transistor pass_transistor_32 (.in_1(not_24_out), .out_3(pass_transistor_32_out_3), .in_2(STORE_CNTR));
  Pass_Transistor pass_transistor_33 (.in_1(not_24_out), .out_3(pass_transistor_33_out_3), .in_2(F1__INCREMENT));
  // Probe on not_23_out
  not not_23 (not_23_out, not_24_out);
  not not_24 (not_24_out, pass_transistor_34_out_3);
  Pass_Transistor pass_transistor_34 (.in_1(nand_7_out), .out_3(pass_transistor_34_out_3), .in_2(F2));
  nand nand_7 (nand_7_out, nand_8_out, or_4_out);
  nand nand_8 (nand_8_out, pass_transistor_33_out_3, nor_8_out);
  Pass_Transistor pass_transistor_35 (.in_1(not_26_out), .out_3(pass_transistor_32_out_3), .in_2(F2));
  not not_25 (not_25_out, pass_transistor_32_out_3);
  or or_4 (or_4_out, pass_transistor_33_out_3, nor_8_out);
  Pass_Transistor pass_transistor_36 (.in_1(not_26_out), .out_3(pass_transistor_33_out_3), .in_2(LOAD_CNTR));
  not not_26 (not_26_out, not_25_out);
  Transistor #(.\type ("n")) transistor_7 (.in(not_26_out), .out(transistor_7_out), .gate(VSYNC));
  Pass_Transistor pass_transistor_37 (.in_1(not_27_out), .out_3(pass_transistor_37_out_3), .in_2(STORE_CNTR));
  Pass_Transistor pass_transistor_38 (.in_1(not_27_out), .out_3(pass_transistor_38_out_3), .in_2(F1__INCREMENT));
  nor nor_8 (nor_8_out, pass_transistor_38_out_3, pass_transistor_42_out_3);
  // Probe on not_27_out
  not not_27 (not_27_out, pass_transistor_39_out_3);
  Pass_Transistor pass_transistor_39 (.in_1(nor_9_out), .out_3(pass_transistor_39_out_3), .in_2(F2));
  nor nor_9 (nor_9_out, nor_8_out, and_4_out);
  and and_4 (and_4_out, pass_transistor_38_out_3, pass_transistor_42_out_3);
  Pass_Transistor pass_transistor_40 (.in_1(not_28_out), .out_3(pass_transistor_38_out_3), .in_2(LOAD_CNTR));
  Pass_Transistor pass_transistor_41 (.in_1(not_28_out), .out_3(pass_transistor_37_out_3), .in_2(F2));
  not not_28 (not_28_out, not_29_out);
  not not_29 (not_29_out, pass_transistor_37_out_3);
  not not_30 (not_30_out, nor_10_out);
  Pass_Transistor pass_transistor_42 (.in_1(not_30_out), .out_3(pass_transistor_42_out_3), .in_2(F1__INCREMENT));
  Transistor #(.\type ("n")) transistor_8 (.in(not_29_out), .out(transistor_8_out), .gate(VSYNC));
  nor nor_10 (nor_10_out, not_42_out, not_35_out, pass_transistor_55_out_3, pass_transistor_46_out_3);
  Transistor #(.\type ("n"), .gate("br")) transistor_9 (
    .in(nor_10_out), .out(transistor_9_out), .gate(INCR_ENABLE_prime));
  Pass_Transistor pass_transistor_43 (.in_1(not_33_out), .out_3(pass_transistor_43_out_3), .in_2(F1__INCREMENT));
  Pass_Transistor pass_transistor_44 (.in_1(not_33_out), .out_3(pass_transistor_44_out_3), .in_2(STORE_CNTR));
  nand nand_9 (nand_9_out, pass_transistor_43_out_3, nor_12_out);
  Pass_Transistor pass_transistor_45 (.in_1(not_34_out), .out_3(pass_transistor_44_out_3), .in_2(F2));
  not not_31 (not_31_out, pass_transistor_44_out_3);
  // Probe on not_32_out
  not not_32 (not_32_out, not_33_out);
  not not_33 (not_33_out, pass_transistor_46_out_3);
  Pass_Transistor pass_transistor_46 (.in_1(nand_10_out), .out_3(pass_transistor_46_out_3), .in_2(F2));
  nand nand_10 (nand_10_out, nand_9_out, or_5_out);
  or or_5 (or_5_out, pass_transistor_43_out_3, nor_12_out);
  Pass_Transistor pass_transistor_47 (.in_1(not_34_out), .out_3(pass_transistor_43_out_3), .in_2(LOAD_CNTR));
  not not_34 (not_34_out, not_31_out);
  Transistor #(.\type ("n")) transistor_10 (.in(not_34_out), .out(transistor_10_out), .gate(VSYNC));
  Pass_Transistor pass_transistor_48 (.in_1(not_35_out), .out_3(pass_transistor_48_out_3), .in_2(STORE_CNTR));
  Pass_Transistor pass_transistor_49 (.in_1(not_35_out), .out_3(pass_transistor_49_out_3), .in_2(F1__INCREMENT));
  // Probe on not_35_out
  not not_35 (not_35_out, pass_transistor_50_out_3);
  Pass_Transistor pass_transistor_50 (.in_1(nor_11_out), .out_3(pass_transistor_50_out_3), .in_2(F2));
  nor nor_11 (nor_11_out, nor_12_out, and_5_out);
  nor nor_12 (nor_12_out, pass_transistor_49_out_3, nand_11_out);
  Pass_Transistor pass_transistor_51 (.in_1(not_37_out), .out_3(pass_transistor_48_out_3), .in_2(F2));
  not not_36 (not_36_out, pass_transistor_48_out_3);
  and and_5 (and_5_out, pass_transistor_49_out_3, nand_11_out);
  Pass_Transistor pass_transistor_52 (.in_1(not_37_out), .out_3(pass_transistor_49_out_3), .in_2(LOAD_CNTR));
  not not_37 (not_37_out, not_36_out);
  Transistor #(.\type ("n")) transistor_11 (.in(not_36_out), .out(transistor_11_out), .gate(VSYNC));
  Pass_Transistor pass_transistor_53 (.in_1(not_39_out), .out_3(pass_transistor_53_out_3), .in_2(STORE_CNTR));
  Pass_Transistor pass_transistor_54 (.in_1(not_39_out), .out_3(pass_transistor_54_out_3), .in_2(F1__INCREMENT));
  nand nand_11 (nand_11_out, pass_transistor_54_out_3, nor_14_out);
  // Probe on not_38_out
  not not_38 (not_38_out, not_39_out);
  not not_39 (not_39_out, pass_transistor_55_out_3);
  Pass_Transistor pass_transistor_55 (.in_1(nand_12_out), .out_3(pass_transistor_55_out_3), .in_2(F2));
  nand nand_12 (nand_12_out, nand_11_out, or_6_out);
  or or_6 (or_6_out, pass_transistor_54_out_3, nor_14_out);
  Pass_Transistor pass_transistor_56 (.in_1(not_40_out), .out_3(pass_transistor_54_out_3), .in_2(LOAD_CNTR));
  Pass_Transistor pass_transistor_57 (.in_1(not_40_out), .out_3(pass_transistor_53_out_3), .in_2(F2));
  not not_40 (not_40_out, not_41_out);
  not not_41 (not_41_out, pass_transistor_53_out_3);
  Transistor #(.\type ("n")) transistor_12 (.in(not_40_out), .out(transistor_12_out), .gate(VSYNC));
  Pass_Transistor pass_transistor_58 (.in_1(not_42_out), .out_3(pass_transistor_58_out_3), .in_2(F1__INCREMENT));
  Pass_Transistor pass_transistor_59 (.in_1(not_42_out), .out_3(pass_transistor_59_out_3), .in_2(STORE_CNTR));
  // Probe on not_42_out
  not not_42 (not_42_out, pass_transistor_60_out_3);
  Pass_Transistor pass_transistor_60 (.in_1(nor_13_out), .out_3(pass_transistor_60_out_3), .in_2(F2));
  nor nor_13 (nor_13_out, nor_14_out, and_6_out);
  nor nor_14 (nor_14_out, pass_transistor_58_out_3, INCR_ENABLE_prime);
  Pass_Transistor pass_transistor_61 (.in_1(not_44_out), .out_3(pass_transistor_59_out_3), .in_2(F2));
  not not_43 (not_43_out, pass_transistor_59_out_3);
  and and_6 (and_6_out, pass_transistor_58_out_3, INCR_ENABLE_prime);
  Pass_Transistor pass_transistor_62 (.in_1(not_44_out), .out_3(pass_transistor_58_out_3), .in_2(LOAD_CNTR));
  not not_44 (not_44_out, not_43_out);
  Transistor #(.\type ("n")) transistor_13 (.in(not_43_out), .out(transistor_13_out), .gate(VSYNC));
  // also tied to GND on the sheet: {transistor_1_out, transistor_2_out, transistor_3_out, transistor_4_out, transistor_5_out, transistor_6_out, transistor_7_out, transistor_8_out, transistor_9_out, transistor_10_out, transistor_11_out, transistor_12_out, transistor_13_out}
endmodule

module Pass_Transistor (
  input  in_1,
  input  in_2,
  output out_3
);

  Register #(.width(1)) register_1 (.D(in_1), .en(1'b1), .Q(out_3), .clk(in_2));  // open: clr
endmodule

module Pass_Transistor_2 (
  input  IN,
  input  in_2,
  input  CLEAR,
  input  PRESET,
  output OUT
);

  D_Flip_Flop d_ff_1 (.clk(in_2), .D(IN), .Q(OUT), .preset(PRESET), .en(1'b1), .reset(CLEAR));  // open: Qn
endmodule

module Pass_Transistor_3 (
  input  IN,
  input  in_2,
  input  SET,
  output OUT
);

  wire controlled_buffer_1_out, controlled_buffer_2_out, not_1_out;

  not not_1 (not_1_out, SET);
  assign controlled_buffer_1_out = SET ? SET : 1'bz;  // Controlled_Buffer controlled_buffer_1
  assign controlled_buffer_2_out = not_1_out ? not_1_out : 1'bz;  // Controlled_Buffer controlled_buffer_2
  D_Flip_Flop d_ff_1 (
    .clk(in_2), .D(IN), .Q(OUT), .preset(controlled_buffer_1_out), .en(1'b1), .reset(controlled_buffer_2_out));  // open: Qn
endmodule
