// Logisim project video_matrix_counter_cell.circ as structural Verilog: 4 circuits, main circuit main
module main (
  input  INCREMENT,
  input  VSYNC
);

  wire and_1_out, F1_out, F2_out, nor_1_out, nor_2_out, not_1_out, not_2_out, not_3_out,
       pass_transistor_1_out_3, pass_transistor_2_out_3, pass_transistor_3_out_3, transistor_1_out;

  Pass_Transistor pass_transistor_1 (.in_1(not_1_out), .out_3(pass_transistor_1_out_3), .in_2(F1_out));
  Pass_Transistor pass_transistor_2 (.in_1(not_1_out), .out_3(pass_transistor_2_out_3), .in_2(F1_out));
  not not_1 (not_1_out, pass_transistor_3_out_3);
  Pass_Transistor pass_transistor_3 (.in_1(nor_1_out), .out_3(pass_transistor_3_out_3), .in_2(F2_out));
  nor nor_1 (nor_1_out, and_1_out, nor_2_out);
  and and_1 (and_1_out, pass_transistor_1_out_3, INCREMENT);
  Pass_Transistor pass_transistor_4 (.in_1(not_2_out), .out_3(pass_transistor_2_out_3), .in_2(F2_out));
  nor nor_2 (nor_2_out, pass_transistor_1_out_3, INCREMENT);
  Pass_Transistor pass_transistor_5 (.in_1(not_2_out), .out_3(pass_transistor_1_out_3), .in_2(F1_out));
  not not_2 (not_2_out, not_3_out);
  not not_3 (not_3_out, pass_transistor_2_out_3);
  Transistor #(.\type ("n")) transistor_1 (.in(pass_transistor_2_out_3), .out(transistor_1_out), .gate(VSYNC));
  not F2 (F2_out, F1_out);
  Clock F1 (.out(F1_out));
  // also tied to GND on the sheet: transistor_1_out

  // Notes on the sheet:
  //   CDC LAST VALUE F1
  //   LOAD LATCH
  //   LOAD COUNTER
  //   D LATCH
  //   CLEAR LATCH
  //   MID F1
endmodule

module Pass_Transistor (
  input  in_1,
  input  in_2,
  output out_3
);

  Register #(.width(1)) register_1 (.D(in_1), .en(1'b1), .Q(out_3), .clk(in_2));  // open: clr
endmodule

module Pass_Transistor_2 (
  input  IN,
  input  in_2,
  input  CLEAR,
  input  PRESET,
  output OUT
);

  D_Flip_Flop d_ff_1 (.clk(in_2), .D(IN), .Q(OUT), .preset(PRESET), .en(1'b1), .reset(CLEAR));  // open: Qn
endmodule

module Pass_Transistor_3 (
  input  IN,
  input  in_2,
  input  SET,
  output OUT
);

  wire controlled_buffer_1_out, controlled_buffer_2_out, not_1_out;

  not not_1 (not_1_out, SET);
  assign controlled_buffer_1_out = SET ? SET : 1'bz;  // Controlled_Buffer controlled_buffer_1
  assign controlled_buffer_2_out = not_1_out ? not_1_out : 1'bz;  // Controlled_Buffer controlled_buffer_2
  D_Flip_Flop d_ff_1 (
    .clk(in_2), .D(IN), .Q(OUT), .preset(controlled_buffer_1_out), .en(1'b1), .reset(controlled_buffer_2_out));  // open: Qn
endmodule
