// Logisim project video_matrix_counter_f1_signals.circ as structural Verilog: 4 circuits, main circuit main
module main (
  input  START_NEW_LINE_prime,
  input  CDC_LAST_VALUE_prime
);

  wire F1_out, F2_out, not_1_out, not_2_out, not_3_out, pass_transistor_1_out_3, pass_transistor_2_out_3,
       pass_transistor_3_out_3, pass_transistor_4_out_3, pass_transistor_5_out_3, transistor_1_out,
       transistor_4_out, transistor_7_out;

  // Probe on transistor_1_out
  Transistor #(.\type ("n"), .gate("br")) transistor_1 (
    .in(F1_out), .out(transistor_1_out), .gate(pass_transistor_1_out_3));
  Transistor #(.\type ("n")) transistor_2 (.in(1'b0), .out(transistor_1_out), .gate(CDC_LAST_VALUE_prime));
  Pass_Transistor pass_transistor_1 (.in_1(not_1_out), .out_3(pass_transistor_1_out_3), .in_2(F2_out));
  not not_1 (not_1_out, CDC_LAST_VALUE_prime);
  Transistor #(.\type ("n"), .gate("br")) transistor_3 (.in(1'b0), .out(transistor_1_out), .gate(F2_out));
  Transistor #(.\type ("n")) transistor_4 (.in(1'b0), .out(transistor_4_out), .gate(F2_out));
  Pass_Transistor pass_transistor_2 (.in_1(not_2_out), .out_3(pass_transistor_2_out_3), .in_2(F2_out));
  Transistor #(.\type ("n"), .gate("br")) transistor_5 (
    .in(F1_out), .out(transistor_4_out), .gate(pass_transistor_2_out_3));
  Transistor #(.\type ("n"), .gate("br")) transistor_6 (
    .in(1'b0), .out(transistor_4_out), .gate(pass_transistor_3_out_3));
  // Probe on transistor_4_out
  not not_2 (not_2_out, START_NEW_LINE_prime);
  Pass_Transistor pass_transistor_3 (.in_1(START_NEW_LINE_prime), .out_3(pass_transistor_3_out_3), .in_2(F2_out));
  // Probe on transistor_7_out
  Transistor #(.\type ("n"), .gate("br")) transistor_7 (
    .in(F1_out), .out(transistor_7_out), .gate(pass_transistor_4_out_3));
  Pass_Transistor pass_transistor_4 (.in_1(START_NEW_LINE_prime), .out_3(pass_transistor_4_out_3), .in_2(F2_out));
  Transistor #(.\type ("n")) transistor_8 (.in(1'b0), .out(transistor_7_out), .gate(F2_out));
  Transistor #(.\type ("n"), .gate("br")) transistor_9 (.in(1'b0), .out(transistor_7_out), .gate(not_3_out));
  not not_3 (not_3_out, pass_transistor_5_out_3);
  not F2 (F2_out, F1_out);
  Pass_Transistor pass_transistor_5 (.in_1(START_NEW_LINE_prime), .out_3(pass_transistor_5_out_3), .in_2(F2_out));
  Clock F1 (.out(F1_out));
endmodule

module Pass_Transistor (
  input  in_1,
  input  in_2,
  output out_3
);

  Register #(.width(1)) register_1 (.D(in_1), .en(1'b1), .Q(out_3), .clk(in_2));  // open: clr
endmodule

module Pass_Transistor_2 (
  input  IN,
  input  in_2,
  input  CLEAR,
  input  PRESET,
  output OUT
);

  D_Flip_Flop d_ff_1 (.clk(in_2), .D(IN), .Q(OUT), .preset(PRESET), .en(1'b1), .reset(CLEAR));  // open: Qn
endmodule

module Pass_Transistor_3 (
  input  IN,
  input  in_2,
  input  SET,
  output OUT
);

  wire controlled_buffer_1_out, controlled_buffer_2_out, not_1_out;

  not not_1 (not_1_out, SET);
  assign controlled_buffer_1_out = SET ? SET : 1'bz;  // Controlled_Buffer controlled_buffer_1
  assign controlled_buffer_2_out = not_1_out ? not_1_out : 1'bz;  // Controlled_Buffer controlled_buffer_2
  D_Flip_Flop d_ff_1 (
    .clk(in_2), .D(IN), .Q(OUT), .preset(controlled_buffer_1_out), .en(1'b1), .reset(controlled_buffer_2_out));  // open: Qn
endmodule
