// Logisim project vsync_pulses_latch.circ as structural Verilog: 1 circuit, main circuit main
module main (
  input  _2,
  input  _38,
  input  _6,
  input  _41
);

  wire nor_1_out, nor_2_out;

  nor nor_1 (nor_1_out, _2, _38, nor_2_out);
  nor nor_2 (nor_2_out, nor_1_out, _6, _41);
  // Probe on nor_1_out
endmodule
