// Logisim project within_video_matrix_logic_6.circ as structural Verilog: 2 circuits, main circuit main
module main (
  input  HORIZ_CELL_CNTR_LAST_VALUE,
  input  START_OF_NEW_LINE_prime,
  input  LAST_LINE,
  input  VERT_CELL_CNTR_LAST_VALUE,
  input  SX_COMPARE,
  input  SY_COMPARE
);

  wire and_1_out, F1_out, F2_out, nor_1_out, nor_2_out, nor_3_out, nor_4_out, nor_5_out, nor_6_out,
       nor_7_out, not_1_out, not_2_out, not_3_out, not_4_out, not_5_out, not_6_out, not_7_out, not_8_out,
       not_9_out, not_10_out, not_11_out, pass_transistor_1_out_3, pass_transistor_2_out_3,
       pass_transistor_3_out_3, pass_transistor_4_out_3, pass_transistor_5_out_3, pass_transistor_6_out_3,
       pass_transistor_7_out_3, pass_transistor_8_out_3, pass_transistor_9_out_3;

  Clock F2 (.out(F2_out));
  Clock F1 (.out(F1_out));
  Pass_Transistor pass_transistor_1 (.in_1(SX_COMPARE), .out_3(pass_transistor_1_out_3), .in_2(F1_out));
  not not_1 (not_1_out, pass_transistor_1_out_3);
  not not_2 (not_2_out, pass_transistor_2_out_3);
  Pass_Transistor pass_transistor_2 (.in_1(SY_COMPARE), .out_3(pass_transistor_2_out_3), .in_2(F1_out));
  not not_3 (not_3_out, pass_transistor_3_out_3);
  Pass_Transistor pass_transistor_3 (.in_1(not_1_out), .out_3(pass_transistor_3_out_3), .in_2(F2_out));
  Pass_Transistor pass_transistor_4 (.in_1(not_2_out), .out_3(pass_transistor_4_out_3), .in_2(F2_out));
  not not_4 (not_4_out, pass_transistor_4_out_3);
  nor nor_1 (nor_1_out, LAST_LINE, VERT_CELL_CNTR_LAST_VALUE, nor_2_out);
  nor nor_2 (nor_2_out, nor_1_out, not_4_out);
  // Probe on nor_5_out
  Pass_Transistor pass_transistor_5 (.in_1(nor_4_out), .out_3(pass_transistor_5_out_3), .in_2(F1_out));
  not not_5 (not_5_out, START_OF_NEW_LINE_prime);
  and and_1 (and_1_out, not_3_out, nor_1_out);
  Pass_Transistor pass_transistor_6 (.in_1(not_6_out), .out_3(pass_transistor_6_out_3), .in_2(F2_out));
  not not_6 (not_6_out, pass_transistor_5_out_3);
  nor nor_3 (nor_3_out, and_1_out, nor_4_out);
  not not_7 (not_7_out, pass_transistor_6_out_3);
  Pass_Transistor pass_transistor_7 (.in_1(not_7_out), .out_3(pass_transistor_7_out_3), .in_2(F1_out));
  not not_8 (not_8_out, pass_transistor_7_out_3);
  // Probe on pass_transistor_7_out_3
  nor nor_4 (nor_4_out, HORIZ_CELL_CNTR_LAST_VALUE, not_5_out, nor_3_out);
  Pass_Transistor pass_transistor_8 (.in_1(not_8_out), .out_3(pass_transistor_8_out_3), .in_2(F2_out));
  Pass_Transistor pass_transistor_9 (.in_1(not_9_out), .out_3(pass_transistor_9_out_3), .in_2(F1_out));
  not not_9 (not_9_out, pass_transistor_8_out_3);
  not not_10 (not_10_out, pass_transistor_9_out_3);
  nor nor_5 (nor_5_out, nor_4_out, nor_6_out);
  nor nor_6 (nor_6_out, nor_5_out, nor_2_out);
  nor nor_7 (nor_7_out, not_6_out, not_10_out);
  not not_11 (not_11_out, nor_7_out);
  // Probe on not_11_out

  // Notes on the sheet:
  //   WITHIN THE MATRIX
endmodule

module Pass_Transistor (
  input  in_1,
  input  in_2,
  output out_3
);

  Register #(.width(1)) register_1 (.D(in_1), .en(1'b1), .Q(out_3), .clk(in_2));  // open: clr
endmodule
