// Logisim project 6561_full_logisim_2.circ as structural Verilog: 14 circuits, main circuit main
module main (
  input  inv_reset
);

  wire clk_out, mos_6561_1_clk_out_1, mos_6561_1_clk_out_2;

  Clock #(.highDuration(2), .lowDuration(2)) clk (.out(clk_out));
  Clock sysclk ();  // open: out
  LED led_1 (.in(mos_6561_1_clk_out_2));
  MOS_6561 mos_6561_1 (
    .clk_in_1(clk_out), .inv_reset(inv_reset), .clk_out_2(mos_6561_1_clk_out_2),
    .clk_out_1(mos_6561_1_clk_out_1));
  LED led_2 (.in(mos_6561_1_clk_out_1));
endmodule

module Pass_Transistor (
  input  in_1,
  input  in_2,
  output out_3
);

  Register #(.width(1)) register_1 (.D(in_1), .en(1'b1), .clk(in_2), .Q(out_3));  // open: clr
endmodule

module Pass_Transistor_2 (
  input  IN,
  input  CLEAR,
  input  in_3,
  input  PRESET,
  output OUT
);

  D_Flip_Flop d_ff_1 (.D(IN), .clk(in_3), .Q(OUT), .preset(PRESET), .reset(CLEAR));  // open: Qn
endmodule

module Pass_Transistor_3 (
  input  IN,
  input  in_2,
  input  SET,
  output OUT
);

  wire controlled_buffer_1_out, controlled_buffer_2_out, not_1_out;

  not not_1 (not_1_out, SET);
  assign controlled_buffer_1_out = SET ? SET : 1'bz;  // Controlled_Buffer controlled_buffer_1
  assign controlled_buffer_2_out = not_1_out ? not_1_out : 1'bz;  // Controlled_Buffer controlled_buffer_2
  D_Flip_Flop d_ff_1 (
    .clk(in_2), .D(IN), .Q(OUT), .preset(controlled_buffer_1_out), .reset(controlled_buffer_2_out));  // open: Qn
endmodule

module Clock_Generator (
  input  clk_in_1,
  input  inv_reset,
  output mem_clk_1,
  output mem_clk_2,
  output in1,
  output in2,
  output f2,
  output f1
);

  wire nand_1_out, nand_2_out, nor_1_out, nor_2_out, nor_3_out, nor_4_out, nor_5_out, nor_6_out, nor_7_out,
       nor_8_out, nor_9_out, not_1_out, not_3_out, not_4_out, not_6_out, not_7_out, not_10_out, not_11_out,
       not_12_out, not_13_out, not_14_out, not_15_out, not_16_out, not_17_out, not_18_out, not_19_out,
       or_1_out, pass_transistor_1_out_3, pass_transistor_2_out_3, pass_transistor_3_out_3,
       pass_transistor_4_out_3, pass_transistor_5_out_3, pass_transistor_6_out_3, transistor_1_out;

  nor nor_1 (nor_1_out, nor_4_out, f1);
  not not_1 (not_1_out, nor_1_out);
  not not_2 (f2, not_1_out);
  not not_3 (not_3_out, nor_4_out);
  nor nor_2 (nor_2_out, f2, not_3_out);
  not not_4 (not_4_out, nor_2_out);
  not not_5 (f1, not_4_out);
  not not_6 (not_6_out, pass_transistor_1_out_3);
  Pass_Transistor pass_transistor_1 (.in_1(not_7_out), .out_3(pass_transistor_1_out_3), .in_2(not_16_out));
  not not_7 (not_7_out, inv_reset);
  Pass_Transistor pass_transistor_2 (.in_1(not_6_out), .out_3(pass_transistor_2_out_3), .in_2(not_15_out));
  not not_8 (mem_clk_1, not_10_out);
  not not_9 (mem_clk_2, not_11_out);
  nor nor_3 (nor_3_out, pass_transistor_2_out_3, inv_reset);
  not not_10 (not_10_out, nor_5_out);
  not not_11 (not_11_out, nor_6_out);
  nor nor_4 (nor_4_out, nor_3_out, pass_transistor_4_out_3);
  Pass_Transistor pass_transistor_3 (.in_1(nor_4_out), .out_3(pass_transistor_3_out_3), .in_2(not_15_out));
  nor nor_5 (nor_5_out, not_13_out, mem_clk_2);
  nor nor_6 (nor_6_out, mem_clk_1, not_12_out);
  Pass_Transistor pass_transistor_4 (.in_1(nand_1_out), .out_3(pass_transistor_4_out_3), .in_2(not_16_out));
  nand nand_1 (nand_1_out, nand_2_out, or_1_out);
  nand nand_2 (nand_2_out, pass_transistor_3_out_3, not_14_out);
  not not_12 (not_12_out, not_13_out);
  or or_1 (or_1_out, pass_transistor_3_out_3, not_14_out);
  Pass_Transistor pass_transistor_5 (.in_1(nor_7_out), .out_3(pass_transistor_5_out_3), .in_2(not_16_out));
  nor nor_7 (nor_7_out, nor_3_out, not_14_out);
  not not_13 (not_13_out, pass_transistor_5_out_3);
  not not_14 (not_14_out, pass_transistor_6_out_3);
  Pass_Transistor pass_transistor_6 (.in_1(not_13_out), .out_3(pass_transistor_6_out_3), .in_2(not_15_out));
  not not_15 (not_15_out, not_17_out);
  not not_16 (not_16_out, not_18_out);
  nor nor_8 (nor_8_out, not_19_out, not_16_out);
  not not_17 (not_17_out, nor_8_out);
  nor nor_9 (nor_9_out, not_15_out, clk_in_1);
  not not_18 (not_18_out, nor_9_out);
  not not_19 (not_19_out, clk_in_1);
  Transistor #(.\type ("n")) transistor_1 (.in(1'b1), .out(transistor_1_out), .gate(not_15_out));
  Transistor #(.\type ("n")) transistor_2 (.in(1'b0), .out(transistor_1_out), .gate(not_16_out));
  not not_20 (in2, transistor_1_out);

  assign in1 = clk_in_1;
endmodule

module Vertical_Counter (
  input  f2,
  input  vc_reset,
  input  vc_enable,
  input  vc_inc,
  input  inv_half_ena,
  output hl,
  output inv_hl,
  output [8:0] vc,
  output [8:0] inv_vc
);

  not not_1 (inv_hl, inv_half_ena);
  Counter #(.width(9), .max('h1ff)) counter_1 (
    .clr(vc_reset), .load(1'b0), .up(1'b1), .count(vc_enable), .clk(vc_inc), .Q(vc));  // open: D, carry
  assign inv_vc = ~vc;  // NOT_Gate not_2, 9 bits wide

  assign hl = inv_half_ena;
endmodule

module Horizontal_Counter (
  input  f2,
  input  hc_inc,
  input  hc_reset,
  output [7:0] hc,
  output [7:0] inv_hc
);

  wire and_1_out, and_2_out, and_3_out, and_4_out, nand_1_out, nand_2_out, nand_3_out, nand_4_out,
       nand_5_out, nand_6_out, nand_7_out, nand_8_out, nor_1_out, nor_2_out, nor_3_out, nor_4_out, nor_5_out,
       nor_6_out, nor_7_out, nor_8_out, nor_9_out, not_9_out, or_1_out, or_2_out, or_3_out, or_4_out,
       pass_transistor_1_out_3, pass_transistor_2_1_out, pass_transistor_2_2_out, pass_transistor_2_3_out,
       pass_transistor_2_4_out, pass_transistor_2_5_out, pass_transistor_2_6_out, pass_transistor_2_7_out,
       pass_transistor_2_8_out, pass_transistor_2_9_out, pass_transistor_2_out_3, pass_transistor_3_out_3,
       pass_transistor_4_out_3, pass_transistor_5_out_3, pass_transistor_6_out_3, pass_transistor_7_out_3,
       pass_transistor_8_out_3;

  and and_1 (and_1_out, hc_reset, pass_transistor_2_1_out);
  not not_1 (hc[0], inv_hc[0]);
  not not_2 (inv_hc[0], pass_transistor_1_out_3);
  Pass_Transistor pass_transistor_1 (.in_1(nor_1_out), .out_3(pass_transistor_1_out_3), .in_2(f2));
  nor nor_1 (nor_1_out, and_1_out, nor_2_out);
  nor nor_2 (nor_2_out, hc_reset, pass_transistor_2_1_out);
  Pass_Transistor_2 pass_transistor_2_1 (
    .in_3(hc_inc), .PRESET(hc_reset), .IN(inv_hc[0]), .OUT(pass_transistor_2_1_out));  // open: CLEAR
  not not_3 (inv_hc[1], hc[1]);
  or or_1 (or_1_out, nor_2_out, pass_transistor_2_2_out);
  not not_4 (hc[1], pass_transistor_2_out_3);
  Pass_Transistor pass_transistor_2 (.in_1(nand_1_out), .out_3(pass_transistor_2_out_3), .in_2(f2));
  nand nand_1 (nand_1_out, or_1_out, nand_2_out);
  nand nand_2 (nand_2_out, nor_2_out, pass_transistor_2_2_out);
  Pass_Transistor_2 pass_transistor_2_2 (
    .in_3(hc_inc), .CLEAR(hc_reset), .IN(hc[1]), .OUT(pass_transistor_2_2_out));  // open: PRESET
  and and_2 (and_2_out, nand_2_out, pass_transistor_2_3_out);
  not not_5 (inv_hc[2], pass_transistor_3_out_3);
  Pass_Transistor pass_transistor_3 (.in_1(nor_3_out), .out_3(pass_transistor_3_out_3), .in_2(f2));
  nor nor_3 (nor_3_out, and_2_out, nor_4_out);
  not not_6 (hc[2], inv_hc[2]);
  Pass_Transistor_2 pass_transistor_2_3 (
    .in_3(hc_inc), .PRESET(hc_reset), .IN(inv_hc[2]), .OUT(pass_transistor_2_3_out));  // open: CLEAR
  nor nor_4 (nor_4_out, nand_2_out, pass_transistor_2_3_out);
  not not_7 (inv_hc[3], hc[3]);
  not not_8 (hc[3], pass_transistor_4_out_3);
  Pass_Transistor pass_transistor_4 (.in_1(nand_3_out), .out_3(pass_transistor_4_out_3), .in_2(f2));
  nand nand_3 (nand_3_out, or_2_out, nand_4_out);
  or or_2 (or_2_out, nor_4_out, pass_transistor_2_4_out);
  nand nand_4 (nand_4_out, nor_4_out, pass_transistor_2_4_out);
  Pass_Transistor_2 pass_transistor_2_4 (
    .in_3(hc_inc), .CLEAR(hc_reset), .IN(hc[3]), .OUT(pass_transistor_2_4_out));  // open: PRESET
  nor nor_5 (nor_5_out, inv_hc[0], inv_hc[2], pass_transistor_4_out_3, pass_transistor_2_out_3);
  not not_9 (not_9_out, nor_5_out);
  Pass_Transistor_2 pass_transistor_2_5 (
    .in_3(hc_inc), .PRESET(hc_reset), .IN(not_9_out), .OUT(pass_transistor_2_5_out));  // open: CLEAR
  and and_3 (and_3_out, pass_transistor_2_5_out, pass_transistor_2_6_out);
  not not_10 (hc[4], inv_hc[4]);
  not not_11 (inv_hc[4], pass_transistor_5_out_3);
  Pass_Transistor pass_transistor_5 (.in_1(nor_6_out), .out_3(pass_transistor_5_out_3), .in_2(f2));
  nor nor_6 (nor_6_out, and_3_out, nor_7_out);
  nor nor_7 (nor_7_out, pass_transistor_2_5_out, pass_transistor_2_6_out);
  Pass_Transistor_2 pass_transistor_2_6 (
    .in_3(hc_inc), .PRESET(hc_reset), .IN(inv_hc[4]), .OUT(pass_transistor_2_6_out));  // open: CLEAR
  not not_12 (inv_hc[5], hc[5]);
  or or_3 (or_3_out, nor_7_out, pass_transistor_2_7_out);
  not not_13 (hc[5], pass_transistor_6_out_3);
  Pass_Transistor pass_transistor_6 (.in_1(nand_5_out), .out_3(pass_transistor_6_out_3), .in_2(f2));
  nand nand_5 (nand_5_out, or_3_out, nand_6_out);
  Pass_Transistor_2 pass_transistor_2_7 (
    .in_3(hc_inc), .CLEAR(hc_reset), .IN(hc[5]), .OUT(pass_transistor_2_7_out));  // open: PRESET
  nand nand_6 (nand_6_out, nor_7_out, pass_transistor_2_7_out);
  not not_14 (inv_hc[6], pass_transistor_7_out_3);
  Pass_Transistor pass_transistor_7 (.in_1(nor_8_out), .out_3(pass_transistor_7_out_3), .in_2(f2));
  nor nor_8 (nor_8_out, and_4_out, nor_9_out);
  and and_4 (and_4_out, nand_6_out, pass_transistor_2_8_out);
  not not_15 (hc[6], inv_hc[6]);
  nor nor_9 (nor_9_out, nand_6_out, pass_transistor_2_8_out);
  Pass_Transistor_2 pass_transistor_2_8 (
    .in_3(hc_inc), .PRESET(hc_reset), .IN(inv_hc[6]), .OUT(pass_transistor_2_8_out));  // open: CLEAR
  not not_16 (inv_hc[7], hc[7]);
  not not_17 (hc[7], pass_transistor_8_out_3);
  Pass_Transistor pass_transistor_8 (.in_1(nand_7_out), .out_3(pass_transistor_8_out_3), .in_2(f2));
  nand nand_7 (nand_7_out, or_4_out, nand_8_out);
  or or_4 (or_4_out, nor_9_out, pass_transistor_2_9_out);
  nand nand_8 (nand_8_out, nor_9_out, pass_transistor_2_9_out);
  Pass_Transistor_2 pass_transistor_2_9 (
    .in_3(hc_inc), .CLEAR(hc_reset), .IN(hc[7]), .OUT(pass_transistor_2_9_out));  // open: PRESET
endmodule

module X_Decoder (
  input  [7:0] hc,
  input  [7:0] inv_hc,
  input  f1,
  input  f2,
  output col_brst,
  output h_blank,
  output x_35,
  output x_0,
  output h_sync,
  output x_70,
  output v_sync_pulse
);

  wire cb7_out, cb11_out, hb12_out, hb70_out, hs1_out, hs6_out, nor_5_out, nor_7_out, nor_8_out, nor_10_out,
       x_2_out, x_6_out, x_38_out, x_41_out;

  nor cb11 (cb11_out, inv_hc[3], inv_hc[0], inv_hc[1], hc[7], hc[5], hc[2], hc[6], hc[4], f1);
  nor cb7 (cb7_out, inv_hc[2], inv_hc[0], inv_hc[1], hc[7], hc[5], hc[4], hc[3], hc[6]);
  nor hb12 (hb12_out, inv_hc[3], inv_hc[2], hc[1], hc[7], hc[0], hc[5], hc[4], hc[6], f1);
  nor hb70 (hb70_out, inv_hc[2], inv_hc[1], hc[7], inv_hc[6], hc[0], hc[5], hc[4], hc[3]);
  nor nor_1 (x_35, inv_hc[0], inv_hc[1], hc[7], inv_hc[5], hc[2], hc[4], hc[3], hc[6]);
  nor nor_2 (x_0, hc[1], hc[7], hc[2], hc[0], hc[5], hc[4], hc[3], hc[6]);
  nor hs1 (hs1_out, hc[1], inv_hc[0], hc[7], hc[2], hc[5], hc[4], hc[3], hc[6]);
  nor hs6 (hs6_out, inv_hc[2], inv_hc[1], hc[7], hc[0], hc[5], hc[4], hc[3], hc[6]);
  nor nor_3 (x_70, inv_hc[2], inv_hc[1], hc[7], inv_hc[6], hc[0], hc[5], hc[4], hc[3]);
  nor x_41 (x_41_out, inv_hc[3], hc[1], inv_hc[0], hc[7], inv_hc[5], hc[2], hc[4], hc[6]);
  nor x_6 (x_6_out, inv_hc[2], inv_hc[1], hc[7], hc[0], hc[5], hc[4], hc[3], hc[6]);
  nor x_2 (x_2_out, inv_hc[1], hc[7], hc[2], hc[0], hc[5], hc[4], hc[3], hc[6], f2);
  nor x_38 (x_38_out, inv_hc[2], inv_hc[1], hc[7], inv_hc[5], hc[0], hc[4], hc[3], hc[6], f1);
  nor nor_4 (col_brst, cb11_out, nor_5_out);
  nor nor_5 (nor_5_out, col_brst, cb7_out);
  nor nor_6 (h_blank, hb12_out, nor_7_out);
  nor nor_7 (nor_7_out, h_blank, hb70_out);
  nor nor_8 (nor_8_out, hs1_out, h_sync);
  nor nor_9 (h_sync, nor_8_out, hs6_out);
  nor nor_10 (nor_10_out, x_41_out, x_6_out, v_sync_pulse);
  nor nor_11 (v_sync_pulse, nor_10_out, x_2_out, x_38_out);
endmodule

module Horizontal_Reset (
  input  f1,
  input  x_70,
  input  f2,
  input  inv_reset,
  output hc_reset,
  output inv_start_line,
  output hc_inc,
  output ext_reset
);

  wire nor_1_out, not_2_out, not_3_out, not_5_out, not_6_out, pass_transistor_1_out_3,
       pass_transistor_2_out_3, pass_transistor_3_out_3, pass_transistor_4_out_3;

  not not_1 (ext_reset, pass_transistor_1_out_3);
  Pass_Transistor pass_transistor_1 (.in_1(not_2_out), .out_3(pass_transistor_1_out_3), .in_2(f2));
  not not_2 (not_2_out, not_3_out);
  not not_3 (not_3_out, inv_reset);
  not not_4 (hc_reset, not_5_out);
  not not_5 (not_5_out, pass_transistor_2_out_3);
  Pass_Transistor pass_transistor_2 (.in_1(not_6_out), .out_3(pass_transistor_2_out_3), .in_2(f1));
  not not_6 (not_6_out, nor_1_out);
  nor nor_1 (nor_1_out, x_70, ext_reset);
  Pass_Transistor pass_transistor_3 (.in_1(hc_reset), .out_3(pass_transistor_3_out_3), .in_2(f2));
  Pass_Transistor pass_transistor_4 (.in_1(nor_1_out), .out_3(pass_transistor_4_out_3), .in_2(f1));
  not not_7 (inv_start_line, pass_transistor_3_out_3);
  Multiplexer #(.enable("false")) multiplexer_1 (.in0(1'b0), .in1(f1), .out(hc_inc), .sel(pass_transistor_4_out_3));
endmodule

module MOS_6561 (
  input  clk_in_1,
  input  inv_reset,
  output clk_out_2,
  output clk_out_1
);

  wire clock_generator_1_in1, clock_generator_1_in2, clock_generator_1_mem_clk_1,
       clock_generator_1_mem_clk_2, horizontal_reset_1_ext_reset, horizontal_reset_1_hc_inc,
       horizontal_reset_1_hc_reset, sx_comparator_1_int, vertical_counter_1_hl, vertical_counter_1_inv_hl,
       vertical_reset_1_inv_half_ena, vertical_reset_1_vc_enable, vertical_reset_1_vc_inc,
       vertical_reset_1_vc_reset, x_decoder_1_col_brst, x_decoder_1_h_blank, x_decoder_1_h_sync,
       x_decoder_1_v_sync_pulse, x_decoder_1_x_0, x_decoder_1_x_35, x_decoder_1_x_70, y_decoder_1_v_blank,
       y_decoder_1_v_sync, y_decoder_1_y_311, y_decoder_1_y_312;
  wire [7:0] cr0_sx_int_q, cr1_sy_q, horizontal_counter_1_hc, horizontal_counter_1_inv_hc;
  wire [8:0] vertical_counter_1_inv_vc, vertical_counter_1_vc;

  Register cr0_sx_int (.Q(cr0_sx_int_q));  // open: D, en, clk, clr
  // Probe on horizontal_counter_1_hc
  Horizontal_Counter horizontal_counter_1 (
    .hc_reset(horizontal_reset_1_hc_reset), .hc_inc(horizontal_reset_1_hc_inc), .hc(horizontal_counter_1_hc),
    .inv_hc(horizontal_counter_1_inv_hc), .f2(clk_out_2));
  Horizontal_Reset horizontal_reset_1 (
    .hc_inc(horizontal_reset_1_hc_inc), .inv_reset(inv_reset), .x_70(x_decoder_1_x_70), .f1(clk_out_1),
    .f2(clk_out_2), .hc_reset(horizontal_reset_1_hc_reset), .ext_reset(horizontal_reset_1_ext_reset));  // open: inv_start_line
  Clock_Generator clock_generator_1 (
    .f2(clk_out_2), .mem_clk_2(clock_generator_1_mem_clk_2), .clk_in_1(clk_in_1),
    .mem_clk_1(clock_generator_1_mem_clk_1), .in2(clock_generator_1_in2), .in1(clock_generator_1_in1),
    .inv_reset(inv_reset), .f1(clk_out_1));
  Register cr1_sy (.Q(cr1_sy_q));  // open: D, en, clk, clr
  SX_Comparator sx_comparator_1 (
    .\int (sx_comparator_1_int), .hc(horizontal_counter_1_hc), .cr0(cr0_sx_int_q));  // open: sx_cmp
  X_Decoder x_decoder_1 (
    .h_sync(x_decoder_1_h_sync), .x_0(x_decoder_1_x_0), .x_35(x_decoder_1_x_35),
    .h_blank(x_decoder_1_h_blank), .col_brst(x_decoder_1_col_brst), .f2(clk_out_2), .f1(clk_out_1),
    .inv_hc(horizontal_counter_1_inv_hc), .hc(horizontal_counter_1_hc), .x_70(x_decoder_1_x_70),
    .v_sync_pulse(x_decoder_1_v_sync_pulse));
  LED led_1 (.in(x_decoder_1_col_brst));
  LED led_2 (.in(x_decoder_1_h_blank));
  LED led_3 (.in(x_decoder_1_h_sync));
  // Probe on vertical_counter_1_vc
  Vertical_Reset vertical_reset_1 (
    .vc_inc(vertical_reset_1_vc_inc), .vc_reset(vertical_reset_1_vc_reset), .x_0(x_decoder_1_x_0),
    .x_35(x_decoder_1_x_35), .ext_reset(horizontal_reset_1_ext_reset), .y_312(y_decoder_1_y_312),
    .y_311(y_decoder_1_y_311), .vc_enable(vertical_reset_1_vc_enable),
    .inv_half_ena(vertical_reset_1_inv_half_ena), .f1(clk_out_1), .f2(clk_out_2));  // open: last_line
  LED led_4 (.in(clock_generator_1_in1));
  LED led_5 (.in(clock_generator_1_in2));
  LED led_6 (.in(clock_generator_1_mem_clk_1));
  LED led_7 (.in(clock_generator_1_mem_clk_2));
  SY_Comparator sy_comparator_1 (.vc(vertical_counter_1_vc), .cr1(cr1_sy_q));  // open: sy_cmp
  Y_Decoder y_decoder_1 (
    .y_311(y_decoder_1_y_311), .v_blank(y_decoder_1_v_blank), .v_sync_pulse(x_decoder_1_v_sync_pulse),
    .hl(vertical_counter_1_hl), .inv_hl(vertical_counter_1_inv_hl), .vc(vertical_counter_1_vc),
    .inv_vc(vertical_counter_1_inv_vc), .\int (sx_comparator_1_int), .y_312(y_decoder_1_y_312),
    .v_sync(y_decoder_1_v_sync));
  Vertical_Counter vertical_counter_1 (
    .inv_vc(vertical_counter_1_inv_vc), .inv_half_ena(vertical_reset_1_inv_half_ena), .f2(clk_out_2),
    .vc_reset(vertical_reset_1_vc_reset), .vc(vertical_counter_1_vc), .vc_enable(vertical_reset_1_vc_enable),
    .vc_inc(vertical_reset_1_vc_inc), .hl(vertical_counter_1_hl), .inv_hl(vertical_counter_1_inv_hl));
  LED led_8 (.in(y_decoder_1_v_blank));
  LED led_9 (.in(y_decoder_1_v_sync));
endmodule

module Vertical_Reset (
  input  y_311,
  input  y_312,
  input  ext_reset,
  input  x_35,
  input  x_0,
  input  f1,
  input  f2,
  output vc_reset,
  output vc_inc,
  output vc_enable,
  output last_line,
  output inv_half_ena
);

  wire nor_1_out, nor_2_out, nor_4_out, not_3_out, not_5_out, not_6_out, pass_transistor_1_out_3,
       pass_transistor_2_out_3, pass_transistor_3_out_3, pass_transistor_4_out_3, pass_transistor_5_out_3,
       pass_transistor_6_out_3, pass_transistor_7_out_3, pass_transistor_8_out_3, transistor_1_out;

  Pass_Transistor pass_transistor_1 (.in_1(nor_1_out), .out_3(pass_transistor_1_out_3), .in_2(f1));
  not not_1 (inv_half_ena, pass_transistor_1_out_3);
  nor nor_1 (nor_1_out, transistor_1_out, last_line);
  Pass_Transistor pass_transistor_2 (.in_1(y_311), .out_3(pass_transistor_2_out_3), .in_2(f1));
  Pass_Transistor pass_transistor_3 (.in_1(y_312), .out_3(pass_transistor_3_out_3), .in_2(f1));
  nor nor_2 (nor_2_out, pass_transistor_2_out_3, pass_transistor_3_out_3, pass_transistor_5_out_3);
  Pass_Transistor pass_transistor_4 (.in_1(nor_2_out), .out_3(pass_transistor_4_out_3), .in_2(f2));
  not not_2 (last_line, pass_transistor_4_out_3);
  Pass_Transistor pass_transistor_5 (.in_1(ext_reset), .out_3(pass_transistor_5_out_3), .in_2(f1));
  Transistor #(.\type ("n")) transistor_1 (.in(1'b0), .out(transistor_1_out), .gate(pass_transistor_5_out_3));
  nor nor_3 (transistor_1_out, x_35, x_0);
  not not_3 (not_3_out, pass_transistor_6_out_3);
  Pass_Transistor pass_transistor_6 (.in_1(nor_4_out), .out_3(pass_transistor_6_out_3), .in_2(f1));
  nor nor_4 (nor_4_out, transistor_1_out, pass_transistor_4_out_3);
  not not_4 (vc_reset, not_3_out);
  not not_5 (not_5_out, nor_4_out);
  Pass_Transistor pass_transistor_7 (.in_1(not_5_out), .out_3(pass_transistor_7_out_3), .in_2(f2));
  not not_6 (not_6_out, x_0);
  Pass_Transistor pass_transistor_8 (.in_1(not_6_out), .out_3(pass_transistor_8_out_3), .in_2(f1));
  Multiplexer #(.enable("false")) multiplexer_1 (.in0(1'b0), .in1(f1), .out(vc_inc), .sel(pass_transistor_7_out_3));
  nor nor_5 (vc_enable, pass_transistor_8_out_3, inv_half_ena);

  // Notes on the sheet:
  //   X != 0,35
  //   WHEN NOT LAST LINE
endmodule

module Y_Decoder (
  input  \int ,
  input  [8:0] inv_vc,
  input  inv_hl,
  input  hl,
  input  [8:0] vc,
  input  v_sync_pulse,
  output v_blank,
  output y_311,
  output y_312,
  output v_sync
);

  wire and_1_out, multiplexer_1_out, not_1_out, not_2_out, or_1_out, or_2_out, s_r_ff_2_q, y_1_out, y_4_out,
       y_7_out, y_10_out;

  not not_1 (not_1_out, \int );
  nor y_1 (y_1_out, inv_vc[0], vc[1], vc[2], vc[3], vc[4], vc[5], vc[6], vc[7], vc[8]);
  nor y_10 (y_10_out, vc[0], inv_vc[1], vc[2], inv_vc[3], vc[4], vc[5], vc[6], vc[7], vc[8]);
  // NOR_Gate nor_1 is placed but not wired
  nor y_4 (y_4_out, vc[0], vc[1], inv_vc[2], vc[3], vc[4], vc[5], vc[6], vc[7], vc[8]);
  not not_2 (not_2_out, v_sync_pulse);
  nor y_7 (y_7_out, inv_vc[0], inv_vc[1], inv_vc[2], vc[3], vc[4], vc[5], vc[6], vc[7], vc[8]);
  nor nor_2 (y_311, inv_vc[0], inv_vc[1], inv_vc[2], vc[3], inv_vc[4], inv_vc[5], vc[6], vc[7], inv_vc[8]);
  nor nor_3 (y_312, vc[0], vc[1], vc[2], inv_vc[3], inv_vc[4], inv_vc[5], vc[6], vc[7], inv_vc[8], \int , not_1_out);
  S_R_Flip_Flop s_r_ff_1 (.S(y_1_out), .R(y_10_out), .clk(or_1_out), .Q(v_blank));  // open: reset, Qn, preset
  or or_1 (or_1_out, y_1_out, y_10_out);
  and and_1 (and_1_out, y_4_out, not_2_out);
  S_R_Flip_Flop s_r_ff_2 (.S(and_1_out), .R(y_7_out), .clk(or_2_out), .Q(s_r_ff_2_q));  // open: reset, Qn, preset
  or or_2 (or_2_out, and_1_out, y_7_out);
  Multiplexer #(.enable("false")) multiplexer_1 (
    .in0(1'b0), .in1(s_r_ff_2_q), .out(multiplexer_1_out), .sel(v_sync_pulse));
  not not_3 (v_sync, multiplexer_1_out);
endmodule

module SX_Comparator (
  input  [7:0] cr0,
  input  [7:0] hc,
  output sx_cmp,
  output \int 
);

  Comparator #(.width(7), .mode("unsigned")) comparator_1 (.a(cr0[6:0]), .b(hc[6:0]), .eq(sx_cmp));  // open: gt, lt

  assign \int  = cr0[7];
endmodule

module SY_Comparator (
  input  [7:0] cr1,
  input  [8:0] vc,
  output sy_cmp
);

  Comparator comparator_1 (.a(cr1), .b(vc[8:1]), .eq(sy_cmp));  // open: gt, lt
endmodule
