// Logisim project 6561_full_logisim_3.circ as structural Verilog: 23 circuits, main circuit main
module main (
  input  i_ext_reset
);

  wire clk_out, mos_6561_1_clk_out_1, mos_6561_1_clk_out_2;

  Clock #(.highDuration(2), .lowDuration(2)) clk (.out(clk_out));
  Clock sysclk ();  // open: out
  LED led_1 (.in(mos_6561_1_clk_out_2));
  MOS_6561 mos_6561_1 (
    .clk_in_1(clk_out), .i_ext_reset(i_ext_reset), .clk_out_2(mos_6561_1_clk_out_2),
    .clk_out_1(mos_6561_1_clk_out_1));
  LED led_2 (.in(mos_6561_1_clk_out_1));
endmodule

module Pass_Transistor (
  input  in_1,
  input  in_2,
  output out_3
);

  Register #(.width(1)) register_1 (.D(in_1), .en(1'b1), .clk(in_2), .Q(out_3));  // open: clr
endmodule

module Pass_Transistor_2 (
  input  IN,
  input  CLEAR,
  input  in_3,
  input  PRESET,
  output OUT
);

  D_Flip_Flop d_ff_1 (.D(IN), .clk(in_3), .Q(OUT), .preset(PRESET), .reset(CLEAR));  // open: Qn
endmodule

module Pass_Transistor_3 (
  input  IN,
  input  in_2,
  input  SET,
  output OUT
);

  wire controlled_buffer_1_out, controlled_buffer_2_out, not_1_out;

  not not_1 (not_1_out, SET);
  assign controlled_buffer_1_out = SET ? SET : 1'bz;  // Controlled_Buffer controlled_buffer_1
  assign controlled_buffer_2_out = not_1_out ? not_1_out : 1'bz;  // Controlled_Buffer controlled_buffer_2
  D_Flip_Flop d_ff_1 (
    .clk(in_2), .D(IN), .Q(OUT), .preset(controlled_buffer_1_out), .reset(controlled_buffer_2_out));  // open: Qn
endmodule

module Clock_Generator (
  input  clk_in_1,
  input  i_ext_reset,
  output mem_clk_1,
  output mem_clk_2,
  output in1,
  output in2,
  output f2,
  output f1
);

  wire nand_1_out, nand_2_out, nor_1_out, nor_2_out, nor_3_out, nor_4_out, nor_5_out, nor_6_out, nor_7_out,
       nor_8_out, nor_9_out, not_1_out, not_3_out, not_4_out, not_6_out, not_7_out, not_10_out, not_11_out,
       not_12_out, not_13_out, not_14_out, not_15_out, not_16_out, not_17_out, not_18_out, not_19_out,
       or_1_out, pass_transistor_1_out_3, pass_transistor_2_out_3, pass_transistor_3_out_3,
       pass_transistor_4_out_3, pass_transistor_5_out_3, pass_transistor_6_out_3, transistor_1_out;

  nor nor_1 (nor_1_out, nor_4_out, f1);
  not not_1 (not_1_out, nor_1_out);
  not not_2 (f2, not_1_out);
  not not_3 (not_3_out, nor_4_out);
  nor nor_2 (nor_2_out, f2, not_3_out);
  not not_4 (not_4_out, nor_2_out);
  not not_5 (f1, not_4_out);
  not not_6 (not_6_out, pass_transistor_1_out_3);
  Pass_Transistor pass_transistor_1 (.in_1(not_7_out), .out_3(pass_transistor_1_out_3), .in_2(not_16_out));
  not not_7 (not_7_out, i_ext_reset);
  Pass_Transistor pass_transistor_2 (.in_1(not_6_out), .out_3(pass_transistor_2_out_3), .in_2(not_15_out));
  not not_8 (mem_clk_1, not_10_out);
  not not_9 (mem_clk_2, not_11_out);
  nor nor_3 (nor_3_out, pass_transistor_2_out_3, i_ext_reset);
  not not_10 (not_10_out, nor_5_out);
  not not_11 (not_11_out, nor_6_out);
  nor nor_4 (nor_4_out, nor_3_out, pass_transistor_4_out_3);
  Pass_Transistor pass_transistor_3 (.in_1(nor_4_out), .out_3(pass_transistor_3_out_3), .in_2(not_15_out));
  nor nor_5 (nor_5_out, not_13_out, mem_clk_2);
  nor nor_6 (nor_6_out, mem_clk_1, not_12_out);
  Pass_Transistor pass_transistor_4 (.in_1(nand_1_out), .out_3(pass_transistor_4_out_3), .in_2(not_16_out));
  nand nand_1 (nand_1_out, nand_2_out, or_1_out);
  nand nand_2 (nand_2_out, pass_transistor_3_out_3, not_14_out);
  not not_12 (not_12_out, not_13_out);
  or or_1 (or_1_out, pass_transistor_3_out_3, not_14_out);
  Pass_Transistor pass_transistor_5 (.in_1(nor_7_out), .out_3(pass_transistor_5_out_3), .in_2(not_16_out));
  nor nor_7 (nor_7_out, nor_3_out, not_14_out);
  not not_13 (not_13_out, pass_transistor_5_out_3);
  not not_14 (not_14_out, pass_transistor_6_out_3);
  Pass_Transistor pass_transistor_6 (.in_1(not_13_out), .out_3(pass_transistor_6_out_3), .in_2(not_15_out));
  not not_15 (not_15_out, not_17_out);
  not not_16 (not_16_out, not_18_out);
  not not_17 (not_17_out, nor_8_out);
  nor nor_8 (nor_8_out, not_19_out, not_16_out);
  nor nor_9 (nor_9_out, not_15_out, clk_in_1);
  not not_18 (not_18_out, nor_9_out);
  not not_19 (not_19_out, clk_in_1);
  Transistor #(.\type ("n")) transistor_1 (.in(1'b1), .out(transistor_1_out), .gate(not_15_out));
  Transistor #(.\type ("n")) transistor_2 (.in(1'b0), .out(transistor_1_out), .gate(not_16_out));
  not not_20 (in2, transistor_1_out);

  assign in1 = clk_in_1;
endmodule

module Vertical_Counter (
  input  f2,
  input  vc_reset,
  input  vc_enable,
  input  vc_inc,
  input  i_half_ena,
  output hl,
  output i_hl,
  output [8:0] vc,
  output [8:0] i_vc
);

  not not_1 (i_hl, i_half_ena);
  Counter #(.width(9), .max('h1ff)) counter_1 (
    .clr(vc_reset), .load(1'b0), .up(1'b1), .count(vc_enable), .clk(vc_inc), .Q(vc));  // open: D, carry
  assign i_vc = ~vc;  // NOT_Gate not_2, 9 bits wide

  assign hl = i_half_ena;
endmodule

module Horizontal_Counter (
  input  hc_reset,
  input  hc_inc,
  input  f2,
  output [7:0] hc,
  output [7:0] i_hc
);

  Counter counter_1 (.clr(hc_reset), .load(1'b0), .up(1'b1), .count(1'b1), .clk(hc_inc), .Q(hc));  // open: D, carry
  assign i_hc = ~hc;  // NOT_Gate not_1, 8 bits wide
endmodule

module X_Decoder (
  input  [7:0] hc,
  input  [7:0] i_hc,
  input  f1,
  input  f2,
  output col_brst,
  output h_blank,
  output x_35,
  output x_0,
  output h_sync,
  output x_70,
  output v_sync_pulse
);

  wire cb7_out, cb11_out, hb12_out, hb70_out, hs1_out, hs6_out, or_1_out, or_2_out, or_3_out, or_4_out,
       or_5_out, or_6_out, x_2_out, x_6_out, x_38_out, x_41_out;

  nor cb11 (cb11_out, i_hc[3], i_hc[0], i_hc[1], hc[7], hc[5], hc[2], hc[6], hc[4], f1);
  or or_1 (or_1_out, cb7_out, cb11_out);
  nor cb7 (cb7_out, i_hc[2], i_hc[0], i_hc[1], hc[7], hc[5], hc[4], hc[3], hc[6]);
  nor hb12 (hb12_out, i_hc[3], i_hc[2], hc[1], hc[7], hc[0], hc[5], hc[4], hc[6], f1);
  or or_2 (or_2_out, hb70_out, hb12_out);
  nor hb70 (hb70_out, i_hc[2], i_hc[1], hc[7], i_hc[6], hc[0], hc[5], hc[4], hc[3]);
  nor nor_1 (x_35, i_hc[0], i_hc[1], hc[7], i_hc[5], hc[2], hc[4], hc[3], hc[6]);
  nor nor_2 (x_0, hc[1], hc[7], hc[2], hc[0], hc[5], hc[4], hc[3], hc[6]);
  nor hs1 (hs1_out, hc[1], i_hc[0], hc[7], hc[2], hc[5], hc[4], hc[3], hc[6]);
  or or_3 (or_3_out, hs1_out, hs6_out);
  nor hs6 (hs6_out, i_hc[2], i_hc[1], hc[7], hc[0], hc[5], hc[4], hc[3], hc[6]);
  nor nor_3 (x_70, i_hc[2], i_hc[1], hc[7], i_hc[6], hc[0], hc[5], hc[4], hc[3]);
  nor x_41 (x_41_out, i_hc[3], hc[1], i_hc[0], hc[7], i_hc[5], hc[2], hc[4], hc[6]);
  or or_4 (or_4_out, x_41_out, x_6_out);
  nor x_6 (x_6_out, i_hc[2], i_hc[1], hc[7], hc[0], hc[5], hc[4], hc[3], hc[6]);
  nor x_2 (x_2_out, i_hc[1], hc[7], hc[2], hc[0], hc[5], hc[4], hc[3], hc[6], f2);
  or or_5 (or_5_out, x_2_out, x_38_out);
  nor x_38 (x_38_out, i_hc[2], i_hc[1], hc[7], i_hc[5], hc[0], hc[4], hc[3], hc[6], f1);
  S_R_Flip_Flop s_r_ff_1 (.S(cb7_out), .R(cb11_out), .clk(or_1_out), .Q(col_brst));  // open: reset, Qn, preset
  S_R_Flip_Flop s_r_ff_2 (.S(hb70_out), .R(hb12_out), .clk(or_2_out), .Q(h_blank));  // open: reset, Qn, preset
  S_R_Flip_Flop s_r_ff_3 (.S(hs1_out), .R(hs6_out), .clk(or_3_out), .Q(h_sync));  // open: reset, Qn, preset
  S_R_Flip_Flop s_r_ff_4 (.S(or_4_out), .R(or_5_out), .clk(or_6_out), .Q(v_sync_pulse));  // open: reset, Qn, preset
  or or_6 (or_6_out, or_4_out, or_5_out);
endmodule

module Horizontal_Reset (
  input  f1,
  input  x_70,
  input  f2,
  input  i_ext_reset,
  output hc_reset,
  output i_new_line,
  output hc_inc,
  output ext_reset
);

  wire nor_1_out, not_2_out, not_3_out, not_5_out, not_6_out, pass_transistor_1_out_3,
       pass_transistor_2_out_3, pass_transistor_3_out_3, pass_transistor_4_out_3;

  not not_1 (ext_reset, pass_transistor_1_out_3);
  Pass_Transistor pass_transistor_1 (.in_1(not_2_out), .out_3(pass_transistor_1_out_3), .in_2(f2));
  not not_2 (not_2_out, not_3_out);
  not not_3 (not_3_out, i_ext_reset);
  not not_4 (hc_reset, not_5_out);
  not not_5 (not_5_out, pass_transistor_2_out_3);
  Pass_Transistor pass_transistor_2 (.in_1(not_6_out), .out_3(pass_transistor_2_out_3), .in_2(f1));
  not not_6 (not_6_out, nor_1_out);
  nor nor_1 (nor_1_out, x_70, ext_reset);
  Pass_Transistor pass_transistor_3 (.in_1(hc_reset), .out_3(pass_transistor_3_out_3), .in_2(f2));
  Pass_Transistor pass_transistor_4 (.in_1(nor_1_out), .out_3(pass_transistor_4_out_3), .in_2(f1));
  not not_7 (i_new_line, pass_transistor_3_out_3);
  Multiplexer #(.enable("false")) multiplexer_1 (.in0(1'b0), .in1(f1), .out(hc_inc), .sel(pass_transistor_4_out_3));
endmodule

module MOS_6561 (
  input  clk_in_1,
  input  i_ext_reset,
  output clk_out_2,
  output clk_out_1
);

  wire cell_depth_reset_1_cdc_enable, cell_depth_reset_1_cdc_inc, cell_depth_reset_1_cdc_reset,
       clock_generator_1_in1, clock_generator_1_in2, clock_generator_1_mem_clk_1,
       clock_generator_1_mem_clk_2, cr0_1_int, cr3_1_double, horiz_cell_counter_1_hcc_last,
       horizontal_reset_1_ext_reset, horizontal_reset_1_hc_inc, horizontal_reset_1_hc_reset,
       horizontal_reset_1_i_new_line, sx_comparator_1_sx_cmp, sy_comparator_1_sy_cmp,
       vert_cell_counter_1_vcc_last, vertical_counter_1_hl, vertical_counter_1_i_hl,
       vertical_reset_1_i_half_ena, vertical_reset_1_last_line, vertical_reset_1_vc_enable,
       vertical_reset_1_vc_inc, vertical_reset_1_vc_reset, within_matrix_1_i_in_matrix,
       within_matrix_1_i_mtrx_line, x_decoder_1_col_brst, x_decoder_1_h_blank, x_decoder_1_h_sync,
       x_decoder_1_v_sync_pulse, x_decoder_1_x_0, x_decoder_1_x_35, x_decoder_1_x_70, y_decoder_1_v_blank,
       y_decoder_1_v_sync, y_decoder_1_y_311, y_decoder_1_y_312;
  wire [3:0] cell_depth_counter_1_i_cdc;
  wire [5:0] cr3_1_num_rows;
  wire [6:0] cr0_1_sx, cr2_1_num_cols;
  wire [7:0] cr1_1_sy, horizontal_counter_1_hc, horizontal_counter_1_i_hc;
  wire [8:0] vertical_counter_1_i_vc, vertical_counter_1_vc;

  // Probe on horizontal_counter_1_hc
  Horizontal_Counter horizontal_counter_1 (
    .hc_reset(horizontal_reset_1_hc_reset), .hc_inc(horizontal_reset_1_hc_inc), .hc(horizontal_counter_1_hc),
    .i_hc(horizontal_counter_1_i_hc), .f2(clk_out_2));
  Horizontal_Reset horizontal_reset_1 (
    .f2(clk_out_2), .x_70(x_decoder_1_x_70), .i_ext_reset(i_ext_reset),
    .hc_reset(horizontal_reset_1_hc_reset), .hc_inc(horizontal_reset_1_hc_inc), .f1(clk_out_1),
    .ext_reset(horizontal_reset_1_ext_reset), .i_new_line(horizontal_reset_1_i_new_line));
  Clock_Generator clock_generator_1 (
    .f2(clk_out_2), .in1(clock_generator_1_in1), .mem_clk_1(clock_generator_1_mem_clk_1),
    .clk_in_1(clk_in_1), .i_ext_reset(i_ext_reset), .mem_clk_2(clock_generator_1_mem_clk_2),
    .in2(clock_generator_1_in2), .f1(clk_out_1));
  CR0 cr0_1 (.sx(cr0_1_sx), .\int (cr0_1_int));  // open: data_out, i_write, address, i_read, data_in
  SX_Comparator sx_comparator_1 (.sx_cmp(sx_comparator_1_sx_cmp), .hc(horizontal_counter_1_hc), .sx(cr0_1_sx));
  X_Decoder x_decoder_1 (
    .h_sync(x_decoder_1_h_sync), .hc(horizontal_counter_1_hc), .x_0(x_decoder_1_x_0),
    .i_hc(horizontal_counter_1_i_hc), .x_35(x_decoder_1_x_35), .f1(clk_out_1), .h_blank(x_decoder_1_h_blank),
    .f2(clk_out_2), .col_brst(x_decoder_1_col_brst), .x_70(x_decoder_1_x_70),
    .v_sync_pulse(x_decoder_1_v_sync_pulse));
  LED led_1 (.in(x_decoder_1_col_brst));
  LED led_2 (.in(x_decoder_1_h_blank));
  LED led_3 (.in(x_decoder_1_h_sync));
  // Probe on vertical_counter_1_vc
  Vertical_Reset vertical_reset_1 (
    .vc_inc(vertical_reset_1_vc_inc), .vc_enable(vertical_reset_1_vc_enable),
    .vc_reset(vertical_reset_1_vc_reset), .last_line(vertical_reset_1_last_line), .x_0(x_decoder_1_x_0),
    .y_311(y_decoder_1_y_311), .x_35(x_decoder_1_x_35), .y_312(y_decoder_1_y_312),
    .ext_reset(horizontal_reset_1_ext_reset), .i_half_ena(vertical_reset_1_i_half_ena), .f1(clk_out_1),
    .f2(clk_out_2));
  LED led_4 (.in(clock_generator_1_in1));
  LED led_5 (.in(clock_generator_1_in2));
  LED led_6 (.in(clock_generator_1_mem_clk_1));
  LED led_7 (.in(clock_generator_1_mem_clk_2));
  CR1 cr1_1 (.sy(cr1_1_sy));  // open: data_out, i_write, address, i_read, data_in
  SY_Comparator sy_comparator_1 (.sy_cmp(sy_comparator_1_sy_cmp), .sy(cr1_1_sy), .vc(vertical_counter_1_vc));
  Y_Decoder y_decoder_1 (
    .\int (cr0_1_int), .y_311(y_decoder_1_y_311), .i_vc(vertical_counter_1_i_vc),
    .v_blank(y_decoder_1_v_blank), .vc(vertical_counter_1_vc), .v_sync_pulse(x_decoder_1_v_sync_pulse),
    .i_hl(vertical_counter_1_i_hl), .hl(vertical_counter_1_hl), .y_312(y_decoder_1_y_312),
    .v_sync(y_decoder_1_v_sync));
  Vertical_Counter vertical_counter_1 (
    .i_vc(vertical_counter_1_i_vc), .vc_enable(vertical_reset_1_vc_enable),
    .vc_reset(vertical_reset_1_vc_reset), .f2(clk_out_2), .vc_inc(vertical_reset_1_vc_inc),
    .i_half_ena(vertical_reset_1_i_half_ena), .vc(vertical_counter_1_vc), .hl(vertical_counter_1_hl),
    .i_hl(vertical_counter_1_i_hl));
  // Probe on cr1_1_sy
  LED led_8 (.in(y_decoder_1_v_blank));
  LED led_9 (.in(y_decoder_1_v_sync));
  Cell_Depth_Reset cell_depth_reset_1 (
    .cdc_reset(cell_depth_reset_1_cdc_reset), .i_mtrx_line(within_matrix_1_i_mtrx_line), .f1(clk_out_1),
    .i_new_line(horizontal_reset_1_i_new_line), .i_cdc(cell_depth_counter_1_i_cdc), .double(cr3_1_double),
    .cdc_enable(cell_depth_reset_1_cdc_enable), .f2(clk_out_2), .cdc_inc(cell_depth_reset_1_cdc_inc));  // open: cdc_last
  Cell_Depth_Counter cell_depth_counter_1 (
    .i_cdc(cell_depth_counter_1_i_cdc), .cdc_inc(cell_depth_reset_1_cdc_inc),
    .cdc_enable(cell_depth_reset_1_cdc_enable), .cdc_reset(cell_depth_reset_1_cdc_reset), .f2(clk_out_2));  // open: cdc
  CR3 cr3_1 (.double(cr3_1_double), .num_rows(cr3_1_num_rows));  // open: data_out, i_write, address, i_read, data_in
  Vert_Cell_Counter vert_cell_counter_1 (
    .num_rows(cr3_1_num_rows), .f2(clk_out_2), .f1(clk_out_1), .vcc_last(vert_cell_counter_1_vcc_last));  // open: vcc_enable, vcc_load
  Within_Matrix within_matrix_1 (
    .i_mtrx_line(within_matrix_1_i_mtrx_line), .f1(clk_out_1), .f2(clk_out_2),
    .sy_cmp(sy_comparator_1_sy_cmp), .sx_cmp(sx_comparator_1_sx_cmp),
    .vcc_last(vert_cell_counter_1_vcc_last), .last_line(vertical_reset_1_last_line),
    .i_new_line(horizontal_reset_1_i_new_line), .hcc_last(horiz_cell_counter_1_hcc_last),
    .i_in_matrix(within_matrix_1_i_in_matrix));  // open: bus_avail
  CR2 cr2_1 (.num_cols(cr2_1_num_cols));  // open: data_out, i_write, address, i_read, data_in, bv9
  Horiz_Cell_Counter horiz_cell_counter_1 (
    .num_cols(cr2_1_num_cols), .f2(clk_out_2), .f1(clk_out_1), .hcc_enable(within_matrix_1_i_in_matrix),
    .hcc_last(horiz_cell_counter_1_hcc_last));  // open: hcc0, hcc_load
endmodule

module Vertical_Reset (
  input  y_311,
  input  y_312,
  input  ext_reset,
  input  x_35,
  input  x_0,
  input  f1,
  input  f2,
  output vc_reset,
  output vc_inc,
  output vc_enable,
  output last_line,
  output i_half_ena
);

  wire nor_1_out, nor_2_out, nor_4_out, not_3_out, not_5_out, not_6_out, pass_transistor_1_out_3,
       pass_transistor_2_out_3, pass_transistor_3_out_3, pass_transistor_4_out_3, pass_transistor_5_out_3,
       pass_transistor_6_out_3, pass_transistor_7_out_3, pass_transistor_8_out_3, transistor_1_out;

  Pass_Transistor pass_transistor_1 (.in_1(nor_1_out), .out_3(pass_transistor_1_out_3), .in_2(f1));
  not not_1 (i_half_ena, pass_transistor_1_out_3);
  nor nor_1 (nor_1_out, transistor_1_out, last_line);
  Pass_Transistor pass_transistor_2 (.in_1(y_311), .out_3(pass_transistor_2_out_3), .in_2(f1));
  Pass_Transistor pass_transistor_3 (.in_1(y_312), .out_3(pass_transistor_3_out_3), .in_2(f1));
  nor nor_2 (nor_2_out, pass_transistor_2_out_3, pass_transistor_3_out_3, pass_transistor_5_out_3);
  Pass_Transistor pass_transistor_4 (.in_1(nor_2_out), .out_3(pass_transistor_4_out_3), .in_2(f2));
  not not_2 (last_line, pass_transistor_4_out_3);
  Pass_Transistor pass_transistor_5 (.in_1(ext_reset), .out_3(pass_transistor_5_out_3), .in_2(f1));
  Transistor #(.\type ("n")) transistor_1 (.in(1'b0), .out(transistor_1_out), .gate(pass_transistor_5_out_3));
  nor nor_3 (transistor_1_out, x_35, x_0);
  not not_3 (not_3_out, pass_transistor_6_out_3);
  Pass_Transistor pass_transistor_6 (.in_1(nor_4_out), .out_3(pass_transistor_6_out_3), .in_2(f1));
  nor nor_4 (nor_4_out, transistor_1_out, pass_transistor_4_out_3);
  not not_4 (vc_reset, not_3_out);
  not not_5 (not_5_out, nor_4_out);
  Pass_Transistor pass_transistor_7 (.in_1(not_5_out), .out_3(pass_transistor_7_out_3), .in_2(f2));
  not not_6 (not_6_out, x_0);
  Pass_Transistor pass_transistor_8 (.in_1(not_6_out), .out_3(pass_transistor_8_out_3), .in_2(f1));
  Multiplexer #(.enable("false")) multiplexer_1 (.in0(1'b0), .in1(f1), .out(vc_inc), .sel(pass_transistor_7_out_3));
  nor nor_5 (vc_enable, pass_transistor_8_out_3, i_half_ena);

  // Notes on the sheet:
  //   X != 0,35
  //   WHEN NOT LAST LINE
endmodule

module Y_Decoder (
  input  \int ,
  input  [8:0] i_vc,
  input  i_hl,
  input  hl,
  input  [8:0] vc,
  input  v_sync_pulse,
  output v_blank,
  output y_311,
  output y_312,
  output v_sync
);

  wire and_1_out, multiplexer_1_out, not_1_out, not_2_out, or_1_out, or_2_out, s_r_ff_2_qn, y_1_out, y_4_out,
       y_7_out, y_10_out;

  not not_1 (not_1_out, \int );
  nor y_1 (y_1_out, i_vc[0], vc[1], vc[2], vc[3], vc[4], vc[5], vc[6], vc[7], vc[8]);
  nor y_10 (y_10_out, vc[0], i_vc[1], vc[2], i_vc[3], vc[4], vc[5], vc[6], vc[7], vc[8]);
  // NOR_Gate nor_1 is placed but not wired
  nor y_4 (y_4_out, vc[0], vc[1], i_vc[2], vc[3], vc[4], vc[5], vc[6], vc[7], vc[8]);
  not not_2 (not_2_out, v_sync_pulse);
  nor y_7 (y_7_out, i_vc[0], i_vc[1], i_vc[2], vc[3], vc[4], vc[5], vc[6], vc[7], vc[8]);
  nor nor_2 (y_311, i_vc[0], i_vc[1], i_vc[2], vc[3], i_vc[4], i_vc[5], vc[6], vc[7], i_vc[8]);
  nor nor_3 (y_312, vc[0], vc[1], vc[2], i_vc[3], i_vc[4], i_vc[5], vc[6], vc[7], i_vc[8], \int , not_1_out);
  S_R_Flip_Flop s_r_ff_1 (.S(y_1_out), .R(y_10_out), .clk(or_1_out), .Q(v_blank));  // open: reset, Qn, preset
  or or_1 (or_1_out, y_1_out, y_10_out);
  and and_1 (and_1_out, y_4_out, not_2_out);
  S_R_Flip_Flop s_r_ff_2 (.S(and_1_out), .R(y_7_out), .clk(or_2_out), .Qn(s_r_ff_2_qn));  // open: Q, reset, preset
  or or_2 (or_2_out, and_1_out, y_7_out);
  Multiplexer #(.enable("false")) multiplexer_1 (
    .in0(1'b1), .in1(s_r_ff_2_qn), .out(multiplexer_1_out), .sel(v_sync_pulse));
  not not_3 (v_sync, multiplexer_1_out);
endmodule

module SX_Comparator (
  input  [6:0] sx,
  input  [7:0] hc,
  output sx_cmp
);

  Comparator #(.width(7), .mode("unsigned")) comparator_1 (.a(sx), .b(hc[6:0]), .eq(sx_cmp));  // open: gt, lt
endmodule

module SY_Comparator (
  input  [7:0] sy,
  input  [8:0] vc,
  output sy_cmp
);

  Comparator comparator_1 (.a(sy), .b(vc[8:1]), .eq(sy_cmp));  // open: gt, lt
endmodule

module Cell_Depth_Counter (
  input  cdc_reset,
  input  cdc_enable,
  input  cdc_inc,
  input  f2,
  output [3:0] cdc,
  output [3:0] i_cdc
);

  Counter #(.width(4), .max('hf)) counter_1 (
    .clr(cdc_reset), .load(1'b0), .up(1'b1), .count(cdc_enable), .clk(cdc_inc), .Q(cdc));  // open: D, carry
  assign i_cdc = ~cdc;  // NOT_Gate not_1, 4 bits wide
endmodule

module Cell_Depth_Reset (
  input  double,
  input  [3:0] i_cdc,
  input  i_new_line,
  input  f1,
  input  f2,
  input  i_mtrx_line,
  output cdc_last,
  output cdc_reset,
  output cdc_inc,
  output cdc_enable
);

  wire and_1_out, and_2_out, and_3_out, and_4_out, nand_1_out, not_1_out, not_2_out, not_3_out, not_4_out,
       not_5_out, not_6_out, not_7_out, or_1_out, or_2_out, or_3_out, pass_transistor_1_out_3,
       pass_transistor_2_out_3, pass_transistor_3_out_3, pass_transistor_4_out_3, undriven;

  not not_1 (not_1_out, i_cdc[3]);
  not not_2 (not_2_out, i_cdc[2]);
  not not_3 (not_3_out, i_cdc[1]);
  not not_4 (not_4_out, i_cdc[0]);
  Multiplexer #(.enable("false")) multiplexer_1 (.in0(1'b0), .in1(f1), .out(cdc_inc), .sel(pass_transistor_1_out_3));
  Pass_Transistor pass_transistor_1 (.in_1(cdc_reset), .out_3(pass_transistor_1_out_3), .in_2(f2));
  nor nor_1 (cdc_enable, pass_transistor_2_out_3, cdc_reset, pass_transistor_3_out_3);
  not not_5 (not_5_out, double);
  Pass_Transistor pass_transistor_2 (.in_1(not_7_out), .out_3(pass_transistor_2_out_3), .in_2(f1));
  not not_6 (not_6_out, i_new_line);
  not not_7 (not_7_out, not_6_out);
  or or_1 (or_1_out, double, not_5_out);
  or or_2 (or_2_out, double, not_5_out);
  or or_3 (or_3_out, double, not_5_out);
  nand nand_1 (nand_1_out, cdc_last, not_6_out);
  Pass_Transistor pass_transistor_3 (.in_1(i_mtrx_line), .out_3(pass_transistor_3_out_3), .in_2(undriven));
  and and_1 (and_1_out, double, not_1_out);
  and and_2 (and_2_out, or_1_out, not_2_out);
  and and_3 (and_3_out, or_2_out, not_3_out);
  and and_4 (and_4_out, or_3_out, not_4_out);
  not not_8 (cdc_reset, pass_transistor_4_out_3);
  Pass_Transistor pass_transistor_4 (.in_1(nand_1_out), .out_3(pass_transistor_4_out_3), .in_2(undriven));
  nor nor_2 (cdc_last, and_1_out, and_2_out, and_3_out, and_4_out);
endmodule

module Within_Matrix (
  input  hcc_last,
  input  i_new_line,
  input  last_line,
  input  vcc_last,
  input  sx_cmp,
  input  sy_cmp,
  input  f2,
  input  f1,
  output i_mtrx_line,
  output bus_avail,
  output i_in_matrix
);

  wire and_1_out, nor_1_out, nor_2_out, nor_3_out, nor_4_out, nor_6_out, nor_7_out, not_1_out, not_2_out,
       not_3_out, not_4_out, not_5_out, not_6_out, not_7_out, not_9_out, not_10_out, pass_transistor_1_out_3,
       pass_transistor_2_out_3, pass_transistor_3_out_3, pass_transistor_4_out_3, pass_transistor_5_out_3,
       pass_transistor_6_out_3, pass_transistor_7_out_3, pass_transistor_8_out_3, pass_transistor_9_out_3;

  not not_1 (not_1_out, pass_transistor_1_out_3);
  Pass_Transistor pass_transistor_1 (.in_1(sx_cmp), .out_3(pass_transistor_1_out_3), .in_2(f1));
  Pass_Transistor pass_transistor_2 (.in_1(sy_cmp), .out_3(pass_transistor_2_out_3), .in_2(f1));
  not not_2 (not_2_out, pass_transistor_2_out_3);
  Pass_Transistor pass_transistor_3 (.in_1(not_1_out), .out_3(pass_transistor_3_out_3), .in_2(f2));
  not not_3 (not_3_out, pass_transistor_3_out_3);
  Pass_Transistor pass_transistor_4 (.in_1(not_2_out), .out_3(pass_transistor_4_out_3), .in_2(f2));
  not not_4 (not_4_out, pass_transistor_4_out_3);
  nor nor_1 (nor_1_out, last_line, vcc_last, nor_2_out);
  nor nor_2 (nor_2_out, nor_1_out, not_4_out);
  Pass_Transistor pass_transistor_5 (.in_1(nor_4_out), .out_3(pass_transistor_5_out_3), .in_2(f1));
  not not_5 (not_5_out, i_new_line);
  and and_1 (and_1_out, not_3_out, nor_1_out);
  not not_6 (not_6_out, pass_transistor_5_out_3);
  Pass_Transistor pass_transistor_6 (.in_1(not_6_out), .out_3(pass_transistor_6_out_3), .in_2(f2));
  nor nor_3 (nor_3_out, and_1_out, nor_4_out);
  not not_7 (not_7_out, pass_transistor_6_out_3);
  not not_8 (bus_avail, pass_transistor_7_out_3);
  Pass_Transistor pass_transistor_7 (.in_1(not_7_out), .out_3(pass_transistor_7_out_3), .in_2(f1));
  nor nor_4 (nor_4_out, hcc_last, not_5_out, nor_3_out);
  Pass_Transistor pass_transistor_8 (.in_1(bus_avail), .out_3(pass_transistor_8_out_3), .in_2(f2));
  Pass_Transistor pass_transistor_9 (.in_1(not_9_out), .out_3(pass_transistor_9_out_3), .in_2(f1));
  not not_9 (not_9_out, pass_transistor_8_out_3);
  not not_10 (not_10_out, pass_transistor_9_out_3);
  nor nor_5 (i_mtrx_line, nor_4_out, nor_6_out);
  nor nor_6 (nor_6_out, i_mtrx_line, nor_2_out);
  nor nor_7 (nor_7_out, not_6_out, not_10_out);
  not not_11 (i_in_matrix, nor_7_out);
endmodule

module Horiz_Cell_Counter (
  input  hcc_load,
  input  hcc_enable,
  input  f1,
  input  f2,
  input  [6:0] num_cols,
  output hcc0,
  output hcc_last
);

  wire multiplexer_1_out, pass_transistor_1_out_3;
  wire [6:0] not_1_out;
  wire [7:1] counter_1_q;

  Pass_Transistor pass_transistor_1 (.in_1(hcc_load), .out_3(pass_transistor_1_out_3), .in_2(f2));
  Multiplexer #(.enable("false")) multiplexer_1 (
    .in0(f1), .in1(1'b0), .out(multiplexer_1_out), .sel(pass_transistor_1_out_3));
  assign not_1_out = ~num_cols;  // NOT_Gate not_1, 7 bits wide
  Counter counter_1 (
    .clr(1'b0), .load(hcc_load), .up(1'b1), .count(hcc_enable), .clk(multiplexer_1_out),
    .D({not_1_out, 1'b0}), .Q({counter_1_q, hcc0}));  // open: carry
  nor nor_1 (hcc_last, hcc0, counter_1_q[1], counter_1_q[2], counter_1_q[3], counter_1_q[4], counter_1_q[5], counter_1_q[6], counter_1_q[7], 1'b0);
endmodule

module CR0 (
  input  [7:0] data_in,
  input  i_read,
  input  [3:0] address,
  input  i_write,
  output [7:0] data_out,
  output [6:0] sx,
  output \int 
);

  wire nor_1_out, nor_2_out, nor_3_out, not_1_out;
  wire [7:0] multiplexer_2_out;

  nor nor_1 (nor_1_out, i_read, not_1_out);
  Multiplexer #(.width(8), .disabled("Z"), .enable("false")) multiplexer_1 (
    .in1({\int , sx}), .out(data_out), .sel(nor_1_out));  // open: in0
  nor nor_2 (nor_2_out, 1'b0, address[3], address[2], address[1], address[0]);
  not not_1 (not_1_out, nor_2_out);
  nor nor_3 (nor_3_out, not_1_out, i_write);
  Register register_1 (.D(multiplexer_2_out), .en(nor_3_out), .clk(nor_3_out), .Q({\int , sx}));  // open: clr
  Multiplexer #(.width(8), .disabled("Z"), .enable("false")) multiplexer_2 (
    .in1(data_in), .out(multiplexer_2_out), .sel(nor_3_out));  // open: in0
endmodule

module CR1 (
  input  [7:0] data_in,
  input  i_read,
  input  [3:0] address,
  input  i_write,
  output [7:0] data_out,
  output [7:0] sy
);

  wire nor_1_out, nor_2_out, nor_3_out, not_1_out, not_2_out;
  wire [7:0] multiplexer_2_out;

  nor nor_1 (nor_1_out, i_read, not_2_out);
  Multiplexer #(.width(8), .disabled("Z"), .enable("false")) multiplexer_1 (
    .in1(sy), .out(data_out), .sel(nor_1_out));  // open: in0
  not not_1 (not_1_out, address[0]);
  nor nor_2 (nor_2_out, 1'b0, address[3], address[2], address[1], not_1_out);
  not not_2 (not_2_out, nor_2_out);
  nor nor_3 (nor_3_out, not_2_out, i_write);
  Register register_1 (.D(multiplexer_2_out), .en(nor_3_out), .clk(nor_3_out), .Q(sy));  // open: clr
  Multiplexer #(.width(8), .disabled("Z"), .enable("false")) multiplexer_2 (
    .in1(data_in), .out(multiplexer_2_out), .sel(nor_3_out));  // open: in0
endmodule

module CR2 (
  input  [7:0] data_in,
  input  i_read,
  input  [3:0] address,
  input  i_write,
  output [7:0] data_out,
  output [6:0] num_cols,
  output bv9
);

  wire nor_1_out, nor_2_out, nor_3_out, not_1_out, not_2_out;
  wire [7:0] multiplexer_2_out;

  nor nor_1 (nor_1_out, i_read, not_2_out);
  Multiplexer #(.width(8), .disabled("Z"), .enable("false")) multiplexer_1 (
    .in1({bv9, num_cols}), .out(data_out), .sel(nor_1_out));  // open: in0
  not not_1 (not_1_out, address[1]);
  nor nor_2 (nor_2_out, 1'b0, address[3], address[2], not_1_out, address[0]);
  not not_2 (not_2_out, nor_2_out);
  nor nor_3 (nor_3_out, not_2_out, i_write);
  Register register_1 (.D(multiplexer_2_out), .en(nor_3_out), .clk(nor_3_out), .Q({bv9, num_cols}));  // open: clr
  Multiplexer #(.width(8), .disabled("Z"), .enable("false")) multiplexer_2 (
    .in1(data_in), .out(multiplexer_2_out), .sel(nor_3_out));  // open: in0
endmodule

module CR3 (
  input  [7:0] data_in,
  input  i_read,
  input  [3:0] address,
  input  i_write,
  output [7:0] data_out,
  output double,
  output [5:0] num_rows
);

  wire nor_1_out, nor_2_out, nor_3_out, not_1_out, not_2_out, not_3_out;
  wire [7:0] multiplexer_2_out;
  wire [7:7] register_1_q;

  nor nor_1 (nor_1_out, i_read, not_3_out);
  Multiplexer #(.width(8), .disabled("Z"), .enable("false")) multiplexer_1 (
    .in1({register_1_q[7], num_rows, double}), .out(data_out), .sel(nor_1_out));  // open: in0
  not not_1 (not_1_out, address[1]);
  not not_2 (not_2_out, address[0]);
  nor nor_2 (nor_2_out, 1'b0, address[3], address[2], not_1_out, not_2_out);
  not not_3 (not_3_out, nor_2_out);
  nor nor_3 (nor_3_out, not_3_out, i_write);
  Register register_1 (
    .D(multiplexer_2_out), .en(nor_3_out), .clk(nor_3_out), .Q({register_1_q[7], num_rows, double}));  // open: clr
  Multiplexer #(.width(8), .disabled("Z"), .enable("false")) multiplexer_2 (
    .in1(data_in), .out(multiplexer_2_out), .sel(nor_3_out));  // open: in0
endmodule

module Vert_Cell_Counter (
  input  vcc_load,
  input  vcc_enable,
  input  f1,
  input  f2,
  input  [5:0] num_rows,
  output vcc_last
);

  wire multiplexer_1_out, pass_transistor_1_out_3;
  wire [5:0] counter_1_q, not_1_out;

  Pass_Transistor pass_transistor_1 (.in_1(vcc_load), .out_3(pass_transistor_1_out_3), .in_2(f2));
  Multiplexer #(.enable("false")) multiplexer_1 (
    .in0(f1), .in1(1'b0), .out(multiplexer_1_out), .sel(pass_transistor_1_out_3));
  assign not_1_out = ~num_rows;  // NOT_Gate not_1, 6 bits wide
  Counter #(.width(6), .max('h3f)) counter_1 (
    .clr(1'b0), .load(vcc_load), .up(1'b1), .count(vcc_enable), .clk(multiplexer_1_out), .D(not_1_out),
    .Q(counter_1_q));  // open: carry
  nor nor_1 (vcc_last, counter_1_q[0], counter_1_q[1], counter_1_q[2], counter_1_q[3], counter_1_q[4], counter_1_q[5], 1'b0);
endmodule
