// Logisim project 6561_full_logisim_6.circ as structural Verilog
module VIC_System (
  input  i_ext_reset,
  input  in_2
);

  wire clk_out, mos_6561_1_bus_avail, mos_6561_1_clk_out_1, mos_6561_1_clk_out_2, multiplexer_1_out,
       not_1_out;
  wire [3:0] controlled_buffer_3_out, dipswitch_1_sw4, dipswitch_4_sw4;
  wire [7:0] controlled_buffer_1_out, dipswitch_2_sw8, dipswitch_3_sw8, mos_6561_1_d0_out;

  DipSwitch #(.number(4)) dipswitch_1 (
    .sw1(dipswitch_1_sw4[3]), .sw2(dipswitch_1_sw4[2]), .sw3(dipswitch_1_sw4[1]), .sw4(dipswitch_1_sw4[0]));
  not not_1 (not_1_out, in_2);
  DipSwitch dipswitch_2 (
    .sw1(dipswitch_2_sw8[7]), .sw2(dipswitch_2_sw8[6]), .sw3(dipswitch_2_sw8[5]), .sw4(dipswitch_2_sw8[4]),
    .sw5(dipswitch_2_sw8[3]), .sw6(dipswitch_2_sw8[2]), .sw7(dipswitch_2_sw8[1]), .sw8(dipswitch_2_sw8[0]));
  assign controlled_buffer_1_out = mos_6561_1_clk_out_2 ? dipswitch_2_sw8 : 8'bz;  // Controlled_Buffer controlled_buffer_1
  assign controlled_buffer_1_out = mos_6561_1_clk_out_1 ? dipswitch_3_sw8 : 8'bz;  // Controlled_Buffer controlled_buffer_2
  DipSwitch dipswitch_3 (
    .sw1(dipswitch_3_sw8[7]), .sw2(dipswitch_3_sw8[6]), .sw3(dipswitch_3_sw8[5]), .sw4(dipswitch_3_sw8[4]),
    .sw5(dipswitch_3_sw8[3]), .sw6(dipswitch_3_sw8[2]), .sw7(dipswitch_3_sw8[1]), .sw8(dipswitch_3_sw8[0]));
  LED led_1 (.in(mos_6561_1_bus_avail));
  Multiplexer #(.enable("false")) multiplexer_1 (
    .in0(1'b1), .in1(not_1_out), .out(multiplexer_1_out), .sel(mos_6561_1_clk_out_2));
  DotMatrix #(.matrixcols(8), .matrixrows(1)) dotmatrix_1 (
    .col0(mos_6561_1_d0_out[7]), .col1(mos_6561_1_d0_out[6]), .col2(mos_6561_1_d0_out[5]),
    .col3(mos_6561_1_d0_out[4]), .col4(mos_6561_1_d0_out[3]), .col5(mos_6561_1_d0_out[2]),
    .col6(mos_6561_1_d0_out[1]), .col7(mos_6561_1_d0_out[0]));
  MOS_6561 mos_6561_1 (
    .clk_out_2(mos_6561_1_clk_out_2), .i_ext_reset(i_ext_reset), .clk_in_1(clk_out),
    .clk_out_1(mos_6561_1_clk_out_1), .a0_in(controlled_buffer_3_out[0]), .a1_in(controlled_buffer_3_out[1]),
    .a2_in(controlled_buffer_3_out[2]), .a3_in(controlled_buffer_3_out[3]), .a8_in(1'b0), .a9_in(1'b0),
    .a10_in(1'b0), .a11_in(1'b0), .a12_in(1'b1), .a13_in(1'b0), .d0_in(controlled_buffer_1_out[0]),
    .d1_in(controlled_buffer_1_out[1]), .d2_in(controlled_buffer_1_out[2]),
    .d3_in(controlled_buffer_1_out[3]), .d4_in(controlled_buffer_1_out[4]),
    .d5_in(controlled_buffer_1_out[5]), .d6_in(controlled_buffer_1_out[6]),
    .d7_in(controlled_buffer_1_out[7]), .d8_in(dipswitch_1_sw4[0]), .d9_in(dipswitch_1_sw4[1]),
    .d10_in(dipswitch_1_sw4[2]), .d11_in(dipswitch_1_sw4[3]), .bus_avail(mos_6561_1_bus_avail),
    .r_w(multiplexer_1_out), .d7_out(mos_6561_1_d0_out[7]), .d6_out(mos_6561_1_d0_out[6]),
    .d5_out(mos_6561_1_d0_out[5]), .d4_out(mos_6561_1_d0_out[4]), .d3_out(mos_6561_1_d0_out[3]),
    .d2_out(mos_6561_1_d0_out[2]), .d1_out(mos_6561_1_d0_out[1]), .d0_out(mos_6561_1_d0_out[0]));  // open: a4_in, a5_in, a6_in, a7_in, a8_out, a9_out, a10_out, a11_out, a12_out, a13_out, a7_out, a6_out, a5_out, a4_out, a3_out, a2_out, a1_out, a0_out, d11_out, d10_out, d9_out, d8_out
  assign controlled_buffer_3_out = mos_6561_1_clk_out_2 ? dipswitch_4_sw4 : 4'bz;  // Controlled_Buffer controlled_buffer_3
  Clock sysclk ();  // open: out
  Clock #(.highDuration(2), .lowDuration(2)) clk (.out(clk_out));
  DipSwitch #(.number(4)) dipswitch_4 (
    .sw1(dipswitch_4_sw4[3]), .sw2(dipswitch_4_sw4[2]), .sw3(dipswitch_4_sw4[1]), .sw4(dipswitch_4_sw4[0]));
endmodule

module Pass_Transistor (
  input  in_1,
  input  in_2,
  output out_3
);

  Register #(.width(1)) register_1 (.D(in_1), .en(1'b1), .clk(in_2), .Q(out_3));  // open: clr
endmodule

module Pass_Transistor_2 (
  input  IN,
  input  CLEAR,
  input  in_3,
  input  PRESET,
  output OUT
);

  D_Flip_Flop d_ff_1 (.D(IN), .clk(in_3), .Q(OUT), .preset(PRESET), .reset(CLEAR));  // open: Qn
endmodule

module Pass_Transistor_3 (
  input  IN,
  input  in_2,
  input  SET,
  output OUT
);

  wire controlled_buffer_1_out, controlled_buffer_2_out, not_1_out;

  not not_1 (not_1_out, SET);
  assign controlled_buffer_1_out = SET ? SET : 1'bz;  // Controlled_Buffer controlled_buffer_1
  assign controlled_buffer_2_out = not_1_out ? not_1_out : 1'bz;  // Controlled_Buffer controlled_buffer_2
  D_Flip_Flop d_ff_1 (
    .clk(in_2), .D(IN), .Q(OUT), .preset(controlled_buffer_1_out), .reset(controlled_buffer_2_out));  // open: Qn
endmodule

module Clock_Generator (
  input  clk_in_1,
  input  i_ext_reset,
  output mem_clk_1,
  output mem_clk_2,
  output in1,
  output in2,
  output f2,
  output f1
);

  wire nand_1_out, nand_2_out, nor_1_out, nor_2_out, nor_3_out, nor_4_out, nor_5_out, nor_6_out, nor_7_out,
       nor_8_out, nor_9_out, not_1_out, not_3_out, not_4_out, not_6_out, not_7_out, not_10_out, not_11_out,
       not_12_out, not_13_out, not_14_out, not_15_out, not_16_out, not_17_out, not_18_out, not_19_out,
       or_1_out, pass_transistor_1_out_3, pass_transistor_2_out_3, pass_transistor_3_out_3,
       pass_transistor_4_out_3, pass_transistor_5_out_3, pass_transistor_6_out_3, transistor_1_out;

  nor nor_1 (nor_1_out, nor_4_out, f1);
  not not_1 (not_1_out, nor_1_out);
  not not_2 (f2, not_1_out);
  not not_3 (not_3_out, nor_4_out);
  nor nor_2 (nor_2_out, f2, not_3_out);
  not not_4 (not_4_out, nor_2_out);
  not not_5 (f1, not_4_out);
  not not_6 (not_6_out, pass_transistor_1_out_3);
  Pass_Transistor pass_transistor_1 (.in_1(not_7_out), .out_3(pass_transistor_1_out_3), .in_2(not_16_out));
  not not_7 (not_7_out, i_ext_reset);
  Pass_Transistor pass_transistor_2 (.in_1(not_6_out), .out_3(pass_transistor_2_out_3), .in_2(not_15_out));
  not not_8 (mem_clk_1, not_10_out);
  not not_9 (mem_clk_2, not_11_out);
  nor nor_3 (nor_3_out, pass_transistor_2_out_3, i_ext_reset);
  not not_10 (not_10_out, nor_5_out);
  not not_11 (not_11_out, nor_6_out);
  nor nor_4 (nor_4_out, nor_3_out, pass_transistor_4_out_3);
  Pass_Transistor pass_transistor_3 (.in_1(nor_4_out), .out_3(pass_transistor_3_out_3), .in_2(not_15_out));
  nor nor_5 (nor_5_out, not_13_out, mem_clk_2);
  nor nor_6 (nor_6_out, mem_clk_1, not_12_out);
  Pass_Transistor pass_transistor_4 (.in_1(nand_1_out), .out_3(pass_transistor_4_out_3), .in_2(not_16_out));
  nand nand_1 (nand_1_out, nand_2_out, or_1_out);
  nand nand_2 (nand_2_out, pass_transistor_3_out_3, not_14_out);
  not not_12 (not_12_out, not_13_out);
  or or_1 (or_1_out, pass_transistor_3_out_3, not_14_out);
  Pass_Transistor pass_transistor_5 (.in_1(nor_7_out), .out_3(pass_transistor_5_out_3), .in_2(not_16_out));
  nor nor_7 (nor_7_out, nor_3_out, not_14_out);
  not not_13 (not_13_out, pass_transistor_5_out_3);
  not not_14 (not_14_out, pass_transistor_6_out_3);
  Pass_Transistor pass_transistor_6 (.in_1(not_13_out), .out_3(pass_transistor_6_out_3), .in_2(not_15_out));
  not not_15 (not_15_out, not_17_out);
  not not_16 (not_16_out, not_18_out);
  nor nor_8 (nor_8_out, not_19_out, not_16_out);
  not not_17 (not_17_out, nor_8_out);
  not not_18 (not_18_out, nor_9_out);
  nor nor_9 (nor_9_out, not_15_out, clk_in_1);
  not not_19 (not_19_out, clk_in_1);
  Transistor #(.\type ("n")) transistor_1 (.in(1'b1), .out(transistor_1_out), .gate(not_15_out));
  Transistor #(.\type ("n")) transistor_2 (.in(1'b0), .out(transistor_1_out), .gate(not_16_out));
  not not_20 (in2, transistor_1_out);

  assign in1 = clk_in_1;
endmodule

module Vertical_Counter (
  input  i_half_ena,
  input  f2,
  input  vc_enable,
  input  vc_reset,
  input  vc_inc,
  output hl,
  output i_hl,
  output [8:0] vc,
  output [8:0] i_vc
);

  J_K_Flip_Flop vc_in (.J(1'b1), .K(1'b1), .clk(vc_enable), .Q(vc[0]), .Qn(i_vc[0]), .reset(vc_reset));  // open: preset
  J_K_Flip_Flop j_k_ff_1 (
    .J(1'b1), .K(1'b1), .clk(i_vc[0]), .Q(vc[1]), .Qn(i_vc[1]), .reset(vc_reset));  // open: preset
  J_K_Flip_Flop j_k_ff_2 (
    .J(1'b1), .K(1'b1), .clk(i_vc[1]), .Q(vc[2]), .Qn(i_vc[2]), .reset(vc_reset));  // open: preset
  J_K_Flip_Flop j_k_ff_3 (
    .J(1'b1), .K(1'b1), .clk(i_vc[2]), .Q(vc[3]), .Qn(i_vc[3]), .reset(vc_reset));  // open: preset
  J_K_Flip_Flop j_k_ff_4 (
    .J(1'b1), .K(1'b1), .clk(i_vc[3]), .Q(vc[4]), .Qn(i_vc[4]), .reset(vc_reset));  // open: preset
  J_K_Flip_Flop j_k_ff_5 (
    .J(1'b1), .K(1'b1), .clk(i_vc[4]), .Q(vc[5]), .Qn(i_vc[5]), .reset(vc_reset));  // open: preset
  J_K_Flip_Flop j_k_ff_6 (
    .J(1'b1), .K(1'b1), .clk(i_vc[5]), .Q(vc[6]), .Qn(i_vc[6]), .reset(vc_reset));  // open: preset
  J_K_Flip_Flop j_k_ff_7 (
    .J(1'b1), .K(1'b1), .clk(i_vc[6]), .Q(vc[7]), .Qn(i_vc[7]), .reset(vc_reset));  // open: preset
  J_K_Flip_Flop j_k_ff_8 (
    .J(1'b1), .K(1'b1), .clk(i_vc[7]), .Q(vc[8]), .Qn(i_vc[8]), .reset(vc_reset));  // open: preset
endmodule

module Horizontal_Counter (
  input  hc_reset,
  input  hc_inc,
  input  f2,
  output [7:0] hc,
  output [7:0] i_hc
);

  Counter counter_1 (.clr(hc_reset), .load(1'b0), .up(1'b1), .count(1'b1), .clk(hc_inc), .Q(hc));  // open: D, carry
  assign i_hc = ~hc;  // NOT_Gate not_1, 8 bits wide
endmodule

module X_Decoder (
  input  [7:0] hc,
  input  [7:0] i_hc,
  input  f1,
  input  f2,
  output col_brst,
  output h_blank,
  output x_35,
  output x_0,
  output h_sync,
  output x_70,
  output v_sync_pulse
);

  wire cb7_out, cb11_out, hb12_out, hb70_out, hs1_out, hs6_out, or_1_out, or_2_out, or_3_out, or_4_out,
       or_5_out, or_6_out, x_2_out, x_6_out, x_38_out, x_41_out;

  nor cb11 (cb11_out, i_hc[3], i_hc[0], i_hc[1], hc[7], hc[5], hc[2], hc[6], hc[4], f1);
  or or_1 (or_1_out, cb7_out, cb11_out);
  nor cb7 (cb7_out, i_hc[2], i_hc[0], i_hc[1], hc[7], hc[5], hc[4], hc[3], hc[6]);
  nor hb12 (hb12_out, i_hc[3], i_hc[2], hc[1], hc[7], hc[0], hc[5], hc[4], hc[6], f1);
  or or_2 (or_2_out, hb70_out, hb12_out);
  nor hb70 (hb70_out, i_hc[2], i_hc[1], hc[7], i_hc[6], hc[0], hc[5], hc[4], hc[3]);
  nor nor_1 (x_35, i_hc[0], i_hc[1], hc[7], i_hc[5], hc[2], hc[4], hc[3], hc[6]);
  nor nor_2 (x_0, hc[1], hc[7], hc[2], hc[0], hc[5], hc[4], hc[3], hc[6]);
  nor hs1 (hs1_out, hc[1], i_hc[0], hc[7], hc[2], hc[5], hc[4], hc[3], hc[6]);
  or or_3 (or_3_out, hs1_out, hs6_out);
  nor hs6 (hs6_out, i_hc[2], i_hc[1], hc[7], hc[0], hc[5], hc[4], hc[3], hc[6]);
  nor nor_3 (x_70, i_hc[2], i_hc[1], hc[7], i_hc[6], hc[0], hc[5], hc[4], hc[3]);
  nor x_41 (x_41_out, i_hc[3], hc[1], i_hc[0], hc[7], i_hc[5], hc[2], hc[4], hc[6]);
  or or_4 (or_4_out, x_41_out, x_6_out);
  nor x_6 (x_6_out, i_hc[2], i_hc[1], hc[7], hc[0], hc[5], hc[4], hc[3], hc[6]);
  nor x_2 (x_2_out, i_hc[1], hc[7], hc[2], hc[0], hc[5], hc[4], hc[3], hc[6], f2);
  or or_5 (or_5_out, x_2_out, x_38_out);
  nor x_38 (x_38_out, i_hc[2], i_hc[1], hc[7], i_hc[5], hc[0], hc[4], hc[3], hc[6], f1);
  S_R_Flip_Flop s_r_ff_1 (.S(cb7_out), .R(cb11_out), .clk(or_1_out), .Q(col_brst));  // open: reset, Qn, preset
  S_R_Flip_Flop s_r_ff_2 (.S(hb70_out), .R(hb12_out), .clk(or_2_out), .Q(h_blank));  // open: reset, Qn, preset
  S_R_Flip_Flop s_r_ff_3 (.S(hs1_out), .R(hs6_out), .clk(or_3_out), .Q(h_sync));  // open: reset, Qn, preset
  S_R_Flip_Flop s_r_ff_4 (.S(or_4_out), .R(or_5_out), .clk(or_6_out), .Q(v_sync_pulse));  // open: reset, Qn, preset
  or or_6 (or_6_out, or_4_out, or_5_out);
endmodule

module Horizontal_Reset (
  input  f1,
  input  x_70,
  input  f2,
  input  i_ext_reset,
  output hc_reset,
  output i_new_line,
  output hc_inc,
  output ext_reset
);

  wire nor_1_out, not_2_out, not_3_out, not_5_out, not_6_out, pass_transistor_1_out_3,
       pass_transistor_2_out_3, pass_transistor_3_out_3, pass_transistor_4_out_3;

  not not_1 (ext_reset, pass_transistor_1_out_3);
  Pass_Transistor pass_transistor_1 (.in_1(not_2_out), .out_3(pass_transistor_1_out_3), .in_2(f2));
  not not_2 (not_2_out, not_3_out);
  not not_3 (not_3_out, i_ext_reset);
  not not_4 (hc_reset, not_5_out);
  not not_5 (not_5_out, pass_transistor_2_out_3);
  Pass_Transistor pass_transistor_2 (.in_1(not_6_out), .out_3(pass_transistor_2_out_3), .in_2(f1));
  not not_6 (not_6_out, nor_1_out);
  nor nor_1 (nor_1_out, x_70, ext_reset);
  Pass_Transistor pass_transistor_3 (.in_1(hc_reset), .out_3(pass_transistor_3_out_3), .in_2(f2));
  Pass_Transistor pass_transistor_4 (.in_1(nor_1_out), .out_3(pass_transistor_4_out_3), .in_2(f1));
  not not_7 (i_new_line, pass_transistor_3_out_3);
  Multiplexer #(.enable("false")) multiplexer_1 (.in0(1'b0), .in1(f1), .out(hc_inc), .sel(pass_transistor_4_out_3));
  // Probe on pass_transistor_4_out_3
endmodule

module MOS_6561 (
  input  a0_in,
  input  d0_in,
  input  a1_in,
  input  d1_in,
  input  a2_in,
  input  d2_in,
  input  a3_in,
  input  d3_in,
  input  a4_in,
  input  d4_in,
  input  a5_in,
  input  d5_in,
  input  a6_in,
  input  d6_in,
  input  a7_in,
  input  d7_in,
  input  a8_in,
  input  d8_in,
  input  a9_in,
  input  d9_in,
  input  a10_in,
  input  d10_in,
  input  a11_in,
  input  d11_in,
  input  a12_in,
  input  a13_in,
  input  clk_in_1,
  input  i_ext_reset,
  input  r_w,
  output a0_out,
  output d0_out,
  output a1_out,
  output d1_out,
  output a2_out,
  output d2_out,
  output a3_out,
  output d3_out,
  output a4_out,
  output d4_out,
  output a5_out,
  output d5_out,
  output a6_out,
  output d6_out,
  output a7_out,
  output d7_out,
  output a8_out,
  output d8_out,
  output a9_out,
  output d9_out,
  output a10_out,
  output d10_out,
  output a11_out,
  output d11_out,
  output a12_out,
  output a13_out,
  output bus_avail,
  output clk_out_2,
  output clk_out_1
);

  wire address_out_enable_1_addr_out_ena, c_s_out, cell_depth_reset_1_cdc_enable, cell_depth_reset_1_cdc_inc,
       cell_depth_reset_1_cdc_reset, clock_generator_1_in1, clock_generator_1_in2,
       clock_generator_1_mem_clk_1, clock_generator_1_mem_clk_2, cr0_1_int, cr3_1_double,
       data_in_out_control_1_dat_out_ena, data_in_out_control_1_i_dat_in_ena, data_in_out_control_1_i_read,
       data_in_out_control_1_i_write, horiz_cell_counter_1_hcc_last, horizontal_reset_1_ext_reset,
       horizontal_reset_1_hc_inc, horizontal_reset_1_hc_reset, horizontal_reset_1_i_new_line, not_1_out,
       not_2_out, sx_comparator_1_sx_cmp, sy_comparator_1_sy_cmp, vert_cell_counter_1_vcc_last,
       vertical_counter_1_hl, vertical_counter_1_i_hl, vertical_reset_1_i_half_ena,
       vertical_reset_1_last_line, vertical_reset_1_vc_enable, vertical_reset_1_vc_inc,
       vertical_reset_1_vc_reset, within_matrix_1_i_in_matrix, within_matrix_1_i_mtrx_line,
       x_decoder_1_col_brst, x_decoder_1_h_blank, x_decoder_1_h_sync, x_decoder_1_v_sync_pulse,
       x_decoder_1_x_0, x_decoder_1_x_35, x_decoder_1_x_70, y_decoder_1_v_blank, y_decoder_1_v_sync,
       y_decoder_1_y_311, y_decoder_1_y_312;
  wire [3:0] cell_depth_counter_1_cdc, cell_depth_counter_1_i_cdc;
  wire [5:0] cr3_1_num_rows;
  wire [6:0] cr0_1_sx, cr2_1_num_cols;
  wire [7:0] cr0_1_data_out, cr1_1_sy, horizontal_counter_1_hc, horizontal_counter_1_i_hc;
  wire [8:0] vertical_counter_1_i_vc, vertical_counter_1_vc;

  not not_1 (not_1_out, a12_in);
  nor c_s (c_s_out, a13_in, not_1_out, a11_in, a10_in, a9_in, a8_in);
  // Probe on horizontal_counter_1_hc
  Horizontal_Counter horizontal_counter_1 (
    .i_hc(horizontal_counter_1_i_hc), .hc_reset(horizontal_reset_1_hc_reset), .hc(horizontal_counter_1_hc),
    .hc_inc(horizontal_reset_1_hc_inc), .f2(clk_out_2));
  Horizontal_Reset horizontal_reset_1 (
    .f1(clk_out_1), .f2(clk_out_2), .hc_inc(horizontal_reset_1_hc_inc), .x_70(x_decoder_1_x_70),
    .hc_reset(horizontal_reset_1_hc_reset), .i_ext_reset(i_ext_reset),
    .ext_reset(horizontal_reset_1_ext_reset), .i_new_line(horizontal_reset_1_i_new_line));
  Clock_Generator clock_generator_1 (
    .f2(clk_out_2), .in2(clock_generator_1_in2), .in1(clock_generator_1_in1),
    .mem_clk_2(clock_generator_1_mem_clk_2), .mem_clk_1(clock_generator_1_mem_clk_1),
    .i_ext_reset(i_ext_reset), .clk_in_1(clk_in_1), .f1(clk_out_1));
  // Probe on cr0_1_data_out
  LED led_1 (.in(clock_generator_1_in1));
  LED led_2 (.in(clock_generator_1_in2));
  LED led_3 (.in(clock_generator_1_mem_clk_1));
  LED led_4 (.in(clock_generator_1_mem_clk_2));
  CR0 cr0_1 (
    .sx(cr0_1_sx), .i_write(data_in_out_control_1_i_write), .i_read(data_in_out_control_1_i_read),
    .data_in(cr0_1_data_out), .address({a3_in, a2_in, a1_in, a0_in}), .\int (cr0_1_int),
    .data_out(cr0_1_data_out));
  SX_Comparator sx_comparator_1 (.sx_cmp(sx_comparator_1_sx_cmp), .hc(horizontal_counter_1_hc), .sx(cr0_1_sx));
  X_Decoder x_decoder_1 (
    .h_sync(x_decoder_1_h_sync), .col_brst(x_decoder_1_col_brst), .hc(horizontal_counter_1_hc),
    .f2(clk_out_2), .x_0(x_decoder_1_x_0), .h_blank(x_decoder_1_h_blank), .i_hc(horizontal_counter_1_i_hc),
    .f1(clk_out_1), .x_35(x_decoder_1_x_35), .x_70(x_decoder_1_x_70), .v_sync_pulse(x_decoder_1_v_sync_pulse));
  Vertical_Reset vertical_reset_1 (
    .vc_inc(vertical_reset_1_vc_inc), .ext_reset(horizontal_reset_1_ext_reset),
    .vc_enable(vertical_reset_1_vc_enable), .y_312(y_decoder_1_y_312), .vc_reset(vertical_reset_1_vc_reset),
    .x_35(x_decoder_1_x_35), .last_line(vertical_reset_1_last_line), .y_311(y_decoder_1_y_311),
    .x_0(x_decoder_1_x_0), .i_half_ena(vertical_reset_1_i_half_ena), .f1(clk_out_1), .f2(clk_out_2));
  LED led_5 (.in(x_decoder_1_col_brst));
  LED led_6 (.in(x_decoder_1_h_blank));
  LED led_7 (.in(x_decoder_1_h_sync));
  // Probe on vertical_counter_1_vc
  CR1 cr1_1 (
    .data_out(cr0_1_data_out), .data_in(cr0_1_data_out), .i_write(data_in_out_control_1_i_write),
    .i_read(data_in_out_control_1_i_read), .address({a3_in, a2_in, a1_in, a0_in}), .sy(cr1_1_sy));
  // Probe on cr1_1_sy
  SY_Comparator sy_comparator_1 (.sy_cmp(sy_comparator_1_sy_cmp), .vc(vertical_counter_1_vc), .sy(cr1_1_sy));
  Y_Decoder y_decoder_1 (
    .hl(vertical_counter_1_hl), .\int (cr0_1_int), .i_hl(vertical_counter_1_i_hl), .y_311(y_decoder_1_y_311),
    .v_sync_pulse(x_decoder_1_v_sync_pulse), .i_vc(vertical_counter_1_i_vc), .vc(vertical_counter_1_vc),
    .v_blank(y_decoder_1_v_blank), .y_312(y_decoder_1_y_312), .v_sync(y_decoder_1_v_sync));
  LED led_8 (.in(y_decoder_1_v_blank));
  LED led_9 (.in(y_decoder_1_v_sync));
  Vertical_Counter vertical_counter_1 (
    .i_vc(vertical_counter_1_i_vc), .vc(vertical_counter_1_vc), .vc_enable(vertical_reset_1_vc_enable),
    .i_half_ena(vertical_reset_1_i_half_ena), .vc_reset(vertical_reset_1_vc_reset),
    .vc_inc(vertical_reset_1_vc_inc), .f2(clk_out_2), .hl(vertical_counter_1_hl),
    .i_hl(vertical_counter_1_i_hl));
  Cell_Depth_Reset cell_depth_reset_1 (
    .i_mtrx_line(within_matrix_1_i_mtrx_line), .i_new_line(horizontal_reset_1_i_new_line),
    .double(cr3_1_double), .cdc_enable(cell_depth_reset_1_cdc_enable), .i_cdc(cell_depth_counter_1_i_cdc),
    .f1(clk_out_1), .cdc_reset(cell_depth_reset_1_cdc_reset), .f2(clk_out_2),
    .cdc_inc(cell_depth_reset_1_cdc_inc));  // open: cdc_last
  // Probe on cell_depth_counter_1_cdc
  Cell_Depth_Counter cell_depth_counter_1 (
    .i_cdc(cell_depth_counter_1_i_cdc), .cdc(cell_depth_counter_1_cdc),
    .cdc_enable(cell_depth_reset_1_cdc_enable), .cdc_reset(cell_depth_reset_1_cdc_reset),
    .cdc_inc(cell_depth_reset_1_cdc_inc), .f2(clk_out_2));
  CR3 cr3_1 (
    .data_in(cr0_1_data_out), .double(cr3_1_double), .i_read(data_in_out_control_1_i_read),
    .data_out(cr0_1_data_out), .address({a3_in, a2_in, a1_in, a0_in}),
    .i_write(data_in_out_control_1_i_write), .num_rows(cr3_1_num_rows));
  Vert_Cell_Counter vert_cell_counter_1 (
    .num_rows(cr3_1_num_rows), .cdc_reset(cell_depth_reset_1_cdc_reset),
    .vcc_last(vert_cell_counter_1_vcc_last), .f2(clk_out_2), .f1(clk_out_1),
    .last_line(vertical_reset_1_last_line));
  Within_Matrix within_matrix_1 (
    .i_mtrx_line(within_matrix_1_i_mtrx_line), .hcc_last(horiz_cell_counter_1_hcc_last), .f1(clk_out_1),
    .i_new_line(horizontal_reset_1_i_new_line), .f2(clk_out_2), .last_line(vertical_reset_1_last_line),
    .sy_cmp(sy_comparator_1_sy_cmp), .vcc_last(vert_cell_counter_1_vcc_last),
    .sx_cmp(sx_comparator_1_sx_cmp), .bus_avail(bus_avail), .i_in_matrix(within_matrix_1_i_in_matrix));
  Address_Out_Enable address_out_enable_1 (
    .f2(clk_out_2), .i_in_matrix(within_matrix_1_i_in_matrix), .f1(clk_out_1),
    .addr_out_ena(address_out_enable_1_addr_out_ena));
  CR2 cr2_1 (
    .data_in(cr0_1_data_out), .num_cols(cr2_1_num_cols), .i_read(data_in_out_control_1_i_read),
    .data_out(cr0_1_data_out), .address({a3_in, a2_in, a1_in, a0_in}), .i_write(data_in_out_control_1_i_write));  // open: bv9
  Horiz_Cell_Counter horiz_cell_counter_1 (
    .i_new_line(horizontal_reset_1_i_new_line), .i_in_matrix(within_matrix_1_i_in_matrix),
    .num_cols(cr2_1_num_cols), .f1(clk_out_1), .f2(clk_out_2), .hcc_last(horiz_cell_counter_1_hcc_last));  // open: hcc0
  Data_In_Out_Control data_in_out_control_1 (
    .read_write(r_w), .i_write(data_in_out_control_1_i_write), .f1(clk_out_1),
    .i_read(data_in_out_control_1_i_read), .chip_select(c_s_out),
    .dat_out_ena(data_in_out_control_1_dat_out_ena), .i_dat_in_ena(data_in_out_control_1_i_dat_in_ena));
  Multiplexer #(.width(8), .disabled("Z"), .enable("false")) multiplexer_1 (
    .in1(cr0_1_data_out), .out({d7_out, d6_out, d5_out, d4_out, d3_out, d2_out, d1_out, d0_out}),
    .sel(data_in_out_control_1_dat_out_ena));  // open: in0
  Multiplexer #(.width(8), .disabled("Z"), .enable("false")) multiplexer_2 (
    .in1({d7_in, d6_in, d5_in, d4_in, d3_in, d2_in, d1_in, d0_in}), .out(cr0_1_data_out), .sel(not_2_out));  // open: in0
  not not_2 (not_2_out, data_in_out_control_1_i_dat_in_ena);
endmodule

module Vertical_Reset (
  input  y_311,
  input  y_312,
  input  ext_reset,
  input  x_35,
  input  x_0,
  input  f1,
  input  f2,
  output vc_reset,
  output vc_inc,
  output vc_enable,
  output last_line,
  output i_half_ena
);

  wire multiplexer_1_out, multiplexer_2_out, nor_1_out, nor_2_out, nor_4_out, not_3_out, not_5_out,
       not_6_out, pass_transistor_1_out_3, pass_transistor_2_out_3, pass_transistor_3_out_3,
       pass_transistor_4_out_3, pass_transistor_5_out_3, pass_transistor_6_out_3, transistor_1_out;

  Multiplexer #(.enable("false")) multiplexer_1 (.in0(1'b0), .in1(nor_1_out), .out(multiplexer_1_out), .sel(f1));
  not not_1 (i_half_ena, multiplexer_1_out);
  nor nor_1 (nor_1_out, transistor_1_out, last_line);
  Pass_Transistor pass_transistor_1 (.in_1(y_311), .out_3(pass_transistor_1_out_3), .in_2(f1));
  Pass_Transistor pass_transistor_2 (.in_1(y_312), .out_3(pass_transistor_2_out_3), .in_2(f1));
  nor nor_2 (nor_2_out, pass_transistor_1_out_3, pass_transistor_2_out_3, pass_transistor_4_out_3);
  Pass_Transistor pass_transistor_3 (.in_1(nor_2_out), .out_3(pass_transistor_3_out_3), .in_2(f2));
  not not_2 (last_line, pass_transistor_3_out_3);
  Pass_Transistor pass_transistor_4 (.in_1(ext_reset), .out_3(pass_transistor_4_out_3), .in_2(f1));
  Transistor #(.\type ("n")) transistor_1 (.in(1'b0), .out(transistor_1_out), .gate(pass_transistor_4_out_3));
  nor nor_3 (transistor_1_out, x_35, x_0);
  not not_3 (not_3_out, pass_transistor_5_out_3);
  Pass_Transistor pass_transistor_5 (.in_1(nor_4_out), .out_3(pass_transistor_5_out_3), .in_2(f1));
  nor nor_4 (nor_4_out, transistor_1_out, pass_transistor_3_out_3);
  not not_4 (vc_reset, not_3_out);
  not not_5 (not_5_out, nor_4_out);
  Pass_Transistor pass_transistor_6 (.in_1(not_5_out), .out_3(pass_transistor_6_out_3), .in_2(f2));
  not not_6 (not_6_out, x_0);
  Multiplexer #(.enable("false")) multiplexer_2 (.in0(1'b0), .in1(not_6_out), .out(multiplexer_2_out), .sel(f1));
  Multiplexer #(.enable("false")) multiplexer_3 (.in0(1'b0), .in1(f1), .out(vc_inc), .sel(pass_transistor_6_out_3));
  // Probe on x_0
  // Probe on not_6_out
  // Probe on multiplexer_2_out
  nor nor_5 (vc_enable, multiplexer_2_out, i_half_ena);

  // Notes on the sheet:
  //   X != 0,35
  //   WHEN NOT LAST LINE
endmodule

module Y_Decoder (
  input  \int ,
  input  [8:0] i_vc,
  input  i_hl,
  input  hl,
  input  [8:0] vc,
  input  v_sync_pulse,
  output v_blank,
  output y_311,
  output y_312,
  output v_sync
);

  wire and_1_out, multiplexer_1_out, not_1_out, not_2_out, or_1_out, or_2_out, s_r_ff_2_qn, y_1_out, y_4_out,
       y_7_out, y_10_out;

  not not_1 (not_1_out, \int );
  nor y_1 (y_1_out, i_vc[0], vc[1], vc[2], vc[3], vc[4], vc[5], vc[6], vc[7], vc[8]);
  nor y_10 (y_10_out, vc[0], i_vc[1], vc[2], i_vc[3], vc[4], vc[5], vc[6], vc[7], vc[8]);
  // NOR_Gate nor_1 is placed but not wired
  nor y_4 (y_4_out, vc[0], vc[1], i_vc[2], vc[3], vc[4], vc[5], vc[6], vc[7], vc[8]);
  not not_2 (not_2_out, v_sync_pulse);
  nor y_7 (y_7_out, i_vc[0], i_vc[1], i_vc[2], vc[3], vc[4], vc[5], vc[6], vc[7], vc[8]);
  nor nor_2 (y_311, i_vc[0], i_vc[1], i_vc[2], vc[3], i_vc[4], i_vc[5], vc[6], vc[7], i_vc[8]);
  nor nor_3 (y_312, vc[0], vc[1], vc[2], i_vc[3], i_vc[4], i_vc[5], vc[6], vc[7], i_vc[8], \int , not_1_out);
  S_R_Flip_Flop s_r_ff_1 (.S(y_1_out), .R(y_10_out), .clk(or_1_out), .Q(v_blank));  // open: reset, Qn, preset
  or or_1 (or_1_out, y_1_out, y_10_out);
  and and_1 (and_1_out, y_4_out, not_2_out);
  S_R_Flip_Flop s_r_ff_2 (.S(and_1_out), .R(y_7_out), .clk(or_2_out), .Qn(s_r_ff_2_qn));  // open: Q, reset, preset
  or or_2 (or_2_out, and_1_out, y_7_out);
  Multiplexer #(.enable("false")) multiplexer_1 (
    .in0(1'b1), .in1(s_r_ff_2_qn), .out(multiplexer_1_out), .sel(v_sync_pulse));
  not not_3 (v_sync, multiplexer_1_out);
endmodule

module SX_Comparator (
  input  [6:0] sx,
  input  [7:0] hc,
  output sx_cmp
);

  Comparator #(.width(7), .mode("unsigned")) comparator_1 (.a(sx), .b(hc[6:0]), .eq(sx_cmp));  // open: gt, lt
endmodule

module SY_Comparator (
  input  [7:0] sy,
  input  [8:0] vc,
  output sy_cmp
);

  Comparator comparator_1 (.a(sy), .b(vc[8:1]), .eq(sy_cmp));  // open: gt, lt
endmodule

module Cell_Depth_Counter (
  input  cdc_reset,
  input  cdc_enable,
  input  cdc_inc,
  input  f2,
  output [3:0] cdc,
  output [3:0] i_cdc
);

  Counter #(.width(4), .max('hf)) counter_1 (
    .clr(cdc_reset), .load(1'b0), .up(1'b1), .count(cdc_enable), .clk(cdc_inc), .Q(cdc));  // open: D, carry
  assign i_cdc = ~cdc;  // NOT_Gate not_1, 4 bits wide
endmodule

module Cell_Depth_Reset (
  input  double,
  input  [3:0] i_cdc,
  input  i_new_line,
  input  f1,
  input  f2,
  input  i_mtrx_line,
  output cdc_last,
  output cdc_reset,
  output cdc_inc,
  output cdc_enable
);

  wire and_1_out, and_2_out, and_3_out, and_4_out, nand_1_out, not_1_out, not_2_out, not_3_out, not_4_out,
       not_5_out, not_6_out, not_7_out, or_1_out, or_2_out, or_3_out, pass_transistor_1_out_3,
       pass_transistor_2_out_3, pass_transistor_3_out_3, pass_transistor_4_out_3;

  not not_1 (not_1_out, i_cdc[3]);
  not not_2 (not_2_out, i_cdc[2]);
  not not_3 (not_3_out, i_cdc[1]);
  not not_4 (not_4_out, i_cdc[0]);
  Multiplexer #(.enable("false")) multiplexer_1 (.in0(1'b0), .in1(f1), .out(cdc_inc), .sel(pass_transistor_1_out_3));
  Pass_Transistor pass_transistor_1 (.in_1(cdc_reset), .out_3(pass_transistor_1_out_3), .in_2(f2));
  nor nor_1 (cdc_enable, pass_transistor_2_out_3, cdc_reset, pass_transistor_3_out_3);
  not not_5 (not_5_out, double);
  Pass_Transistor pass_transistor_2 (.in_1(not_7_out), .out_3(pass_transistor_2_out_3), .in_2(f1));
  not not_6 (not_6_out, i_new_line);
  not not_7 (not_7_out, not_6_out);
  or or_1 (or_1_out, double, not_5_out);
  or or_2 (or_2_out, double, not_5_out);
  or or_3 (or_3_out, double, not_5_out);
  nand nand_1 (nand_1_out, cdc_last, not_6_out);
  Pass_Transistor pass_transistor_3 (.in_1(i_mtrx_line), .out_3(pass_transistor_3_out_3), .in_2(f1));
  and and_1 (and_1_out, double, not_1_out);
  and and_2 (and_2_out, or_1_out, not_2_out);
  and and_3 (and_3_out, or_2_out, not_3_out);
  and and_4 (and_4_out, or_3_out, not_4_out);
  not not_8 (cdc_reset, pass_transistor_4_out_3);
  Pass_Transistor pass_transistor_4 (.in_1(nand_1_out), .out_3(pass_transistor_4_out_3), .in_2(f1));
  nor nor_2 (cdc_last, and_1_out, and_2_out, and_3_out, and_4_out);
endmodule

module Within_Matrix (
  input  sy_cmp,
  input  last_line,
  input  vcc_last,
  input  sx_cmp,
  input  hcc_last,
  input  i_new_line,
  input  f2,
  input  f1,
  output i_mtrx_line,
  output bus_avail,
  output i_in_matrix
);

  wire and_1_out, in_matrix_q, in_matrix_y_q, in_matrix_y_qn, nor_1_out, not_1_out, not_2_out, not_3_out,
       not_4_out, not_5_out, not_6_out, not_8_out, not_9_out, not_10_out, or_1_out, or_2_out, or_3_out,
       or_4_out, or_5_out, pass_transistor_1_out_3, pass_transistor_2_out_3, pass_transistor_3_out_3,
       pass_transistor_4_out_3, pass_transistor_5_out_3, pass_transistor_6_out_3, pass_transistor_7_out_3,
       pass_transistor_8_out_3, pass_transistor_9_out_3;

  Pass_Transistor pass_transistor_1 (.in_1(sy_cmp), .out_3(pass_transistor_1_out_3), .in_2(f1));
  Pass_Transistor pass_transistor_2 (.in_1(sx_cmp), .out_3(pass_transistor_2_out_3), .in_2(f1));
  Pass_Transistor pass_transistor_3 (.in_1(not_1_out), .out_3(pass_transistor_3_out_3), .in_2(f2));
  not not_1 (not_1_out, pass_transistor_1_out_3);
  not not_2 (not_2_out, pass_transistor_2_out_3);
  Pass_Transistor pass_transistor_4 (.in_1(not_2_out), .out_3(pass_transistor_4_out_3), .in_2(f2));
  not not_3 (not_3_out, i_new_line);
  not not_4 (not_4_out, pass_transistor_3_out_3);
  or or_1 (or_1_out, last_line, vcc_last);
  not not_5 (not_5_out, pass_transistor_4_out_3);
  or or_2 (or_2_out, hcc_last, not_3_out);
  Pass_Transistor pass_transistor_5 (.in_1(not_8_out), .out_3(pass_transistor_5_out_3), .in_2(f2));
  not not_6 (not_6_out, pass_transistor_5_out_3);
  and and_1 (and_1_out, in_matrix_y_q, not_5_out);
  not not_7 (bus_avail, pass_transistor_6_out_3);
  Pass_Transistor pass_transistor_6 (.in_1(not_6_out), .out_3(pass_transistor_6_out_3), .in_2(f1));
  S_R_Flip_Flop in_matrix_y (
    .S(not_4_out), .R(or_1_out), .clk(or_3_out), .Q(in_matrix_y_q), .Qn(in_matrix_y_qn));  // open: reset, preset
  or or_3 (or_3_out, not_4_out, or_1_out);
  S_R_Flip_Flop in_matrix (.S(and_1_out), .R(or_2_out), .clk(or_4_out), .Q(in_matrix_q));  // open: reset, Qn, preset
  or or_4 (or_4_out, and_1_out, or_2_out);
  Pass_Transistor pass_transistor_7 (.in_1(bus_avail), .out_3(pass_transistor_7_out_3), .in_2(f2));
  Pass_Transistor pass_transistor_8 (.in_1(in_matrix_q), .out_3(pass_transistor_8_out_3), .in_2(f1));
  not not_8 (not_8_out, pass_transistor_8_out_3);
  not not_9 (not_9_out, pass_transistor_7_out_3);
  Pass_Transistor pass_transistor_9 (.in_1(not_9_out), .out_3(pass_transistor_9_out_3), .in_2(f1));
  S_R_Flip_Flop matrix_line (
    .S(in_matrix_q), .R(in_matrix_y_qn), .clk(or_5_out), .Qn(i_mtrx_line));  // open: Q, reset, preset
  or or_5 (or_5_out, in_matrix_q, in_matrix_y_qn);
  not not_10 (not_10_out, pass_transistor_9_out_3);
  nor nor_1 (nor_1_out, not_8_out, not_10_out);
  not not_11 (i_in_matrix, nor_1_out);
endmodule

module Horiz_Cell_Counter (
  input  i_new_line,
  input  i_in_matrix,
  input  f1,
  input  f2,
  input  [6:0] num_cols,
  output hcc0,
  output hcc_last
);

  wire multiplexer_1_out, not_1_out, pass_transistor_1_out_3, pass_transistor_2_out_3;
  wire [6:0] not_2_out;
  wire [7:1] counter_1_q;

  Pass_Transistor pass_transistor_1 (.in_1(i_new_line), .out_3(pass_transistor_1_out_3), .in_2(f1));
  Pass_Transistor pass_transistor_2 (.in_1(i_new_line), .out_3(pass_transistor_2_out_3), .in_2(f2));
  not not_1 (not_1_out, pass_transistor_1_out_3);
  Multiplexer #(.enable("false")) multiplexer_1 (
    .in0(f1), .in1(1'b0), .out(multiplexer_1_out), .sel(pass_transistor_2_out_3));
  assign not_2_out = ~num_cols;  // NOT_Gate not_2, 7 bits wide
  Counter counter_1 (
    .clr(1'b0), .load(not_1_out), .up(1'b1), .count(i_in_matrix), .clk(multiplexer_1_out),
    .D({not_2_out, 1'b0}), .Q({counter_1_q, hcc0}));  // open: carry
  nor nor_1 (hcc_last, hcc0, counter_1_q[1], counter_1_q[2], counter_1_q[3], counter_1_q[4], counter_1_q[5], counter_1_q[6], counter_1_q[7], 1'b0);
endmodule

module CR0 (
  input  [7:0] data_in,
  input  i_read,
  input  [3:0] address,
  input  i_write,
  output [7:0] data_out,
  output [6:0] sx,
  output \int 
);

  wire nor_1_out, nor_2_out, nor_3_out, not_1_out;
  wire [7:0] multiplexer_2_out;

  nor nor_1 (nor_1_out, i_read, not_1_out);
  Multiplexer #(.width(8), .disabled("Z"), .enable("false")) multiplexer_1 (
    .in1({\int , sx}), .out(data_out), .sel(nor_1_out));  // open: in0
  nor nor_2 (nor_2_out, 1'b0, address[3], address[2], address[1], address[0]);
  not not_1 (not_1_out, nor_2_out);
  nor nor_3 (nor_3_out, not_1_out, i_write);
  Register #(.trigger("high")) register_1 (
    .D(multiplexer_2_out), .en(nor_3_out), .clk(nor_3_out), .Q({\int , sx}));  // open: clr
  // Probe on multiplexer_2_out
  Multiplexer #(.width(8), .disabled("Z"), .enable("false")) multiplexer_2 (
    .in1(data_in), .out(multiplexer_2_out), .sel(nor_3_out));  // open: in0
endmodule

module CR1 (
  input  [7:0] data_in,
  input  i_read,
  input  [3:0] address,
  input  i_write,
  output [7:0] data_out,
  output [7:0] sy
);

  wire nor_1_out, nor_2_out, nor_3_out, not_1_out, not_2_out;
  wire [7:0] multiplexer_2_out;

  nor nor_1 (nor_1_out, i_read, not_2_out);
  Multiplexer #(.width(8), .disabled("Z"), .enable("false")) multiplexer_1 (
    .in1(sy), .out(data_out), .sel(nor_1_out));  // open: in0
  not not_1 (not_1_out, address[0]);
  nor nor_2 (nor_2_out, 1'b0, address[3], address[2], address[1], not_1_out);
  not not_2 (not_2_out, nor_2_out);
  nor nor_3 (nor_3_out, not_2_out, i_write);
  Register #(.trigger("high")) register_1 (
    .D(multiplexer_2_out), .en(nor_3_out), .clk(nor_3_out), .Q(sy));  // open: clr
  Multiplexer #(.width(8), .disabled("Z"), .enable("false")) multiplexer_2 (
    .in1(data_in), .out(multiplexer_2_out), .sel(nor_3_out));  // open: in0
endmodule

module CR2 (
  input  [7:0] data_in,
  input  i_read,
  input  [3:0] address,
  input  i_write,
  output [7:0] data_out,
  output [6:0] num_cols,
  output bv9
);

  wire nor_1_out, nor_2_out, nor_3_out, not_1_out, not_2_out;
  wire [7:0] multiplexer_2_out;

  nor nor_1 (nor_1_out, i_read, not_2_out);
  Multiplexer #(.width(8), .disabled("Z"), .enable("false")) multiplexer_1 (
    .in1({bv9, num_cols}), .out(data_out), .sel(nor_1_out));  // open: in0
  not not_1 (not_1_out, address[1]);
  nor nor_2 (nor_2_out, 1'b0, address[3], address[2], not_1_out, address[0]);
  not not_2 (not_2_out, nor_2_out);
  nor nor_3 (nor_3_out, not_2_out, i_write);
  Register #(.trigger("high")) register_1 (
    .D(multiplexer_2_out), .en(nor_3_out), .clk(nor_3_out), .Q({bv9, num_cols}));  // open: clr
  Multiplexer #(.width(8), .disabled("Z"), .enable("false")) multiplexer_2 (
    .in1(data_in), .out(multiplexer_2_out), .sel(nor_3_out));  // open: in0
endmodule

module CR3 (
  input  [7:0] data_in,
  input  i_read,
  input  [3:0] address,
  input  i_write,
  output [7:0] data_out,
  output double,
  output [5:0] num_rows
);

  wire nor_1_out, nor_2_out, nor_3_out, not_1_out, not_2_out, not_3_out;
  wire [7:0] multiplexer_2_out;
  wire [7:7] register_1_q;

  nor nor_1 (nor_1_out, i_read, not_3_out);
  Multiplexer #(.width(8), .disabled("Z"), .enable("false")) multiplexer_1 (
    .in1({register_1_q[7], num_rows, double}), .out(data_out), .sel(nor_1_out));  // open: in0
  not not_1 (not_1_out, address[0]);
  not not_2 (not_2_out, address[1]);
  nor nor_2 (nor_2_out, 1'b0, address[3], address[2], not_2_out, not_1_out);
  not not_3 (not_3_out, nor_2_out);
  nor nor_3 (nor_3_out, not_3_out, i_write);
  Register #(.trigger("high")) register_1 (
    .D(multiplexer_2_out), .en(nor_3_out), .clk(nor_3_out), .Q({register_1_q[7], num_rows, double}));  // open: clr
  Multiplexer #(.width(8), .disabled("Z"), .enable("false")) multiplexer_2 (
    .in1(data_in), .out(multiplexer_2_out), .sel(nor_3_out));  // open: in0
endmodule

module Vert_Cell_Counter (
  input  last_line,
  input  cdc_reset,
  input  f1,
  input  f2,
  input  [5:0] num_rows,
  output vcc_last
);

  wire multiplexer_1_out, nand_1_out, not_1_out, not_2_out, not_3_out, pass_transistor_1_out_3,
       pass_transistor_2_out_3;
  wire [5:0] counter_1_q, not_4_out;

  not not_1 (not_1_out, last_line);
  not not_2 (not_2_out, last_line);
  Pass_Transistor pass_transistor_1 (.in_1(not_2_out), .out_3(pass_transistor_1_out_3), .in_2(f2));
  Pass_Transistor pass_transistor_2 (.in_1(not_1_out), .out_3(pass_transistor_2_out_3), .in_2(f1));
  not not_3 (not_3_out, pass_transistor_2_out_3);
  nand nand_1 (nand_1_out, pass_transistor_2_out_3, cdc_reset);
  Multiplexer #(.enable("false")) multiplexer_1 (
    .in0(f1), .in1(1'b0), .out(multiplexer_1_out), .sel(pass_transistor_1_out_3));
  assign not_4_out = ~num_rows;  // NOT_Gate not_4, 6 bits wide
  Counter #(.width(6), .max('h3f)) counter_1 (
    .clr(1'b0), .load(not_3_out), .up(1'b1), .count(nand_1_out), .clk(multiplexer_1_out), .D(not_4_out),
    .Q(counter_1_q));  // open: carry
  nor nor_1 (vcc_last, counter_1_q[0], counter_1_q[1], counter_1_q[2], counter_1_q[3], counter_1_q[4], counter_1_q[5], 1'b0);
endmodule

module Address_Out_Enable (
  input  i_in_matrix,
  input  f1,
  input  f2,
  output addr_out_ena
);

  wire pass_transistor_1_out_3;

  Pass_Transistor pass_transistor_1 (.in_1(i_in_matrix), .out_3(pass_transistor_1_out_3), .in_2(f2));
  Multiplexer #(.enable("false")) multiplexer_1 (
    .in0(f1), .in1(1'b0), .out(addr_out_ena), .sel(pass_transistor_1_out_3));
endmodule

module Data_In_Out_Control (
  input  read_write,
  input  f1,
  input  chip_select,
  output dat_out_ena,
  output i_read,
  output i_write,
  output i_dat_in_ena
);

  wire nor_2_out, not_1_out, not_2_out;

  not not_1 (not_1_out, chip_select);
  not not_2 (not_2_out, read_write);
  nor nor_1 (dat_out_ena, not_2_out, f1, not_1_out);
  nor nor_2 (nor_2_out, read_write, f1, not_1_out);
  not not_3 (i_read, dat_out_ena);
  not not_4 (i_write, nor_2_out);
  nor nor_3 (i_dat_in_ena, nor_2_out, f1);
endmodule
