// Logisim project counter_from_flip_flops.circ as structural Verilog: 1 circuit, main circuit main
module main (
  input  in_1,
  input  in_2
);

  wire [8:0] j_k_ff_1_q, j_k_ff_1_qn;

  J_K_Flip_Flop j_k_ff_1 (
    .J(in_1), .K(in_1), .clk(in_1), .Q(j_k_ff_1_q[0]), .Qn(j_k_ff_1_qn[0]), .reset(in_2));  // open: preset
  J_K_Flip_Flop j_k_ff_2 (
    .J(in_1), .K(in_1), .clk(j_k_ff_1_qn[0]), .Q(j_k_ff_1_q[1]), .Qn(j_k_ff_1_qn[1]), .reset(in_2));  // open: preset
  J_K_Flip_Flop j_k_ff_3 (
    .J(in_1), .K(in_1), .clk(j_k_ff_1_qn[1]), .Q(j_k_ff_1_q[2]), .Qn(j_k_ff_1_qn[2]), .reset(in_2));  // open: preset
  J_K_Flip_Flop j_k_ff_4 (
    .J(in_1), .K(in_1), .clk(j_k_ff_1_qn[2]), .Q(j_k_ff_1_q[3]), .Qn(j_k_ff_1_qn[3]), .reset(in_2));  // open: preset
  // Probe on j_k_ff_1_q
  J_K_Flip_Flop j_k_ff_5 (
    .J(in_1), .K(in_1), .clk(j_k_ff_1_qn[3]), .Q(j_k_ff_1_q[4]), .Qn(j_k_ff_1_qn[4]), .reset(in_2));  // open: preset
  // Probe on j_k_ff_1_qn
  J_K_Flip_Flop j_k_ff_6 (
    .J(in_1), .K(in_1), .clk(j_k_ff_1_qn[4]), .Q(j_k_ff_1_q[5]), .Qn(j_k_ff_1_qn[5]), .reset(in_2));  // open: preset
  J_K_Flip_Flop j_k_ff_7 (
    .J(in_1), .K(in_1), .clk(j_k_ff_1_qn[5]), .Q(j_k_ff_1_q[6]), .Qn(j_k_ff_1_qn[6]), .reset(in_2));  // open: preset
  J_K_Flip_Flop j_k_ff_8 (
    .J(in_1), .K(in_1), .clk(j_k_ff_1_qn[6]), .Q(j_k_ff_1_q[7]), .Qn(j_k_ff_1_qn[7]), .reset(in_2));  // open: preset
  J_K_Flip_Flop j_k_ff_9 (
    .J(in_1), .K(in_1), .clk(j_k_ff_1_qn[7]), .Q(j_k_ff_1_q[8]), .Qn(j_k_ff_1_qn[8]), .reset(in_2));  // open: preset
endmodule
