// Logisim project incoming_outgoing_data.circ as structural Verilog: 1 circuit, main circuit main
module main (
  input  in_1,
  input  in_2,
  input  rw,
  input  cs,
  input  f1
);

  wire nor_1_out, nor_2_out, nor_3_out, nor_4_out, not_1_out, not_2_out, not_3_out, not_4_out, not_5_out,
       transistor_1_out;

  not not_1 (not_1_out, rw);
  not not_2 (not_2_out, cs);
  nor nor_1 (nor_1_out, f1, not_1_out, not_2_out);
  nor nor_2 (nor_2_out, nor_1_out, f1);
  not not_3 (not_3_out, in_2);
  not not_4 (not_4_out, not_3_out);
  not not_5 (not_5_out, not_4_out);
  nor nor_3 (nor_3_out, not_5_out, nor_2_out);
  nor nor_4 (nor_4_out, nor_2_out, not_4_out);
  Transistor #(.\type ("n")) transistor_1 (.in(1'b1), .out(transistor_1_out), .gate(nor_3_out));
  Transistor #(.\type ("n")) transistor_2 (.in(1'b0), .out(transistor_1_out), .gate(nor_4_out));

  // Notes on the sheet:
  //   INCOMING
  //   PHASE 2 - WRITE (from CPU)
  //   PHASE 1 - READ MEM
endmodule
